// Logisim project cpu28（2-5）test.circ as structural Verilog: 21 circuits, main circuit ◇单周期MIPS
module \单周期MIPS  (
  output RegWrite,
  output MemWrite,
  output [31:0] PC,
  output [31:0] IR,
  output [31:0] RDin,
  output [31:0] MDin
);

  wire AluSrcB, and_1_out, and_2_out, and_3_out, and_4_out, and_5_out, BLTZ, CLK, comparator_1_eq, Go, IR1,
       IR2, IR3, JAL, LBU, MemToReg, mips_alu_1_equal, not_1_out, not_2_out, RST, SignedExt, stop, syscall,
       W1, W2, W3, \单周期硬布线控制器_1_beq , \单周期硬布线控制器_1_bne , \单周期硬布线控制器_1_regdst ;
  wire [2:0] \单周期硬布线控制器_1_jr ;
  wire [3:0] \单周期硬布线控制器_1_alu_op ;
  wire [4:0] multiplexer_2_out, multiplexer_3_out, multiplexer_5_out, multiplexer_6_out;
  wire [7:0] multiplexer_13_out;
  wire [15:0] \总周期数 , \无条件分支数 , \条件分支成功数 ;
  wire [31:0] a0, adder_1_out, adder_2_out, bit_extender_1_out, bit_extender_2_out, bit_extender_3_out,
       LedData, mips_alu_1_result, multiplexer_1_out, multiplexer_7_out, multiplexer_8_out,
       multiplexer_9_out, multiplexer_10_out, multiplexer_12_out, multiplexer_14_out, ram_1_data,
       shifter_1_out;

  Clock #(.highDuration(1), .lowDuration(1)) clock_1 (.out(CLK));
  Button \u_继续运行  (.out(Go));
  Button \u_总复位  (.out(RST));
  Button _1 (.out(IR1));
  Button _2 (.out(IR2));
  Button _3 (.out(IR3));
  LED #(.active("true")) led_1 (.in(W1));
  LED #(.active("true")) led_2 (.in(W2));
  LED #(.active("true")) led_3 (.in(W3));
  Multiplexer #(.select(3), .width(32), .disabled("Z"), .enable("false")) multiplexer_1 (
    .in0(adder_1_out), .in1({32{1'b0}}), .in2({adder_1_out[31:28], IR[25:0], 2'b00}), .in3(a0),
    .in4(adder_2_out), .in5({32{1'b0}}), .in6({32{1'b0}}), .in7({32{1'b0}}), .out(multiplexer_1_out),
    .sel(\单周期硬布线控制器_1_jr ));
  Hex_Digit_Display hex_digit_display_1 (.value(LedData[31:28]));  // open: dp
  Register #(.width(32), .trigger("rising"), .Select("low")) u_PC (
    .D(multiplexer_1_out), .en(stop), .Q(PC), .clk(CLK), .clr(RST));
  Hex_Digit_Display hex_digit_display_2 (.value(LedData[27:24]));  // open: dp
  Hex_Digit_Display hex_digit_display_3 (.value(LedData[23:20]));  // open: dp
  Adder #(.width(32)) adder_1 (.a(PC), .b(32'h4), .out(adder_1_out));  // open: cin, cout
  Hex_Digit_Display hex_digit_display_4 (.value(LedData[19:16]));  // open: dp
  Hex_Digit_Display hex_digit_display_5 (.value(LedData[15:12]));  // open: dp
  ROM #(.addrWidth(10), .dataWidth(32), .Select("high")) Benchmark_ccmb (.addr(PC[11:2]), .data(IR));
  Hex_Digit_Display hex_digit_display_6 (.value(LedData[11:8]));  // open: dp
  Hex_Digit_Display hex_digit_display_7 (.value(LedData[7:4]));  // open: dp
  Hex_Digit_Display hex_digit_display_8 (.value(LedData[3:0]));  // open: dp
  // Probe on \总周期数 
  // Probe on \无条件分支数 
  // Probe on \条件分支成功数 
  \单周期硬布线控制器  \u_单周期硬布线控制器_1  (
    .Func(IR[5:0]), .OP(IR[31:26]), .ALU_OP(\单周期硬布线控制器_1_alu_op ), .MemToReg(MemToReg), .MemWrite(MemWrite),
    .ALU_SRC(AluSrcB), .RegWrite(RegWrite), .SysCALL(syscall), .SignedExt(SignedExt),
    .RegDst(\单周期硬布线控制器_1_regdst ), .JR(\单周期硬布线控制器_1_jr [0]), .JMP(\单周期硬布线控制器_1_jr [1]),
    .Beq(\单周期硬布线控制器_1_beq ), .JAL(JAL), .Bne(\单周期硬布线控制器_1_bne ), .LBU(LBU), .BLTZ(BLTZ));  // open: MFC0, MTC0, MF, ERET
  Multiplexer #(.select(1), .width(5), .disabled("Z"), .enable("false")) multiplexer_2 (
    .in0(IR[25:21]), .in1(5'b00100), .out(multiplexer_2_out), .sel(syscall));
  Multiplexer #(.select(1), .width(5), .disabled("Z"), .enable("false")) multiplexer_3 (
    .in0(IR[20:16]), .in1(5'b00010), .out(multiplexer_3_out), .sel(syscall));
  Multiplexer #(.select(1), .width(32), .disabled("Z"), .enable("false")) multiplexer_4 (
    .in0(multiplexer_14_out), .in1(adder_1_out), .out(RDin), .sel(JAL));
  assign bit_extender_1_out = {{16{1'b0}}, IR[15:0]};  // Bit_Extender bit_extender_1
  assign bit_extender_2_out = {{16{IR[15]}}, IR[15:0]};  // Bit_Extender bit_extender_2
  Multiplexer #(.select(1), .width(5), .disabled("Z"), .enable("false")) multiplexer_5 (
    .in0(IR[20:16]), .in1(IR[15:11]), .out(multiplexer_5_out), .sel(\单周期硬布线控制器_1_regdst ));
  Multiplexer #(.select(1), .width(5), .disabled("Z"), .enable("false")) multiplexer_6 (
    .in0(multiplexer_5_out), .in1({5{1'b1}}), .out(multiplexer_6_out), .sel(JAL));
  Multiplexer #(.select(1), .width(32), .disabled("Z"), .enable("false")) multiplexer_7 (
    .in0(bit_extender_1_out), .in1(bit_extender_2_out), .out(multiplexer_7_out), .sel(SignedExt));
  Shifter #(.width(32), .shift("ll")) shifter_1 (.in(bit_extender_2_out), .\dist (5'b00010), .out(shifter_1_out));
  // Probe on multiplexer_2_out
  Adder #(.width(32)) adder_2 (.a(shifter_1_out), .b(adder_1_out), .out(adder_2_out));  // open: cin, cout
  MIPS_Regifile mips_regifile_1 (
    .Din(RDin), .Clk(CLK), .R1(a0), .R2(MDin), .WE(RegWrite), .W_num(multiplexer_6_out),
    .R1_num(multiplexer_2_out), .R2_num(multiplexer_3_out));
  // Probe on multiplexer_7_out
  // Probe on a0
  Multiplexer #(.select(1), .width(32), .disabled("Z"), .enable("false")) multiplexer_8 (
    .in0(a0), .in1(32'h22), .out(multiplexer_8_out), .sel(syscall));
  Multiplexer #(.select(1), .width(32), .disabled("Z"), .enable("false")) multiplexer_9 (
    .in0(MDin), .in1(multiplexer_7_out), .out(multiplexer_9_out), .sel(AluSrcB));
  and and_1 (and_1_out, \单周期硬布线控制器_1_bne , not_1_out);
  and and_2 (and_2_out, \单周期硬布线控制器_1_beq , mips_alu_1_equal);
  not not_1 (not_1_out, mips_alu_1_equal);
  // Probe on \单周期硬布线控制器_1_alu_op 
  // Probe on \单周期硬布线控制器_1_alu_op 
  Multiplexer #(.select(1), .width(32), .disabled("Z"), .enable("false")) multiplexer_10 (
    .in0(multiplexer_9_out), .in1({32{1'b0}}), .out(multiplexer_10_out), .sel(BLTZ));
  or or_1 (\单周期硬布线控制器_1_jr [2], and_2_out, and_1_out, and_3_out);
  and and_3 (and_3_out, comparator_1_eq, BLTZ);
  MIPS_ALU mips_alu_1 (
    .X(multiplexer_8_out), .Y(multiplexer_10_out), .AluOP(\单周期硬布线控制器_1_alu_op ), .Equal(mips_alu_1_equal),
    .Result(mips_alu_1_result), .shamt(IR[10:6]));  // open: Result_2
  // Probe on mips_alu_1_result
  Counter #(.width(16), .max('hffff), .ongoal("wrap"), .trigger("rising"), .behavior("old")) counter_1 (
    .count(\单周期硬布线控制器_1_jr [1]), .Q(\无条件分支数 ), .clk(CLK), .clr(RST));  // open: load, D, carry, preset
  Counter #(.width(16), .max('hffff), .ongoal("wrap"), .trigger("rising"), .behavior("old")) counter_2 (
    .count(\单周期硬布线控制器_1_jr [2]), .Q(\条件分支成功数 ), .clk(CLK), .clr(RST));  // open: load, D, carry, preset
  Register #(.width(32), .trigger("rising"), .Select("low")) register_1 (
    .D(a0), .en(and_4_out), .Q(LedData), .clk(CLK), .clr(RST));
  and and_4 (and_4_out, mips_alu_1_equal, syscall);
  Multiplexer #(.select(1), .width(1), .disabled("Z"), .enable("false")) multiplexer_11 (
    .in0(1'b1), .in1(Go), .out(stop), .sel(and_5_out));
  and and_5 (and_5_out, syscall, ~mips_alu_1_equal);  // AND_Gate
  Counter #(.width(16), .max('hffff), .ongoal("wrap"), .trigger("rising"), .behavior("old")) counter_3 (
    .count(stop), .Q(\总周期数 ), .clk(CLK), .clr(RST));  // open: load, D, carry, preset
  Comparator #(.width(32), .mode("twosComplement")) comparator_1 (
    .a(32'h1), .b(mips_alu_1_result), .eq(comparator_1_eq));  // open: gt, lt
  not not_2 (not_2_out, MemWrite);
  RAM #(.addrWidth(10), .dataWidth(32), .bus("separate"), .Select("high")) ram_1 (
    .addr(mips_alu_1_result[11:2]), .din(MDin), .data(ram_1_data), .str(MemWrite), .clk(CLK), .ld(not_2_out),
    .clr(RST));  // open: sel
  Multiplexer #(.select(1), .width(32), .disabled("Z"), .enable("false")) multiplexer_12 (
    .in0(mips_alu_1_result), .in1(ram_1_data), .out(multiplexer_12_out), .sel(MemToReg));
  Multiplexer #(.select(2), .width(8), .disabled("Z"), .enable("false")) multiplexer_13 (
    .in0(multiplexer_12_out[7:0]), .in1(multiplexer_12_out[15:8]), .in2(multiplexer_12_out[23:16]),
    .in3(multiplexer_12_out[31:24]), .out(multiplexer_13_out), .sel(mips_alu_1_result[1:0]));
  ROM #(.addrWidth(10), .dataWidth(32), .Select("high")) u_BLTZ ();  // open: addr, data
  ROM #(.addrWidth(10), .dataWidth(32), .Select("high")) u_LBU ();  // open: addr, data
  ROM #(.addrWidth(10), .dataWidth(32), .Select("high")) SUBU ();  // open: addr, data
  ROM #(.addrWidth(10), .dataWidth(32), .Select("high")) XOR ();  // open: addr, data
  assign bit_extender_3_out = {{24{1'b0}}, multiplexer_13_out};  // Bit_Extender bit_extender_3
  Multiplexer #(.select(1), .width(32), .disabled("Z"), .enable("false")) multiplexer_14 (
    .in0(multiplexer_12_out), .in1(bit_extender_3_out), .out(multiplexer_14_out), .sel(LBU));
  ROM #(.addrWidth(10), .dataWidth(32), .Select("high")) Benchmark ();  // open: addr, data
  ROM #(.addrWidth(10), .dataWidth(32), .Select("high")) LBU1 ();  // open: addr, data

  // Notes on the sheet:
  //   中断源
  //   总复位信号应将除ROM以外所有存储组件全部清零
  //   中断等待指示
  //   数码管输出
  //   数码管输出应该用寄存器锁存，否则显示数据只能一闪而过
  //   contents of Benchmark_ccmb (hex, n*v repeats v):
  //   20110001 8000c05 20110001 20120002 20130003 8000c09 20110001 20120002 20130003 8000c0d 20110001
  //   20120002 20130003 8000c11 20110001 20120002 20130003 c000cf6 20100001 20110001 118fc0 112020
  //   20020022 c 118882 12200001 8000c15 112020 20020022 c 20110001 118880 112020 20020022 c 12200001
  //   8000c1f 20110001 118fc0 112020 20020022 c 1188c3 112020 20020022 c 118903 112020 20020022 c 118903
  //   112020 20020022 c 118903 112020 20020022 c 118903 112020 20020022 c 118903 112020 20020022 c 118903
  //   112020 20020022 c 118903 112020 20020022 c 20100001 109fc0 139fc3 8021 2012000c 24160003 26100001
  //   3210000f 20080008 20090001 139900 2709825 132020 20020022 c 1094022 1500fff9 22100001 2018000f
  //   2188024 108700 20080008 20090001 139902 2709825 132021 20020022 c 1094022 1500fff9 108702 2c9b022
  //   12c00001 8000c50 4020 1084027 84400 3508ffff 82021 20020022 c 2010ffff 20110000 ae300000 22100001
  //   22310004 ae300000 22100001 22310004 ae300000 22100001 22310004 ae300000 22100001 22310004 ae300000
  //   22100001 22310004 ae300000 22100001 22310004 ae300000 22100001 22310004 ae300000 22100001 22310004
  //   ae300000 22100001 22310004 ae300000 22100001 22310004 ae300000 22100001 22310004 ae300000 22100001
  //   22310004 ae300000 22100001 22310004 ae300000 22100001 22310004 ae300000 22100001 22310004 ae300000
  //   22100001 22310004 22100001 8020 2011003c 8e130000 8e340000 274402a 11000002 ae330000 ae140000
  //   2231fffc 1611fff8 102020 20020022 c 22100004 2011003c 1611fff2 20020032 c 20080001 20110010 112020
  //   20020022 c 200b0020 2288823 112020 20020022 c 216bffff 1560fffa 2002000a c 2008ffff 20117777 112020
  //   20020022 c 200b0010 2288826 112020 20020022 c 216bffff 1560fffa 2002000a c 20090000 200b0010
  //   34118483 20120404 118c00 129400 36318281 22520404 ad310000 2328820 21290004 216bffff 1560fffb
  //   200b0020 20090000 91310000 112020 20020022 c 21290001 216bffff 1560fff9 2002000a c 2011fff1 112020
  //   20020022 c 22310001 620fffb 2002000a c 2002000a c 20100000 22100001 102020 20020022 c 22100002
  //   102020 20020022 c 22100003 102020 20020022 c 22100004 102020 20020022 c 22100005 102020 20020022 c
  //   22100006 102020 20020022 c 22100007 102020 20020022 c 22100008 102020 20020022 20020022 c 3e00008
  //   OP
  //   Func
  //   rs
  //   指令字
  //   rt
  //   rd
  //   shamt
  //   imm
  //   JMP
  //   JR
  //   OP
  //   Func
  //   Beq
  //   Bne
  //   AluOP
  //   AluSrcB
  //   RegWrite
  //   JAL
  //   RegDst
  //   Syscall
  //   MemToReg
  //   MemWrite
  //   为方便自动评测，需要输出PC，IR，寄存器文件写入端口RDin，内存写入端口MDin等信号
  //   contents of BLTZ (hex, n*v repeats v):
  //   2011fff1 112020 20020022 c 22310001 620fffb 2002000a c
  //   contents of LBU (hex, n*v repeats v):
  //   20090000 200b0010 34118483 20120404 118c00 129400 36318281 22520404 ad310000 2328820 21290004
  //   216bffff 1560fffb 200b0020 20090000 91310000 112020 20020022 c 21290001 216bffff 1560fff9 2002000a c
  //   contents of SUBU (hex, n*v repeats v):
  //   20080001 20110010 112020 20020022 c 200b0020 2288823 112020 20020022 c 216bffff 1560fffa 2002000a c
  //   contents of XOR (hex, n*v repeats v):
  //   2008ffff 20117777 112020 20020022 c 200b0010 2288826 112020 20020022 c 216bffff 1560fffa 2002000a c
  //   contents of Benchmark (hex, n*v repeats v):
  //   20110001 8000c05 20110001 20120002 20130003 8000c09 20110001 20120002 20130003 8000c0d 20110001
  //   20120002 20130003 8000c11 20110001 20120002 20130003 c000cb8 20100001 20110001 118fc0 112020
  //   20020022 c 118882 12200001 8000c15 112020 20020022 c 20110001 118880 112020 20020022 c 12200001
  //   8000c1f 20110001 118fc0 112020 20020022 c 1188c3 112020 20020022 c 118903 112020 20020022 c 118903
  //   112020 20020022 c 118903 112020 20020022 c 118903 112020 20020022 c 118903 112020 20020022 c 118903
  //   112020 20020022 c 118903 112020 20020022 c 20100001 109fc0 139fc3 8021 2012000c 24160003 26100001
  //   3210000f 20080008 20090001 139900 2709825 132020 20020022 c 1094022 1500fff9 22100001 2018000f
  //   2188024 108700 20080008 20090001 139902 2709825 132021 20020022 c 1094022 1500fff9 108702 2c9b022
  //   12c00001 8000c50 4020 1084027 84400 3508ffff 82021 20020022 c 2010ffff 20110000 ae300000 22100001
  //   22310004 ae300000 22100001 22310004 ae300000 22100001 22310004 ae300000 22100001 22310004 ae300000
  //   22100001 22310004 ae300000 22100001 22310004 ae300000 22100001 22310004 ae300000 22100001 22310004
  //   ae300000 22100001 22310004 ae300000 22100001 22310004 ae300000 22100001 22310004 ae300000 22100001
  //   22310004 ae300000 22100001 22310004 ae300000 22100001 22310004 ae300000 22100001 22310004 ae300000
  //   22100001 22310004 22100001 8020 2011003c 8e130000 8e340000 274402a 11000002 ae330000 ae140000
  //   2231fffc 1611fff8 102020 20020022 c 22100004 2011003c 1611fff2 2002000a c 20100000 22100001 102020
  //   20020022 c 22100002 102020 20020022 c 22100003 102020 20020022 c 22100004 102020 20020022 c 22100005
  //   102020 20020022 c 22100006 102020 20020022 c 22100007 102020 20020022 c 22100008 102020 20020022
  //   20020022 c 3e00008
  //   contents of LBU1 (hex, n*v repeats v):
  //   20090000 200b0020 34118483 20120401 118c00 129400 36318281 22520401 ad310000 2328820 21290004
  //   216bffff 1560fffb 20020022 200b0020 20090000 91310000 112020 20020022 c 21290004 216bffff 1560fff9
  //   2002000a c
endmodule

// 单周期硬布线控制器
module \单周期硬布线控制器  (
  input  [5:0] OP,
  input  [5:0] Func,
  input  [4:0] MF,
  output [3:0] ALU_OP,
  output MemToReg,
  output MemWrite,
  output ALU_SRC,
  output RegWrite,
  output SysCALL,
  output SignedExt,
  output RegDst,
  output Beq,
  output Bne,
  output JR,
  output JMP,
  output JAL,
  output LBU,
  output BLTZ,
  output ERET,
  output MFC0,
  output MTC0
);

  wire comparator_1_eq, comparator_2_eq, comparator_3_eq, comparator_4_eq, \控制信号自动生成_1_regwrite ;

  Comparator #(.width(6), .mode("twosComplement")) comparator_1 (
    .a(Func), .b(6'b011000), .eq(comparator_1_eq));  // open: gt, lt
  Comparator #(.width(6), .mode("twosComplement")) comparator_2 (
    .a(OP), .b(6'b010000), .eq(comparator_2_eq));  // open: gt, lt
  Comparator #(.width(5), .mode("twosComplement")) comparator_3 (
    .a(MF), .b({5{1'b0}}), .eq(comparator_3_eq));  // open: gt, lt
  Comparator #(.width(5), .mode("twosComplement")) comparator_4 (
    .a(MF), .b(5'b00100), .eq(comparator_4_eq));  // open: gt, lt
  \运算控制器自动生成  \u_运算控制器自动生成_1  (
    .OP0(OP[0]), .OP1(OP[1]), .OP2(OP[2]), .OP3(OP[3]), .OP4(OP[4]), .OP5(OP[5]), .F0(Func[0]), .F1(Func[1]),
    .F2(Func[2]), .F3(Func[3]), .F4(Func[4]), .F5(Func[5]), .S0(ALU_OP[0]), .S1(ALU_OP[1]), .S2(ALU_OP[2]),
    .S3(ALU_OP[3]));
  \控制信号自动生成  \u_控制信号自动生成_1  (
    .OP0(OP[0]), .OP1(OP[1]), .OP2(OP[2]), .OP3(OP[3]), .OP4(OP[4]), .OP5(OP[5]), .F0(Func[0]), .F1(Func[1]),
    .F2(Func[2]), .F3(Func[3]), .F4(Func[4]), .F5(Func[5]), .MemToReg(MemToReg), .MemWrite(MemWrite),
    .ALU_SRC(ALU_SRC), .RegWrite(\控制信号自动生成_1_regwrite ), .SysCALL(SysCALL), .SignedExt(SignedExt),
    .RegDst(RegDst), .BEQ(Beq), .BNE(Bne), .JR(JR), .JUMP(JMP), .JAL(JAL));
  CCMB_Control ccmb_control_1 (
    .OP0(OP[0]), .OP1(OP[1]), .OP2(OP[2]), .OP3(OP[3]), .OP4(OP[4]), .OP5(OP[5]), .F0(Func[0]), .F1(Func[1]),
    .F2(Func[2]), .F3(Func[3]), .F4(Func[4]), .F5(Func[5]), .LBU(LBU), .BLTZ(BLTZ));
  and and_1 (ERET, comparator_1_eq, comparator_2_eq);
  and and_2 (MFC0, comparator_3_eq, comparator_2_eq);
  and and_3 (MTC0, comparator_4_eq, comparator_2_eq);
  or or_1 (RegWrite, MFC0, \控制信号自动生成_1_regwrite );

  // Other names for the same wires on the sheet: OP_CODE[5:0] = OP

  // Notes on the sheet:
  //   运算器控制器，根据指令生成运算器功能选择信号
  //   控制信号生成，产生数据通路需要的其他控制信号
endmodule

// 运算器控制器
module \运算控制器自动生成  (
  input  OP0,
  input  OP1,
  input  OP2,
  input  OP3,
  input  OP4,
  input  OP5,
  input  F0,
  input  F1,
  input  F2,
  input  F3,
  input  F4,
  input  F5,
  output S0,
  output S1,
  output S2,
  output S3
);

  wire and_1_out, and_2_out, and_3_out, and_4_out, and_5_out, and_6_out, and_7_out, and_8_out, and_9_out,
       and_10_out, and_11_out, and_12_out, and_13_out, and_14_out, and_15_out, and_16_out, and_17_out,
       and_18_out, and_19_out, and_20_out, and_21_out, and_22_out, and_23_out, and_24_out, and_25_out,
       and_26_out, and_27_out, and_28_out, and_29_out, and_30_out, and_31_out, and_32_out, and_33_out,
       and_34_out, and_35_out, and_36_out, and_37_out, and_38_out, and_39_out, and_40_out, and_41_out,
       and_42_out, and_43_out, not_1_out, not_2_out, not_3_out, not_4_out, not_5_out, not_6_out, not_7_out,
       not_8_out, not_9_out, not_10_out, not_11_out, not_12_out, not_13_out, not_14_out, not_15_out,
       not_16_out, not_17_out, not_18_out, not_19_out, not_20_out, not_21_out, not_22_out, not_23_out,
       not_24_out, not_25_out, not_26_out, not_27_out, not_28_out, not_29_out, not_30_out, not_31_out,
       not_32_out, not_33_out, not_34_out, not_35_out, not_36_out, not_37_out, not_38_out, not_39_out,
       not_40_out, not_41_out, not_42_out, not_43_out, not_44_out, not_45_out, not_46_out, not_47_out,
       not_48_out, not_49_out, not_50_out, not_51_out, not_52_out, not_53_out, not_54_out, not_55_out,
       not_56_out, not_57_out, not_58_out, not_59_out, not_60_out, not_61_out, not_62_out, not_63_out,
       not_64_out, not_65_out, not_66_out, not_67_out, not_68_out, not_69_out, not_70_out, not_71_out,
       not_72_out, not_73_out, not_74_out, not_75_out, not_76_out, not_77_out, not_78_out, not_79_out,
       not_80_out, not_81_out, not_82_out, not_83_out, not_84_out, not_85_out, not_86_out, not_87_out,
       not_88_out, not_89_out, not_90_out, not_91_out, not_92_out, not_93_out, not_94_out, not_95_out,
       not_96_out, not_97_out, not_98_out, not_99_out, not_100_out, not_101_out, not_102_out, not_103_out,
       not_104_out, not_105_out, not_106_out, not_107_out, not_108_out, not_109_out, not_110_out,
       not_111_out, not_112_out, not_113_out, not_114_out, not_115_out, not_116_out, not_117_out,
       not_118_out, not_119_out, not_120_out, not_121_out, not_122_out, not_123_out, not_124_out,
       not_125_out, not_126_out, not_127_out, not_128_out, not_129_out, not_130_out, not_131_out,
       not_132_out, not_133_out, not_134_out, not_135_out, not_136_out, not_137_out, not_138_out,
       not_139_out, not_140_out, not_141_out, not_142_out, not_143_out, not_144_out, not_145_out,
       not_146_out, not_147_out, not_148_out, not_149_out, not_150_out, not_151_out, not_152_out,
       not_153_out, not_154_out, not_155_out, not_156_out, not_157_out, not_158_out, not_159_out,
       not_160_out, not_161_out, not_162_out, not_163_out, not_164_out, not_165_out, not_166_out,
       not_167_out, not_168_out, not_169_out, not_170_out, not_171_out, not_172_out, not_173_out,
       not_174_out, not_175_out, not_176_out, not_177_out, not_178_out, not_179_out, not_180_out,
       not_181_out, not_182_out, not_183_out, not_184_out, not_185_out, not_186_out, not_187_out,
       not_188_out, not_189_out, not_190_out, not_191_out, not_192_out, not_193_out, not_194_out,
       not_195_out, not_196_out, not_197_out, not_198_out, not_199_out, not_200_out, not_201_out,
       not_202_out, not_203_out, not_204_out, not_205_out, not_206_out, not_207_out, not_208_out,
       not_209_out, not_210_out, not_211_out, not_212_out, not_213_out, not_214_out, not_215_out,
       not_216_out, not_217_out, not_218_out, not_219_out, not_220_out, not_221_out, not_222_out,
       not_223_out, not_224_out, not_225_out, not_226_out, not_227_out, not_228_out, not_229_out,
       not_230_out, not_231_out, not_232_out, not_233_out, not_234_out, not_235_out, not_236_out,
       not_237_out, not_238_out, not_239_out, not_240_out, not_241_out, not_242_out, not_243_out,
       not_244_out, not_245_out, not_246_out, not_247_out, not_248_out, not_249_out, not_250_out,
       not_251_out, not_252_out, not_253_out, not_254_out, not_255_out, not_256_out, not_257_out,
       not_258_out, not_259_out, not_260_out, not_261_out, not_262_out, not_263_out, not_264_out,
       not_265_out, not_266_out, not_267_out, not_268_out, not_269_out, not_270_out, not_271_out,
       not_272_out, not_273_out, not_274_out, not_275_out, not_276_out, not_277_out, not_278_out,
       not_279_out, not_280_out, not_281_out, not_282_out, not_283_out, not_284_out, not_285_out,
       not_286_out, not_287_out, not_288_out, not_289_out, not_290_out, not_291_out, not_292_out,
       not_293_out, not_294_out, not_295_out;

  not not_1 (not_1_out, OP5);
  not not_2 (not_2_out, OP4);
  not not_3 (not_3_out, OP3);
  not not_4 (not_4_out, OP2);
  not not_5 (not_5_out, OP1);
  not not_6 (not_6_out, OP0);
  not not_7 (not_7_out, F5);
  not not_8 (not_8_out, F4);
  not not_9 (not_9_out, F3);
  not not_10 (not_10_out, F2);
  not not_11 (not_11_out, OP5);
  not not_12 (not_12_out, OP4);
  not not_13 (not_13_out, OP3);
  not not_14 (not_14_out, OP2);
  not not_15 (not_15_out, OP1);
  not not_16 (not_16_out, OP0);
  not not_17 (not_17_out, F4);
  not not_18 (not_18_out, F3);
  not not_19 (not_19_out, F2);
  not not_20 (not_20_out, F1);
  not not_21 (not_21_out, F0);
  not not_22 (not_22_out, OP5);
  not not_23 (not_23_out, OP4);
  not not_24 (not_24_out, OP3);
  not not_25 (not_25_out, OP2);
  not not_26 (not_26_out, OP1);
  not not_27 (not_27_out, OP0);
  not not_28 (not_28_out, F4);
  not not_29 (not_29_out, F3);
  not not_30 (not_30_out, F2);
  not not_31 (not_31_out, F1);
  not not_32 (not_32_out, OP5);
  not not_33 (not_33_out, OP4);
  not not_34 (not_34_out, OP3);
  not not_35 (not_35_out, OP2);
  not not_36 (not_36_out, OP1);
  not not_37 (not_37_out, OP0);
  not not_38 (not_38_out, F4);
  not not_39 (not_39_out, F3);
  not not_40 (not_40_out, F1);
  not not_41 (not_41_out, F0);
  not not_42 (not_42_out, OP5);
  not not_43 (not_43_out, OP4);
  not not_44 (not_44_out, OP3);
  not not_45 (not_45_out, OP2);
  not not_46 (not_46_out, OP1);
  not not_47 (not_47_out, OP0);
  not not_48 (not_48_out, F4);
  not not_49 (not_49_out, F2);
  not not_50 (not_50_out, F0);
  not not_51 (not_51_out, OP5);
  not not_52 (not_52_out, OP4);
  not not_53 (not_53_out, OP2);
  not not_54 (not_54_out, OP1);
  not not_55 (not_55_out, OP0);
  not not_56 (not_56_out, OP5);
  not not_57 (not_57_out, OP4);
  not not_58 (not_58_out, OP1);
  not not_59 (not_59_out, OP0);
  not not_60 (not_60_out, OP5);
  not not_61 (not_61_out, OP4);
  not not_62 (not_62_out, OP2);
  not not_63 (not_63_out, OP1);
  not not_64 (not_64_out, OP5);
  not not_65 (not_65_out, OP4);
  not not_66 (not_66_out, OP2);
  not not_67 (not_67_out, OP0);
  not not_68 (not_68_out, OP4);
  not not_69 (not_69_out, OP3);
  not not_70 (not_70_out, OP2);
  not not_71 (not_71_out, OP4);
  not not_72 (not_72_out, OP2);
  not not_73 (not_73_out, OP5);
  not not_74 (not_74_out, OP4);
  not not_75 (not_75_out, OP3);
  not not_76 (not_76_out, OP2);
  not not_77 (not_77_out, OP1);
  not not_78 (not_78_out, OP0);
  not not_79 (not_79_out, F4);
  not not_80 (not_80_out, F3);
  not not_81 (not_81_out, F0);
  not not_82 (not_82_out, OP4);
  not not_83 (not_83_out, OP3);
  not not_84 (not_84_out, OP1);
  not not_85 (not_85_out, OP0);
  not not_86 (not_86_out, OP5);
  not not_87 (not_87_out, OP4);
  not not_88 (not_88_out, OP3);
  not not_89 (not_89_out, OP2);
  not not_90 (not_90_out, OP1);
  not not_91 (not_91_out, OP5);
  not not_92 (not_92_out, OP4);
  not not_93 (not_93_out, OP3);
  not not_94 (not_94_out, OP2);
  not not_95 (not_95_out, OP1);
  not not_96 (not_96_out, OP0);
  not not_97 (not_97_out, F5);
  not not_98 (not_98_out, F4);
  not not_99 (not_99_out, F3);
  not not_100 (not_100_out, F2);
  not not_101 (not_101_out, F0);
  not not_102 (not_102_out, OP5);
  not not_103 (not_103_out, OP4);
  not not_104 (not_104_out, OP3);
  not not_105 (not_105_out, OP2);
  not not_106 (not_106_out, OP1);
  not not_107 (not_107_out, OP0);
  not not_108 (not_108_out, F4);
  not not_109 (not_109_out, F3);
  not not_110 (not_110_out, F2);
  not not_111 (not_111_out, F0);
  not not_112 (not_112_out, OP5);
  not not_113 (not_113_out, OP4);
  not not_114 (not_114_out, OP3);
  not not_115 (not_115_out, OP2);
  not not_116 (not_116_out, OP1);
  not not_117 (not_117_out, OP0);
  not not_118 (not_118_out, F4);
  not not_119 (not_119_out, F3);
  not not_120 (not_120_out, F1);
  not not_121 (not_121_out, F0);
  not not_122 (not_122_out, OP5);
  not not_123 (not_123_out, OP4);
  not not_124 (not_124_out, OP3);
  not not_125 (not_125_out, OP2);
  not not_126 (not_126_out, OP1);
  not not_127 (not_127_out, OP0);
  not not_128 (not_128_out, F4);
  not not_129 (not_129_out, F3);
  not not_130 (not_130_out, OP5);
  not not_131 (not_131_out, OP4);
  not not_132 (not_132_out, OP3);
  not not_133 (not_133_out, OP2);
  not not_134 (not_134_out, OP1);
  not not_135 (not_135_out, OP0);
  not not_136 (not_136_out, F4);
  not not_137 (not_137_out, F2);
  not not_138 (not_138_out, F0);
  not not_139 (not_139_out, OP5);
  not not_140 (not_140_out, OP4);
  not not_141 (not_141_out, OP1);
  not not_142 (not_142_out, OP0);
  not not_143 (not_143_out, OP5);
  not not_144 (not_144_out, OP4);
  not not_145 (not_145_out, OP2);
  not not_146 (not_146_out, OP0);
  not not_147 (not_147_out, OP5);
  not not_148 (not_148_out, OP4);
  not not_149 (not_149_out, OP3);
  not not_150 (not_150_out, OP2);
  not not_151 (not_151_out, OP1);
  not not_152 (not_152_out, OP0);
  not not_153 (not_153_out, F4);
  not not_154 (not_154_out, F3);
  not not_155 (not_155_out, F2);
  not not_156 (not_156_out, OP5);
  not not_157 (not_157_out, OP4);
  not not_158 (not_158_out, OP3);
  not not_159 (not_159_out, OP2);
  not not_160 (not_160_out, OP1);
  not not_161 (not_161_out, OP5);
  not not_162 (not_162_out, OP4);
  not not_163 (not_163_out, OP3);
  not not_164 (not_164_out, OP2);
  not not_165 (not_165_out, OP1);
  not not_166 (not_166_out, OP0);
  not not_167 (not_167_out, F4);
  not not_168 (not_168_out, F3);
  not not_169 (not_169_out, F2);
  not not_170 (not_170_out, F1);
  not not_171 (not_171_out, F0);
  not not_172 (not_172_out, OP5);
  not not_173 (not_173_out, OP4);
  not not_174 (not_174_out, OP3);
  not not_175 (not_175_out, OP2);
  not not_176 (not_176_out, OP1);
  not not_177 (not_177_out, OP0);
  not not_178 (not_178_out, F4);
  not not_179 (not_179_out, F3);
  not not_180 (not_180_out, F2);
  not not_181 (not_181_out, F1);
  not not_182 (not_182_out, OP5);
  not not_183 (not_183_out, OP4);
  not not_184 (not_184_out, OP3);
  not not_185 (not_185_out, OP2);
  not not_186 (not_186_out, OP1);
  not not_187 (not_187_out, OP0);
  not not_188 (not_188_out, F4);
  not not_189 (not_189_out, F3);
  not not_190 (not_190_out, F2);
  not not_191 (not_191_out, F0);
  not not_192 (not_192_out, OP5);
  not not_193 (not_193_out, OP4);
  not not_194 (not_194_out, OP3);
  not not_195 (not_195_out, OP2);
  not not_196 (not_196_out, OP1);
  not not_197 (not_197_out, OP0);
  not not_198 (not_198_out, F4);
  not not_199 (not_199_out, F3);
  not not_200 (not_200_out, F1);
  not not_201 (not_201_out, F0);
  not not_202 (not_202_out, OP5);
  not not_203 (not_203_out, OP4);
  not not_204 (not_204_out, OP3);
  not not_205 (not_205_out, OP2);
  not not_206 (not_206_out, OP1);
  not not_207 (not_207_out, OP0);
  not not_208 (not_208_out, F4);
  not not_209 (not_209_out, F2);
  not not_210 (not_210_out, OP5);
  not not_211 (not_211_out, OP4);
  not not_212 (not_212_out, OP2);
  not not_213 (not_213_out, OP1);
  not not_214 (not_214_out, OP0);
  not not_215 (not_215_out, OP5);
  not not_216 (not_216_out, OP4);
  not not_217 (not_217_out, OP1);
  not not_218 (not_218_out, OP0);
  not not_219 (not_219_out, OP5);
  not not_220 (not_220_out, OP4);
  not not_221 (not_221_out, OP2);
  not not_222 (not_222_out, OP1);
  not not_223 (not_223_out, OP4);
  not not_224 (not_224_out, OP3);
  not not_225 (not_225_out, OP2);
  not not_226 (not_226_out, OP4);
  not not_227 (not_227_out, OP2);
  not not_228 (not_228_out, OP5);
  not not_229 (not_229_out, OP4);
  not not_230 (not_230_out, OP3);
  not not_231 (not_231_out, OP2);
  not not_232 (not_232_out, OP1);
  not not_233 (not_233_out, OP0);
  not not_234 (not_234_out, F4);
  not not_235 (not_235_out, F3);
  not not_236 (not_236_out, F2);
  not not_237 (not_237_out, OP4);
  not not_238 (not_238_out, OP3);
  not not_239 (not_239_out, OP1);
  not not_240 (not_240_out, OP0);
  not not_241 (not_241_out, OP5);
  not not_242 (not_242_out, OP4);
  not not_243 (not_243_out, OP3);
  not not_244 (not_244_out, OP2);
  not not_245 (not_245_out, OP1);
  not not_246 (not_246_out, OP0);
  not not_247 (not_247_out, F4);
  not not_248 (not_248_out, F3);
  not not_249 (not_249_out, F1);
  not not_250 (not_250_out, OP5);
  not not_251 (not_251_out, OP4);
  not not_252 (not_252_out, OP3);
  not not_253 (not_253_out, OP2);
  not not_254 (not_254_out, OP1);
  not not_255 (not_255_out, OP0);
  not not_256 (not_256_out, F4);
  not not_257 (not_257_out, F3);
  not not_258 (not_258_out, OP5);
  not not_259 (not_259_out, OP4);
  not not_260 (not_260_out, OP3);
  not not_261 (not_261_out, OP2);
  not not_262 (not_262_out, OP1);
  not not_263 (not_263_out, OP0);
  not not_264 (not_264_out, F4);
  not not_265 (not_265_out, F2);
  not not_266 (not_266_out, F0);
  not not_267 (not_267_out, OP5);
  not not_268 (not_268_out, OP4);
  not not_269 (not_269_out, OP3);
  not not_270 (not_270_out, OP2);
  not not_271 (not_271_out, OP1);
  not not_272 (not_272_out, OP0);
  not not_273 (not_273_out, F4);
  not not_274 (not_274_out, F2);
  not not_275 (not_275_out, OP5);
  not not_276 (not_276_out, OP4);
  not not_277 (not_277_out, OP2);
  not not_278 (not_278_out, OP0);
  not not_279 (not_279_out, OP5);
  not not_280 (not_280_out, OP4);
  not not_281 (not_281_out, OP1);
  not not_282 (not_282_out, OP5);
  not not_283 (not_283_out, OP4);
  not not_284 (not_284_out, OP3);
  not not_285 (not_285_out, OP2);
  not not_286 (not_286_out, OP1);
  not not_287 (not_287_out, OP0);
  not not_288 (not_288_out, F4);
  not not_289 (not_289_out, F3);
  not not_290 (not_290_out, F0);
  not not_291 (not_291_out, OP5);
  not not_292 (not_292_out, OP4);
  not not_293 (not_293_out, OP3);
  not not_294 (not_294_out, OP2);
  not not_295 (not_295_out, OP1);
  and and_1 (and_1_out, not_1_out, not_2_out, not_3_out, not_4_out, not_5_out, not_6_out, not_7_out, not_8_out, not_9_out, not_10_out, F1, F0);
  and and_2 (and_2_out, not_11_out, not_12_out, not_13_out, not_14_out, not_15_out, not_16_out, F5, not_17_out, not_18_out, not_19_out, not_20_out, not_21_out);
  and and_3 (and_3_out, not_22_out, not_23_out, not_24_out, not_25_out, not_26_out, not_27_out, F5, not_28_out, not_29_out, not_30_out, not_31_out, F0);
  and and_4 (and_4_out, not_32_out, not_33_out, not_34_out, not_35_out, not_36_out, not_37_out, F5, not_38_out, not_39_out, F2, not_40_out, not_41_out);
  and and_5 (and_5_out, not_42_out, not_43_out, not_44_out, not_45_out, not_46_out, not_47_out, F5, not_48_out, F3, not_49_out, F1, not_50_out);
  and and_6 (and_6_out, not_51_out, not_52_out, OP3, not_53_out, not_54_out, not_55_out);
  and and_7 (and_7_out, not_56_out, not_57_out, OP3, OP2, not_58_out, not_59_out);
  and and_8 (and_8_out, not_60_out, not_61_out, OP3, not_62_out, not_63_out, OP0);
  and and_9 (and_9_out, not_64_out, not_65_out, OP3, not_66_out, OP1, not_67_out);
  and and_10 (and_10_out, OP5, not_68_out, not_69_out, not_70_out, OP1, OP0);
  and and_11 (and_11_out, OP5, not_71_out, OP3, not_72_out, OP1, OP0);
  and and_12 (and_12_out, not_73_out, not_74_out, not_75_out, not_76_out, not_77_out, not_78_out, F5, not_79_out, not_80_out, F2, F1, not_81_out);
  and and_13 (and_13_out, OP5, not_82_out, not_83_out, OP2, not_84_out, not_85_out);
  and and_14 (and_14_out, not_86_out, not_87_out, not_88_out, not_89_out, not_90_out, OP0);
  and and_15 (and_15_out, not_91_out, not_92_out, not_93_out, not_94_out, not_95_out, not_96_out, not_97_out, not_98_out, not_99_out, not_100_out, F1, not_101_out);
  and and_16 (and_16_out, not_102_out, not_103_out, not_104_out, not_105_out, not_106_out, not_107_out, F5, not_108_out, not_109_out, not_110_out, F1, not_111_out);
  and and_17 (and_17_out, not_112_out, not_113_out, not_114_out, not_115_out, not_116_out, not_117_out, F5, not_118_out, not_119_out, F2, not_120_out, not_121_out);
  and and_18 (and_18_out, not_122_out, not_123_out, not_124_out, not_125_out, not_126_out, not_127_out, F5, not_128_out, not_129_out, F2, F1, F0);
  and and_19 (and_19_out, not_130_out, not_131_out, not_132_out, not_133_out, not_134_out, not_135_out, F5, not_136_out, F3, not_137_out, F1, not_138_out);
  and and_20 (and_20_out, not_139_out, not_140_out, OP3, OP2, not_141_out, not_142_out);
  and and_21 (and_21_out, not_143_out, not_144_out, OP3, not_145_out, OP1, not_146_out);
  and and_22 (and_22_out, not_147_out, not_148_out, not_149_out, not_150_out, not_151_out, not_152_out, F5, not_153_out, not_154_out, not_155_out, F1, F0);
  and and_23 (and_23_out, not_156_out, not_157_out, not_158_out, not_159_out, not_160_out, OP0);
  and and_24 (and_24_out, not_161_out, not_162_out, not_163_out, not_164_out, not_165_out, not_166_out, F5, not_167_out, not_168_out, not_169_out, not_170_out, not_171_out);
  and and_25 (and_25_out, not_172_out, not_173_out, not_174_out, not_175_out, not_176_out, not_177_out, F5, not_178_out, not_179_out, not_180_out, not_181_out, F0);
  and and_26 (and_26_out, not_182_out, not_183_out, not_184_out, not_185_out, not_186_out, not_187_out, F5, not_188_out, not_189_out, not_190_out, F1, not_191_out);
  and and_27 (and_27_out, not_192_out, not_193_out, not_194_out, not_195_out, not_196_out, not_197_out, F5, not_198_out, not_199_out, F2, not_200_out, not_201_out);
  and and_28 (and_28_out, not_202_out, not_203_out, not_204_out, not_205_out, not_206_out, not_207_out, F5, not_208_out, F3, not_209_out, F1, F0);
  and and_29 (and_29_out, not_210_out, not_211_out, OP3, not_212_out, not_213_out, not_214_out);
  and and_30 (and_30_out, not_215_out, not_216_out, OP3, OP2, not_217_out, not_218_out);
  and and_31 (and_31_out, not_219_out, not_220_out, OP3, not_221_out, not_222_out, OP0);
  and and_32 (and_32_out, OP5, not_223_out, not_224_out, not_225_out, OP1, OP0);
  and and_33 (and_33_out, OP5, not_226_out, OP3, not_227_out, OP1, OP0);
  and and_34 (and_34_out, not_228_out, not_229_out, not_230_out, not_231_out, not_232_out, not_233_out, F5, not_234_out, not_235_out, not_236_out, F1, F0);
  and and_35 (and_35_out, OP5, not_237_out, not_238_out, OP2, not_239_out, not_240_out);
  and and_36 (and_36_out, not_241_out, not_242_out, not_243_out, not_244_out, not_245_out, not_246_out, F5, not_247_out, not_248_out, F2, not_249_out, F0);
  and and_37 (and_37_out, not_250_out, not_251_out, not_252_out, not_253_out, not_254_out, not_255_out, F5, not_256_out, not_257_out, F2, F1, F0);
  and and_38 (and_38_out, not_258_out, not_259_out, not_260_out, not_261_out, not_262_out, not_263_out, F5, not_264_out, F3, not_265_out, F1, not_266_out);
  and and_39 (and_39_out, not_267_out, not_268_out, not_269_out, not_270_out, not_271_out, not_272_out, F5, not_273_out, F3, not_274_out, F1, F0);
  and and_40 (and_40_out, not_275_out, not_276_out, OP3, not_277_out, OP1, not_278_out);
  and and_41 (and_41_out, not_279_out, not_280_out, OP3, OP2, not_281_out, OP0);
  and and_42 (and_42_out, not_282_out, not_283_out, not_284_out, not_285_out, not_286_out, not_287_out, F5, not_288_out, not_289_out, F2, F1, not_290_out);
  and and_43 (and_43_out, not_291_out, not_292_out, not_293_out, not_294_out, not_295_out, OP0);
  or or_1 (S1, and_15_out, and_16_out, and_17_out, and_18_out, and_19_out, and_20_out, and_21_out, and_22_out, and_23_out);
  or or_2 (S3, and_36_out, and_37_out, and_38_out, and_39_out, and_40_out, and_41_out, and_42_out, and_43_out);
  or or_3 (S0, and_1_out, and_2_out, and_3_out, and_4_out, and_5_out, and_6_out, and_7_out, and_8_out, and_9_out, and_10_out, and_11_out, and_12_out, and_13_out, and_14_out);
  or or_4 (S2, and_24_out, and_25_out, and_26_out, and_27_out, and_28_out, and_29_out, and_30_out, and_31_out, and_32_out, and_33_out, and_34_out, and_35_out);
endmodule

// 控制信号生成
module \控制信号自动生成  (
  input  OP0,
  input  OP1,
  input  OP2,
  input  OP3,
  input  OP4,
  input  OP5,
  input  F0,
  input  F1,
  input  F2,
  input  F3,
  input  F4,
  input  F5,
  output MemToReg,
  output MemWrite,
  output ALU_SRC,
  output RegWrite,
  output SysCALL,
  output SignedExt,
  output RegDst,
  output BEQ,
  output BNE,
  output JR,
  output JUMP,
  output JAL
);

  wire and_1_out, and_2_out, and_4_out, and_5_out, and_6_out, and_7_out, and_8_out, and_9_out, and_10_out,
       and_11_out, and_12_out, and_13_out, and_14_out, and_15_out, and_16_out, and_17_out, and_18_out,
       and_19_out, and_20_out, and_21_out, and_22_out, and_23_out, and_24_out, and_25_out, and_26_out,
       and_27_out, and_28_out, and_29_out, and_30_out, and_31_out, and_32_out, and_34_out, and_35_out,
       and_36_out, and_37_out, and_38_out, and_39_out, and_40_out, and_41_out, and_42_out, and_43_out,
       and_44_out, and_45_out, and_46_out, and_47_out, and_48_out, and_49_out, and_50_out, and_51_out,
       and_52_out, and_56_out, and_57_out, and_58_out, not_1_out, not_2_out, not_3_out, not_4_out, not_5_out,
       not_6_out, not_7_out, not_8_out, not_9_out, not_10_out, not_11_out, not_12_out, not_13_out,
       not_14_out, not_15_out, not_16_out, not_17_out, not_18_out, not_19_out, not_20_out, not_21_out,
       not_22_out, not_23_out, not_24_out, not_25_out, not_26_out, not_27_out, not_28_out, not_29_out,
       not_30_out, not_31_out, not_32_out, not_33_out, not_34_out, not_35_out, not_36_out, not_37_out,
       not_38_out, not_39_out, not_40_out, not_41_out, not_42_out, not_43_out, not_44_out, not_45_out,
       not_46_out, not_47_out, not_48_out, not_49_out, not_50_out, not_51_out, not_52_out, not_53_out,
       not_54_out, not_55_out, not_56_out, not_57_out, not_58_out, not_59_out, not_60_out, not_61_out,
       not_62_out, not_63_out, not_64_out, not_65_out, not_66_out, not_67_out, not_68_out, not_69_out,
       not_70_out, not_71_out, not_72_out, not_73_out, not_74_out, not_75_out, not_76_out, not_77_out,
       not_78_out, not_79_out, not_80_out, not_81_out, not_82_out, not_83_out, not_84_out, not_85_out,
       not_86_out, not_87_out, not_88_out, not_89_out, not_90_out, not_91_out, not_92_out, not_93_out,
       not_94_out, not_95_out, not_96_out, not_97_out, not_98_out, not_99_out, not_100_out, not_101_out,
       not_102_out, not_103_out, not_104_out, not_105_out, not_106_out, not_107_out, not_108_out,
       not_109_out, not_110_out, not_111_out, not_112_out, not_113_out, not_114_out, not_115_out,
       not_116_out, not_117_out, not_118_out, not_119_out, not_120_out, not_121_out, not_122_out,
       not_123_out, not_124_out, not_125_out, not_126_out, not_127_out, not_128_out, not_129_out,
       not_130_out, not_131_out, not_132_out, not_133_out, not_134_out, not_135_out, not_136_out,
       not_137_out, not_138_out, not_139_out, not_140_out, not_141_out, not_142_out, not_143_out,
       not_144_out, not_145_out, not_146_out, not_147_out, not_148_out, not_149_out, not_150_out,
       not_151_out, not_152_out, not_153_out, not_154_out, not_155_out, not_156_out, not_157_out,
       not_158_out, not_159_out, not_160_out, not_161_out, not_162_out, not_163_out, not_164_out,
       not_165_out, not_166_out, not_167_out, not_168_out, not_169_out, not_170_out, not_171_out,
       not_172_out, not_173_out, not_174_out, not_175_out, not_176_out, not_177_out, not_178_out,
       not_179_out, not_180_out, not_181_out, not_182_out, not_183_out, not_184_out, not_185_out,
       not_186_out, not_187_out, not_188_out, not_189_out, not_190_out, not_191_out, not_192_out,
       not_193_out, not_194_out, not_195_out, not_196_out, not_197_out, not_198_out, not_199_out,
       not_200_out, not_201_out, not_202_out, not_203_out, not_204_out, not_205_out, not_206_out,
       not_207_out, not_208_out, not_209_out, not_210_out, not_211_out, not_212_out, not_213_out,
       not_214_out, not_215_out, not_216_out, not_217_out, not_218_out, not_219_out, not_220_out,
       not_221_out, not_222_out, not_223_out, not_224_out, not_225_out, not_226_out, not_227_out,
       not_228_out, not_229_out, not_230_out, not_231_out, not_232_out, not_233_out, not_234_out,
       not_235_out, not_236_out, not_237_out, not_238_out, not_239_out, not_240_out, not_241_out,
       not_242_out, not_243_out, not_244_out, not_245_out, not_246_out, not_247_out, not_248_out,
       not_249_out, not_250_out, not_251_out, not_252_out, not_253_out, not_254_out, not_255_out,
       not_256_out, not_257_out, not_258_out, not_259_out, not_260_out, not_261_out, not_262_out,
       not_263_out, not_264_out, not_265_out, not_266_out, not_267_out, not_268_out, not_269_out,
       not_270_out, not_271_out, not_272_out, not_273_out, not_274_out, not_275_out, not_276_out,
       not_277_out, not_278_out, not_279_out, not_280_out, not_281_out, not_282_out, not_283_out,
       not_284_out, not_285_out, not_286_out, not_287_out, not_288_out, not_289_out, not_290_out,
       not_291_out, not_292_out, not_293_out, not_294_out, not_295_out, not_296_out, not_297_out,
       not_298_out, not_299_out, not_300_out, not_301_out, not_302_out, not_303_out, not_304_out,
       not_305_out, not_306_out, not_307_out, not_308_out, not_309_out, not_310_out, not_311_out,
       not_312_out, not_313_out, not_314_out, not_315_out, not_316_out, not_317_out, not_318_out,
       not_319_out, not_320_out, not_321_out, not_322_out, not_323_out, not_324_out, not_325_out,
       not_326_out, not_327_out, not_328_out, not_329_out, not_330_out, not_331_out, not_332_out,
       not_333_out, not_334_out, not_335_out, not_336_out, not_337_out, not_338_out, not_339_out,
       not_340_out, not_341_out, not_342_out, not_343_out, not_344_out, not_345_out, not_346_out,
       not_347_out, not_348_out, not_349_out, not_350_out, not_351_out, not_352_out, not_353_out,
       not_354_out, not_355_out, not_356_out, not_357_out, not_358_out, not_359_out, not_360_out,
       not_361_out, not_362_out, not_363_out, not_364_out, not_365_out, not_366_out, not_367_out,
       not_368_out, not_369_out, not_370_out, not_371_out, not_372_out, not_373_out, not_374_out,
       not_375_out, not_376_out, not_377_out, not_378_out, not_379_out, not_380_out, not_381_out,
       not_382_out, not_383_out, not_384_out, not_385_out, not_386_out, not_387_out, not_388_out,
       not_389_out, not_390_out, not_391_out, not_392_out, not_393_out, not_394_out, not_395_out,
       not_396_out, not_397_out;

  not not_1 (not_1_out, OP4);
  not not_2 (not_2_out, OP3);
  not not_3 (not_3_out, OP2);
  not not_4 (not_4_out, OP4);
  not not_5 (not_5_out, OP3);
  not not_6 (not_6_out, OP1);
  not not_7 (not_7_out, OP0);
  not not_8 (not_8_out, OP4);
  not not_9 (not_9_out, OP2);
  not not_10 (not_10_out, OP5);
  not not_11 (not_11_out, OP4);
  not not_12 (not_12_out, OP2);
  not not_13 (not_13_out, OP1);
  not not_14 (not_14_out, OP0);
  not not_15 (not_15_out, OP5);
  not not_16 (not_16_out, OP4);
  not not_17 (not_17_out, OP1);
  not not_18 (not_18_out, OP0);
  not not_19 (not_19_out, OP5);
  not not_20 (not_20_out, OP4);
  not not_21 (not_21_out, OP2);
  not not_22 (not_22_out, OP1);
  not not_23 (not_23_out, OP5);
  not not_24 (not_24_out, OP4);
  not not_25 (not_25_out, OP2);
  not not_26 (not_26_out, OP0);
  not not_27 (not_27_out, OP5);
  not not_28 (not_28_out, OP4);
  not not_29 (not_29_out, OP1);
  not not_30 (not_30_out, OP4);
  not not_31 (not_31_out, OP3);
  not not_32 (not_32_out, OP2);
  not not_33 (not_33_out, OP4);
  not not_34 (not_34_out, OP2);
  not not_35 (not_35_out, OP4);
  not not_36 (not_36_out, OP3);
  not not_37 (not_37_out, OP1);
  not not_38 (not_38_out, OP0);
  not not_39 (not_39_out, OP5);
  not not_40 (not_40_out, OP4);
  not not_41 (not_41_out, OP3);
  not not_42 (not_42_out, OP2);
  not not_43 (not_43_out, OP1);
  not not_44 (not_44_out, OP0);
  not not_45 (not_45_out, F5);
  not not_46 (not_46_out, F4);
  not not_47 (not_47_out, F3);
  not not_48 (not_48_out, F2);
  not not_49 (not_49_out, F1);
  not not_50 (not_50_out, F0);
  not not_51 (not_51_out, OP5);
  not not_52 (not_52_out, OP4);
  not not_53 (not_53_out, OP3);
  not not_54 (not_54_out, OP2);
  not not_55 (not_55_out, OP1);
  not not_56 (not_56_out, OP0);
  not not_57 (not_57_out, F5);
  not not_58 (not_58_out, F4);
  not not_59 (not_59_out, F3);
  not not_60 (not_60_out, F2);
  not not_61 (not_61_out, OP5);
  not not_62 (not_62_out, OP4);
  not not_63 (not_63_out, OP3);
  not not_64 (not_64_out, OP2);
  not not_65 (not_65_out, OP1);
  not not_66 (not_66_out, OP0);
  not not_67 (not_67_out, F5);
  not not_68 (not_68_out, F4);
  not not_69 (not_69_out, F3);
  not not_70 (not_70_out, F2);
  not not_71 (not_71_out, F0);
  not not_72 (not_72_out, OP5);
  not not_73 (not_73_out, OP4);
  not not_74 (not_74_out, OP3);
  not not_75 (not_75_out, OP2);
  not not_76 (not_76_out, OP1);
  not not_77 (not_77_out, OP0);
  not not_78 (not_78_out, F4);
  not not_79 (not_79_out, F3);
  not not_80 (not_80_out, F2);
  not not_81 (not_81_out, F1);
  not not_82 (not_82_out, F0);
  not not_83 (not_83_out, OP5);
  not not_84 (not_84_out, OP4);
  not not_85 (not_85_out, OP3);
  not not_86 (not_86_out, OP2);
  not not_87 (not_87_out, OP1);
  not not_88 (not_88_out, OP0);
  not not_89 (not_89_out, F4);
  not not_90 (not_90_out, F3);
  not not_91 (not_91_out, F2);
  not not_92 (not_92_out, F1);
  not not_93 (not_93_out, OP5);
  not not_94 (not_94_out, OP4);
  not not_95 (not_95_out, OP3);
  not not_96 (not_96_out, OP2);
  not not_97 (not_97_out, OP1);
  not not_98 (not_98_out, OP0);
  not not_99 (not_99_out, F4);
  not not_100 (not_100_out, F3);
  not not_101 (not_101_out, F2);
  not not_102 (not_102_out, F0);
  not not_103 (not_103_out, OP5);
  not not_104 (not_104_out, OP4);
  not not_105 (not_105_out, OP3);
  not not_106 (not_106_out, OP2);
  not not_107 (not_107_out, OP1);
  not not_108 (not_108_out, OP0);
  not not_109 (not_109_out, F4);
  not not_110 (not_110_out, F3);
  not not_111 (not_111_out, F1);
  not not_112 (not_112_out, F0);
  not not_113 (not_113_out, OP5);
  not not_114 (not_114_out, OP4);
  not not_115 (not_115_out, OP3);
  not not_116 (not_116_out, OP2);
  not not_117 (not_117_out, OP1);
  not not_118 (not_118_out, OP0);
  not not_119 (not_119_out, F4);
  not not_120 (not_120_out, F3);
  not not_121 (not_121_out, F1);
  not not_122 (not_122_out, OP5);
  not not_123 (not_123_out, OP4);
  not not_124 (not_124_out, OP3);
  not not_125 (not_125_out, OP2);
  not not_126 (not_126_out, OP1);
  not not_127 (not_127_out, OP0);
  not not_128 (not_128_out, F4);
  not not_129 (not_129_out, F3);
  not not_130 (not_130_out, OP5);
  not not_131 (not_131_out, OP4);
  not not_132 (not_132_out, OP3);
  not not_133 (not_133_out, OP2);
  not not_134 (not_134_out, OP1);
  not not_135 (not_135_out, OP0);
  not not_136 (not_136_out, F4);
  not not_137 (not_137_out, F2);
  not not_138 (not_138_out, F0);
  not not_139 (not_139_out, OP5);
  not not_140 (not_140_out, OP4);
  not not_141 (not_141_out, OP3);
  not not_142 (not_142_out, OP2);
  not not_143 (not_143_out, OP1);
  not not_144 (not_144_out, OP0);
  not not_145 (not_145_out, F4);
  not not_146 (not_146_out, F2);
  not not_147 (not_147_out, OP5);
  not not_148 (not_148_out, OP4);
  not not_149 (not_149_out, OP3);
  not not_150 (not_150_out, OP2);
  not not_151 (not_151_out, OP5);
  not not_152 (not_152_out, OP4);
  not not_153 (not_153_out, OP2);
  not not_154 (not_154_out, OP1);
  not not_155 (not_155_out, OP0);
  not not_156 (not_156_out, OP5);
  not not_157 (not_157_out, OP4);
  not not_158 (not_158_out, OP1);
  not not_159 (not_159_out, OP0);
  not not_160 (not_160_out, OP5);
  not not_161 (not_161_out, OP4);
  not not_162 (not_162_out, OP2);
  not not_163 (not_163_out, OP1);
  not not_164 (not_164_out, OP5);
  not not_165 (not_165_out, OP4);
  not not_166 (not_166_out, OP2);
  not not_167 (not_167_out, OP0);
  not not_168 (not_168_out, OP5);
  not not_169 (not_169_out, OP4);
  not not_170 (not_170_out, OP1);
  not not_171 (not_171_out, OP4);
  not not_172 (not_172_out, OP3);
  not not_173 (not_173_out, OP2);
  not not_174 (not_174_out, OP5);
  not not_175 (not_175_out, OP4);
  not not_176 (not_176_out, OP3);
  not not_177 (not_177_out, OP2);
  not not_178 (not_178_out, OP1);
  not not_179 (not_179_out, OP0);
  not not_180 (not_180_out, F4);
  not not_181 (not_181_out, F3);
  not not_182 (not_182_out, F2);
  not not_183 (not_183_out, OP5);
  not not_184 (not_184_out, OP4);
  not not_185 (not_185_out, OP3);
  not not_186 (not_186_out, OP2);
  not not_187 (not_187_out, OP1);
  not not_188 (not_188_out, OP0);
  not not_189 (not_189_out, F4);
  not not_190 (not_190_out, F3);
  not not_191 (not_191_out, F0);
  not not_192 (not_192_out, OP4);
  not not_193 (not_193_out, OP3);
  not not_194 (not_194_out, OP1);
  not not_195 (not_195_out, OP0);
  not not_196 (not_196_out, OP5);
  not not_197 (not_197_out, OP4);
  not not_198 (not_198_out, OP3);
  not not_199 (not_199_out, OP2);
  not not_200 (not_200_out, OP1);
  not not_201 (not_201_out, OP0);
  not not_202 (not_202_out, F5);
  not not_203 (not_203_out, F4);
  not not_204 (not_204_out, F1);
  not not_205 (not_205_out, F0);
  not not_206 (not_206_out, OP5);
  not not_207 (not_207_out, OP4);
  not not_208 (not_208_out, OP2);
  not not_209 (not_209_out, OP1);
  not not_210 (not_210_out, OP0);
  not not_211 (not_211_out, OP5);
  not not_212 (not_212_out, OP4);
  not not_213 (not_213_out, OP2);
  not not_214 (not_214_out, OP1);
  not not_215 (not_215_out, OP5);
  not not_216 (not_216_out, OP4);
  not not_217 (not_217_out, OP2);
  not not_218 (not_218_out, OP0);
  not not_219 (not_219_out, OP4);
  not not_220 (not_220_out, OP3);
  not not_221 (not_221_out, OP2);
  not not_222 (not_222_out, OP4);
  not not_223 (not_223_out, OP2);
  not not_224 (not_224_out, OP4);
  not not_225 (not_225_out, OP3);
  not not_226 (not_226_out, OP1);
  not not_227 (not_227_out, OP0);
  not not_228 (not_228_out, OP5);
  not not_229 (not_229_out, OP4);
  not not_230 (not_230_out, OP3);
  not not_231 (not_231_out, OP2);
  not not_232 (not_232_out, OP1);
  not not_233 (not_233_out, OP0);
  not not_234 (not_234_out, F5);
  not not_235 (not_235_out, F4);
  not not_236 (not_236_out, F3);
  not not_237 (not_237_out, F2);
  not not_238 (not_238_out, F1);
  not not_239 (not_239_out, F0);
  not not_240 (not_240_out, OP5);
  not not_241 (not_241_out, OP4);
  not not_242 (not_242_out, OP3);
  not not_243 (not_243_out, OP2);
  not not_244 (not_244_out, OP1);
  not not_245 (not_245_out, OP0);
  not not_246 (not_246_out, F5);
  not not_247 (not_247_out, F4);
  not not_248 (not_248_out, F3);
  not not_249 (not_249_out, F2);
  not not_250 (not_250_out, OP5);
  not not_251 (not_251_out, OP4);
  not not_252 (not_252_out, OP3);
  not not_253 (not_253_out, OP2);
  not not_254 (not_254_out, OP1);
  not not_255 (not_255_out, OP0);
  not not_256 (not_256_out, F5);
  not not_257 (not_257_out, F4);
  not not_258 (not_258_out, F3);
  not not_259 (not_259_out, F2);
  not not_260 (not_260_out, F0);
  not not_261 (not_261_out, OP5);
  not not_262 (not_262_out, OP4);
  not not_263 (not_263_out, OP3);
  not not_264 (not_264_out, OP2);
  not not_265 (not_265_out, OP1);
  not not_266 (not_266_out, OP0);
  not not_267 (not_267_out, F4);
  not not_268 (not_268_out, F3);
  not not_269 (not_269_out, F2);
  not not_270 (not_270_out, F1);
  not not_271 (not_271_out, F0);
  not not_272 (not_272_out, OP5);
  not not_273 (not_273_out, OP4);
  not not_274 (not_274_out, OP3);
  not not_275 (not_275_out, OP2);
  not not_276 (not_276_out, OP1);
  not not_277 (not_277_out, OP0);
  not not_278 (not_278_out, F4);
  not not_279 (not_279_out, F3);
  not not_280 (not_280_out, F2);
  not not_281 (not_281_out, F1);
  not not_282 (not_282_out, OP5);
  not not_283 (not_283_out, OP4);
  not not_284 (not_284_out, OP3);
  not not_285 (not_285_out, OP2);
  not not_286 (not_286_out, OP1);
  not not_287 (not_287_out, OP0);
  not not_288 (not_288_out, F4);
  not not_289 (not_289_out, F3);
  not not_290 (not_290_out, F2);
  not not_291 (not_291_out, F0);
  not not_292 (not_292_out, OP5);
  not not_293 (not_293_out, OP4);
  not not_294 (not_294_out, OP3);
  not not_295 (not_295_out, OP2);
  not not_296 (not_296_out, OP1);
  not not_297 (not_297_out, OP0);
  not not_298 (not_298_out, F4);
  not not_299 (not_299_out, F3);
  not not_300 (not_300_out, F1);
  not not_301 (not_301_out, F0);
  not not_302 (not_302_out, OP5);
  not not_303 (not_303_out, OP4);
  not not_304 (not_304_out, OP3);
  not not_305 (not_305_out, OP2);
  not not_306 (not_306_out, OP1);
  not not_307 (not_307_out, OP0);
  not not_308 (not_308_out, F4);
  not not_309 (not_309_out, F3);
  not not_310 (not_310_out, F1);
  not not_311 (not_311_out, OP5);
  not not_312 (not_312_out, OP4);
  not not_313 (not_313_out, OP3);
  not not_314 (not_314_out, OP2);
  not not_315 (not_315_out, OP1);
  not not_316 (not_316_out, OP0);
  not not_317 (not_317_out, F4);
  not not_318 (not_318_out, F3);
  not not_319 (not_319_out, OP5);
  not not_320 (not_320_out, OP4);
  not not_321 (not_321_out, OP3);
  not not_322 (not_322_out, OP2);
  not not_323 (not_323_out, OP1);
  not not_324 (not_324_out, OP0);
  not not_325 (not_325_out, F4);
  not not_326 (not_326_out, F2);
  not not_327 (not_327_out, F0);
  not not_328 (not_328_out, OP5);
  not not_329 (not_329_out, OP4);
  not not_330 (not_330_out, OP3);
  not not_331 (not_331_out, OP2);
  not not_332 (not_332_out, OP1);
  not not_333 (not_333_out, OP0);
  not not_334 (not_334_out, F4);
  not not_335 (not_335_out, F2);
  not not_336 (not_336_out, OP5);
  not not_337 (not_337_out, OP4);
  not not_338 (not_338_out, OP3);
  not not_339 (not_339_out, OP2);
  not not_340 (not_340_out, OP1);
  not not_341 (not_341_out, OP0);
  not not_342 (not_342_out, F4);
  not not_343 (not_343_out, F3);
  not not_344 (not_344_out, F2);
  not not_345 (not_345_out, OP5);
  not not_346 (not_346_out, OP4);
  not not_347 (not_347_out, OP3);
  not not_348 (not_348_out, OP2);
  not not_349 (not_349_out, OP1);
  not not_350 (not_350_out, OP0);
  not not_351 (not_351_out, F4);
  not not_352 (not_352_out, F3);
  not not_353 (not_353_out, F0);
  not not_354 (not_354_out, OP5);
  not not_355 (not_355_out, OP4);
  not not_356 (not_356_out, OP3);
  not not_357 (not_357_out, OP1);
  not not_358 (not_358_out, OP0);
  not not_359 (not_359_out, OP5);
  not not_360 (not_360_out, OP4);
  not not_361 (not_361_out, OP3);
  not not_362 (not_362_out, OP1);
  not not_363 (not_363_out, OP5);
  not not_364 (not_364_out, OP4);
  not not_365 (not_365_out, OP3);
  not not_366 (not_366_out, OP2);
  not not_367 (not_367_out, OP1);
  not not_368 (not_368_out, OP0);
  not not_369 (not_369_out, F5);
  not not_370 (not_370_out, F4);
  not not_371 (not_371_out, F2);
  not not_372 (not_372_out, F1);
  not not_373 (not_373_out, F0);
  not not_374 (not_374_out, OP5);
  not not_375 (not_375_out, OP4);
  not not_376 (not_376_out, OP3);
  not not_377 (not_377_out, OP2);
  not not_378 (not_378_out, OP1);
  not not_379 (not_379_out, OP0);
  not not_380 (not_380_out, F5);
  not not_381 (not_381_out, F4);
  not not_382 (not_382_out, F2);
  not not_383 (not_383_out, F1);
  not not_384 (not_384_out, F0);
  not not_385 (not_385_out, OP5);
  not not_386 (not_386_out, OP4);
  not not_387 (not_387_out, OP3);
  not not_388 (not_388_out, OP2);
  not not_389 (not_389_out, OP0);
  not not_390 (not_390_out, OP5);
  not not_391 (not_391_out, OP4);
  not not_392 (not_392_out, OP3);
  not not_393 (not_393_out, OP2);
  not not_394 (not_394_out, OP5);
  not not_395 (not_395_out, OP4);
  not not_396 (not_396_out, OP3);
  not not_397 (not_397_out, OP2);
  and and_1 (and_1_out, OP5, not_1_out, not_2_out, not_3_out, OP1, OP0);
  and and_2 (and_2_out, OP5, not_4_out, not_5_out, OP2, not_6_out, not_7_out);
  and and_3 (MemWrite, OP5, not_8_out, OP3, not_9_out, OP1, OP0);
  and and_4 (and_4_out, not_10_out, not_11_out, OP3, not_12_out, not_13_out, not_14_out);
  and and_5 (and_5_out, not_15_out, not_16_out, OP3, OP2, not_17_out, not_18_out);
  and and_6 (and_6_out, not_19_out, not_20_out, OP3, not_21_out, not_22_out, OP0);
  and and_7 (and_7_out, not_23_out, not_24_out, OP3, not_25_out, OP1, not_26_out);
  and and_8 (and_8_out, not_27_out, not_28_out, OP3, OP2, not_29_out, OP0);
  and and_9 (and_9_out, OP5, not_30_out, not_31_out, not_32_out, OP1, OP0);
  and and_10 (and_10_out, OP5, not_33_out, OP3, not_34_out, OP1, OP0);
  and and_11 (and_11_out, OP5, not_35_out, not_36_out, OP2, not_37_out, not_38_out);
  and and_12 (and_12_out, not_39_out, not_40_out, not_41_out, not_42_out, not_43_out, not_44_out, not_45_out, not_46_out, not_47_out, not_48_out, not_49_out, not_50_out);
  and and_13 (and_13_out, not_51_out, not_52_out, not_53_out, not_54_out, not_55_out, not_56_out, not_57_out, not_58_out, not_59_out, not_60_out, F1, F0);
  and and_14 (and_14_out, not_61_out, not_62_out, not_63_out, not_64_out, not_65_out, not_66_out, not_67_out, not_68_out, not_69_out, not_70_out, F1, not_71_out);
  and and_15 (and_15_out, not_72_out, not_73_out, not_74_out, not_75_out, not_76_out, not_77_out, F5, not_78_out, not_79_out, not_80_out, not_81_out, not_82_out);
  and and_16 (and_16_out, not_83_out, not_84_out, not_85_out, not_86_out, not_87_out, not_88_out, F5, not_89_out, not_90_out, not_91_out, not_92_out, F0);
  and and_17 (and_17_out, not_93_out, not_94_out, not_95_out, not_96_out, not_97_out, not_98_out, F5, not_99_out, not_100_out, not_101_out, F1, not_102_out);
  and and_18 (and_18_out, not_103_out, not_104_out, not_105_out, not_106_out, not_107_out, not_108_out, F5, not_109_out, not_110_out, F2, not_111_out, not_112_out);
  and and_19 (and_19_out, not_113_out, not_114_out, not_115_out, not_116_out, not_117_out, not_118_out, F5, not_119_out, not_120_out, F2, not_121_out, F0);
  and and_20 (and_20_out, not_122_out, not_123_out, not_124_out, not_125_out, not_126_out, not_127_out, F5, not_128_out, not_129_out, F2, F1, F0);
  and and_21 (and_21_out, not_130_out, not_131_out, not_132_out, not_133_out, not_134_out, not_135_out, F5, not_136_out, F3, not_137_out, F1, not_138_out);
  and and_22 (and_22_out, not_139_out, not_140_out, not_141_out, not_142_out, not_143_out, not_144_out, F5, not_145_out, F3, not_146_out, F1, F0);
  and and_23 (and_23_out, not_147_out, not_148_out, not_149_out, not_150_out, OP1, OP0);
  and and_24 (and_24_out, not_151_out, not_152_out, OP3, not_153_out, not_154_out, not_155_out);
  and and_25 (and_25_out, not_156_out, not_157_out, OP3, OP2, not_158_out, not_159_out);
  and and_26 (and_26_out, not_160_out, not_161_out, OP3, not_162_out, not_163_out, OP0);
  and and_27 (and_27_out, not_164_out, not_165_out, OP3, not_166_out, OP1, not_167_out);
  and and_28 (and_28_out, not_168_out, not_169_out, OP3, OP2, not_170_out, OP0);
  and and_29 (and_29_out, OP5, not_171_out, not_172_out, not_173_out, OP1, OP0);
  and and_30 (and_30_out, not_174_out, not_175_out, not_176_out, not_177_out, not_178_out, not_179_out, F5, not_180_out, not_181_out, not_182_out, F1, F0);
  and and_31 (and_31_out, not_183_out, not_184_out, not_185_out, not_186_out, not_187_out, not_188_out, F5, not_189_out, not_190_out, F2, F1, not_191_out);
  and and_32 (and_32_out, OP5, not_192_out, not_193_out, OP2, not_194_out, not_195_out);
  and and_33 (SysCALL, not_196_out, not_197_out, not_198_out, not_199_out, not_200_out, not_201_out, not_202_out, not_203_out, F3, F2, not_204_out, not_205_out);
  and and_34 (and_34_out, not_206_out, not_207_out, OP3, not_208_out, not_209_out, not_210_out);
  and and_35 (and_35_out, not_211_out, not_212_out, OP3, not_213_out, not_214_out, OP0);
  and and_36 (and_36_out, not_215_out, not_216_out, OP3, not_217_out, OP1, not_218_out);
  and and_37 (and_37_out, OP5, not_219_out, not_220_out, not_221_out, OP1, OP0);
  and and_38 (and_38_out, OP5, not_222_out, OP3, not_223_out, OP1, OP0);
  and and_39 (and_39_out, OP5, not_224_out, not_225_out, OP2, not_226_out, not_227_out);
  and and_40 (and_40_out, not_228_out, not_229_out, not_230_out, not_231_out, not_232_out, not_233_out, not_234_out, not_235_out, not_236_out, not_237_out, not_238_out, not_239_out);
  and and_41 (and_41_out, not_240_out, not_241_out, not_242_out, not_243_out, not_244_out, not_245_out, not_246_out, not_247_out, not_248_out, not_249_out, F1, F0);
  and and_42 (and_42_out, not_250_out, not_251_out, not_252_out, not_253_out, not_254_out, not_255_out, not_256_out, not_257_out, not_258_out, not_259_out, F1, not_260_out);
  and and_43 (and_43_out, not_261_out, not_262_out, not_263_out, not_264_out, not_265_out, not_266_out, F5, not_267_out, not_268_out, not_269_out, not_270_out, not_271_out);
  and and_44 (and_44_out, not_272_out, not_273_out, not_274_out, not_275_out, not_276_out, not_277_out, F5, not_278_out, not_279_out, not_280_out, not_281_out, F0);
  and and_45 (and_45_out, not_282_out, not_283_out, not_284_out, not_285_out, not_286_out, not_287_out, F5, not_288_out, not_289_out, not_290_out, F1, not_291_out);
  and and_46 (and_46_out, not_292_out, not_293_out, not_294_out, not_295_out, not_296_out, not_297_out, F5, not_298_out, not_299_out, F2, not_300_out, not_301_out);
  and and_47 (and_47_out, not_302_out, not_303_out, not_304_out, not_305_out, not_306_out, not_307_out, F5, not_308_out, not_309_out, F2, not_310_out, F0);
  and and_48 (and_48_out, not_311_out, not_312_out, not_313_out, not_314_out, not_315_out, not_316_out, F5, not_317_out, not_318_out, F2, F1, F0);
  and and_49 (and_49_out, not_319_out, not_320_out, not_321_out, not_322_out, not_323_out, not_324_out, F5, not_325_out, F3, not_326_out, F1, not_327_out);
  and and_50 (and_50_out, not_328_out, not_329_out, not_330_out, not_331_out, not_332_out, not_333_out, F5, not_334_out, F3, not_335_out, F1, F0);
  and and_51 (and_51_out, not_336_out, not_337_out, not_338_out, not_339_out, not_340_out, not_341_out, F5, not_342_out, not_343_out, not_344_out, F1, F0);
  and and_52 (and_52_out, not_345_out, not_346_out, not_347_out, not_348_out, not_349_out, not_350_out, F5, not_351_out, not_352_out, F2, F1, not_353_out);
  and and_53 (BEQ, not_354_out, not_355_out, not_356_out, OP2, not_357_out, not_358_out);
  and and_54 (BNE, not_359_out, not_360_out, not_361_out, OP2, not_362_out, OP0);
  and and_55 (JR, not_363_out, not_364_out, not_365_out, not_366_out, not_367_out, not_368_out, not_369_out, not_370_out, F3, not_371_out, not_372_out, not_373_out);
  and and_56 (and_56_out, not_374_out, not_375_out, not_376_out, not_377_out, not_378_out, not_379_out, not_380_out, not_381_out, F3, not_382_out, not_383_out, not_384_out);
  and and_57 (and_57_out, not_385_out, not_386_out, not_387_out, not_388_out, OP1, not_389_out);
  and and_58 (and_58_out, not_390_out, not_391_out, not_392_out, not_393_out, OP1, OP0);
  and and_59 (JAL, not_394_out, not_395_out, not_396_out, not_397_out, OP1, OP0);
  or or_1 (MemToReg, and_1_out, and_2_out);
  or or_2 (ALU_SRC, and_4_out, and_5_out, and_6_out, and_7_out, and_8_out, and_9_out, and_10_out, and_11_out);
  or or_3 (SignedExt, and_34_out, and_35_out, and_36_out, and_37_out, and_38_out, and_39_out);
  or or_4 (JUMP, and_56_out, and_57_out, and_58_out);
  or or_5 (RegWrite, and_12_out, and_13_out, and_14_out, and_15_out, and_16_out, and_17_out, and_18_out, and_19_out, and_20_out, and_21_out, and_22_out, and_23_out, and_24_out, and_25_out, and_26_out, and_27_out, and_28_out, and_29_out, and_30_out, and_31_out, and_32_out);
  or or_6 (RegDst, and_40_out, and_41_out, and_42_out, and_43_out, and_44_out, and_45_out, and_46_out, and_47_out, and_48_out, and_49_out, and_50_out, and_51_out, and_52_out);
endmodule

// CCMB_Control
module CCMB_Control (
  input  OP0,
  input  OP1,
  input  OP2,
  input  OP3,
  input  OP4,
  input  OP5,
  input  F0,
  input  F1,
  input  F2,
  input  F3,
  input  F4,
  input  F5,
  output LBU,
  output BLTZ
);

  wire not_1_out, not_2_out, not_3_out, not_4_out, not_5_out, not_6_out, not_7_out, not_8_out, not_9_out;

  not not_1 (not_1_out, OP4);
  not not_2 (not_2_out, OP3);
  not not_3 (not_3_out, OP1);
  not not_4 (not_4_out, OP0);
  not not_5 (not_5_out, OP5);
  not not_6 (not_6_out, OP4);
  not not_7 (not_7_out, OP3);
  not not_8 (not_8_out, OP2);
  not not_9 (not_9_out, OP1);
  and and_1 (LBU, OP5, not_1_out, not_2_out, OP2, not_3_out, not_4_out);
  and and_2 (BLTZ, not_5_out, not_6_out, not_7_out, not_8_out, not_9_out, OP0);
endmodule

// ALU
module MIPS_ALU (
  input  [4:0] shamt,
  input  [31:0] X,
  input  [31:0] Y,
  input  [3:0] AluOP,
  output Equal,
  output [31:0] Result,
  output [31:0] Result_2
);

  wire [0:0] comparator_1_lt, comparator_2_lt;
  wire [31:0] adder_1_out, AND_out, divider_1_out, divider_1_rem, multiplier_1_cout, multiplier_1_out,
       NOR_out, OR_out, shifter_1_out, shifter_2_out, shifter_3_out, subtractor_1_out, XOR_out;

  assign AND_out = X & Y;  // AND_Gate AND, 32 bits wide
  assign OR_out = X | Y;  // OR_Gate OR, 32 bits wide
  Shifter #(.width(32), .shift("ll")) shifter_1 (.in(Y), .\dist (shamt), .out(shifter_1_out));
  Shifter #(.width(32), .shift("ar")) shifter_2 (.in(Y), .\dist (shamt), .out(shifter_2_out));
  Shifter #(.width(32), .shift("lr")) shifter_3 (.in(Y), .\dist (shamt), .out(shifter_3_out));
  Multiplier #(.width(32)) multiplier_1 (.a(X), .b(Y), .out(multiplier_1_out), .cout(multiplier_1_cout));  // open: cin
  Divider #(.width(32)) divider_1 (.a(X), .b(Y), .out(divider_1_out), .rem(divider_1_rem));  // open: upper
  Adder #(.width(32)) adder_1 (.a(X), .b(Y), .out(adder_1_out));  // open: cin, cout
  Subtractor #(.width(32)) subtractor_1 (.a(X), .b(Y), .out(subtractor_1_out));  // open: bin, bout
  assign XOR_out = X ^ Y;  // XOR_Gate XOR, 32 bits wide
  assign NOR_out = ~(X | Y);  // NOR_Gate NOR, 32 bits wide
  Comparator #(.width(32), .mode("twosComplement")) comparator_1 (
    .a(X), .b(Y), .eq(Equal), .lt(comparator_1_lt[0]));  // open: gt
  Comparator #(.width(32), .mode("unsigned")) comparator_2 (.a(X), .b(Y), .lt(comparator_2_lt[0]));  // open: gt, eq
  Multiplexer #(.select(4), .width(32), .disabled("Z"), .enable("false")) multiplexer_1 (
    .in0(shifter_1_out), .in1(shifter_2_out), .in2(shifter_3_out), .in3(multiplier_1_out),
    .in4(divider_1_out), .in5(adder_1_out), .in6(subtractor_1_out), .in7(AND_out), .in8(OR_out),
    .in9(XOR_out), .in10(NOR_out), .in11({{31{1'b0}}, comparator_1_lt[0]}),
    .in12({{31{1'b0}}, comparator_2_lt[0]}), .in13({32{1'b0}}), .in14({32{1'b0}}), .in15({32{1'b0}}),
    .out(Result), .sel(AluOP));
  Multiplexer #(.select(4), .width(32), .disabled("Z"), .enable("false")) multiplexer_2 (
    .in0({32{1'b0}}), .in1({32{1'b0}}), .in2({32{1'b0}}), .in3(multiplier_1_cout), .in4(divider_1_rem),
    .in5({32{1'b0}}), .in6({32{1'b0}}), .in7({32{1'b0}}), .in8({32{1'b0}}), .in9({32{1'b0}}),
    .in10({32{1'b0}}), .in11({32{1'b0}}), .in12({32{1'b0}}), .in13({32{1'b0}}), .in14({32{1'b0}}),
    .in15({32{1'b0}}), .out(Result_2), .sel(AluOP));

  // Other names for the same wires on the sheet: Result2[31:0] = Result_2; S[3:0] = AluOP

  // Notes on the sheet:
  //   不要改变此引脚区域内容，也不要改变ALU封装形式
  //   输入引脚
  //   输出引脚
endmodule

module MIPS_Regifile (
  input  [31:0] Din,
  input  Clk,
  input  WE,
  input  [4:0] R1_num,
  input  [4:0] W_num,
  input  [4:0] R2_num,
  output [31:0] R1,
  output [31:0] R2
);

  // RegisterFile registerfile_1: pin names not known; wires that end beside it: Din, Clk, WE, W_num, R1_num, R2_num, R1, R2
endmodule

// IF/ID
module IF_ID (
  input  [31:0] PCr_in,
  input  [31:0] PC_in,
  input  [31:0] IR_in,
  input  [31:0] PC_G_in,
  input  [1:0] HG_in,
  input  Reset,
  input  CLK,
  input  Enable,
  output [31:0] PCr_out,
  output [31:0] PC_out,
  output [31:0] IR_out,
  output [31:0] PC_G_out,
  output [1:0] HG_out
);

  wire [1:0] multiplexer_5_out;
  wire [31:0] multiplexer_1_out, multiplexer_2_out, multiplexer_3_out, multiplexer_4_out;

  Multiplexer #(.select(1), .width(32), .disabled("Z"), .enable("false")) multiplexer_1 (
    .in0(PCr_in), .in1({32{1'b0}}), .out(multiplexer_1_out), .sel(Reset));
  Multiplexer #(.select(1), .width(32), .disabled("Z"), .enable("false")) multiplexer_2 (
    .in0(PC_in), .in1({32{1'b0}}), .out(multiplexer_2_out), .sel(Reset));
  Multiplexer #(.select(1), .width(32), .disabled("Z"), .enable("false")) multiplexer_3 (
    .in0(IR_in), .in1({32{1'b0}}), .out(multiplexer_3_out), .sel(Reset));
  Multiplexer #(.select(1), .width(32), .disabled("Z"), .enable("false")) multiplexer_4 (
    .in0(PC_G_in), .in1({32{1'b0}}), .out(multiplexer_4_out), .sel(Reset));
  Multiplexer #(.select(1), .width(2), .disabled("Z"), .enable("false")) multiplexer_5 (
    .in0(HG_in), .in1(2'b00), .out(multiplexer_5_out), .sel(Reset));
  Register #(.width(32), .trigger("rising"), .Select("low")) register_1 (
    .D(multiplexer_1_out), .en(Enable), .Q(PCr_out), .clk(CLK));  // open: clr
  Register #(.width(32), .trigger("rising"), .Select("low")) register_2 (
    .D(multiplexer_2_out), .en(Enable), .Q(PC_out), .clk(CLK));  // open: clr
  Register #(.width(32), .trigger("rising"), .Select("low")) register_3 (
    .D(multiplexer_3_out), .en(Enable), .Q(IR_out), .clk(CLK));  // open: clr
  Register #(.width(32), .trigger("rising"), .Select("low")) register_4 (
    .D(multiplexer_4_out), .en(Enable), .Q(PC_G_out), .clk(CLK));  // open: clr
  Register #(.width(2), .trigger("rising"), .Select("low")) register_5 (
    .D(multiplexer_5_out), .en(Enable), .Q(HG_out), .clk(CLK));  // open: clr

  // Notes on the sheet:
  //   高电平有效
endmodule

// ID/EX
module ID_EX (
  input  [31:0] IR_in,
  input  BEQ_in,
  input  [31:0] PC_in,
  input  BNE_in,
  input  [31:0] R1_in,
  input  MemToReg_in,
  input  MemWrite_in,
  input  [31:0] R2_in,
  input  AluSrcB_in,
  input  [31:0] Imm_in,
  input  RegWrite_in,
  input  [31:0] Address_in,
  input  JAL_in,
  input  [3:0] AluOP_in,
  input  RegDst_in,
  input  [4:0] Shamt_in,
  input  Syscall_in,
  input  Halt_in,
  input  JMP_in,
  input  LBU_in,
  input  JR_in,
  input  BLTZ_in,
  input  [4:0] W__in,
  input  [31:0] PCr_in,
  input  [1:0] HG_in,
  input  [31:0] PCG_in,
  input  [2:0] Interrupt_in,
  input  Reset,
  input  Enable,
  input  CLK,
  output [31:0] IR_out,
  output BEQ_out,
  output [31:0] PC_out,
  output BNE_out,
  output [31:0] R1_out,
  output MemToReg_out,
  output MemWrite_out,
  output [31:0] R2_out,
  output AluSrcB_out,
  output [31:0] Imm_out,
  output RegWrite_out,
  output [31:0] Address_out,
  output JAL_out,
  output [3:0] AluOP_out,
  output RegDst_out,
  output [4:0] Shamt_out,
  output Syscall_out,
  output Halt_out,
  output JMP_out,
  output LBU_out,
  output JR_out,
  output BLTZ_out,
  output [4:0] W__out,
  output [31:0] PCr_out,
  output [1:0] HG_out,
  output [31:0] PCG_out,
  output [2:0] Interrupt_out
);

  wire multiplexer_9_out, multiplexer_10_out, multiplexer_11_out, multiplexer_15_out, multiplexer_16_out,
       multiplexer_17_out, multiplexer_18_out, multiplexer_19_out, multiplexer_20_out, multiplexer_21_out,
       multiplexer_22_out, multiplexer_23_out, multiplexer_24_out, multiplexer_25_out;
  wire [1:0] multiplexer_13_out;
  wire [2:0] multiplexer_14_out;
  wire [3:0] multiplexer_7_out;
  wire [4:0] multiplexer_8_out, multiplexer_12_out;
  wire [31:0] multiplexer_1_out, multiplexer_2_out, multiplexer_3_out, multiplexer_4_out, multiplexer_5_out,
       multiplexer_6_out, multiplexer_26_out, multiplexer_27_out;

  Multiplexer #(.select(1), .width(32), .disabled("Z"), .enable("false")) multiplexer_1 (
    .in0(IR_in), .in1({32{1'b0}}), .out(multiplexer_1_out), .sel(Reset));
  Multiplexer #(.select(1), .width(32), .disabled("Z"), .enable("false")) multiplexer_2 (
    .in0(PC_in), .in1({32{1'b0}}), .out(multiplexer_2_out), .sel(Reset));
  Multiplexer #(.select(1), .width(32), .disabled("Z"), .enable("false")) multiplexer_3 (
    .in0(R1_in), .in1({32{1'b0}}), .out(multiplexer_3_out), .sel(Reset));
  Multiplexer #(.select(1), .width(32), .disabled("Z"), .enable("false")) multiplexer_4 (
    .in0(R2_in), .in1({32{1'b0}}), .out(multiplexer_4_out), .sel(Reset));
  Multiplexer #(.select(1), .width(32), .disabled("Z"), .enable("false")) multiplexer_5 (
    .in0(Imm_in), .in1({32{1'b0}}), .out(multiplexer_5_out), .sel(Reset));
  Multiplexer #(.select(1), .width(32), .disabled("Z"), .enable("false")) multiplexer_6 (
    .in0(Address_in), .in1({32{1'b0}}), .out(multiplexer_6_out), .sel(Reset));
  Multiplexer #(.select(1), .width(4), .disabled("Z"), .enable("false")) multiplexer_7 (
    .in0(AluOP_in), .in1(4'b0000), .out(multiplexer_7_out), .sel(Reset));
  Multiplexer #(.select(1), .width(5), .disabled("Z"), .enable("false")) multiplexer_8 (
    .in0(Shamt_in), .in1({5{1'b0}}), .out(multiplexer_8_out), .sel(Reset));
  Multiplexer #(.select(1), .width(1), .disabled("Z"), .enable("false")) multiplexer_9 (
    .in0(Halt_in), .in1(1'b0), .out(multiplexer_9_out), .sel(Reset));
  Multiplexer #(.select(1), .width(1), .disabled("Z"), .enable("false")) multiplexer_10 (
    .in0(LBU_in), .in1(1'b0), .out(multiplexer_10_out), .sel(Reset));
  Multiplexer #(.select(1), .width(1), .disabled("Z"), .enable("false")) multiplexer_11 (
    .in0(BLTZ_in), .in1(1'b0), .out(multiplexer_11_out), .sel(Reset));
  Multiplexer #(.select(1), .width(5), .disabled("Z"), .enable("false")) multiplexer_12 (
    .in0(W__in), .in1({5{1'b0}}), .out(multiplexer_12_out), .sel(Reset));
  Multiplexer #(.select(1), .width(2), .disabled("Z"), .enable("false")) multiplexer_13 (
    .in0(HG_in), .in1(2'b00), .out(multiplexer_13_out), .sel(Reset));
  Multiplexer #(.select(1), .width(3), .disabled("Z"), .enable("false")) multiplexer_14 (
    .in0(Interrupt_in), .in1(3'b000), .out(multiplexer_14_out), .sel(Reset));
  Register #(.width(32), .trigger("rising"), .Select("low")) register_1 (
    .D(multiplexer_1_out), .en(Enable), .Q(IR_out), .clk(CLK));  // open: clr
  Register #(.width(32), .trigger("rising"), .Select("low")) register_2 (
    .D(multiplexer_2_out), .en(Enable), .Q(PC_out), .clk(CLK));  // open: clr
  Register #(.width(32), .trigger("rising"), .Select("low")) register_3 (
    .D(multiplexer_3_out), .en(Enable), .Q(R1_out), .clk(CLK));  // open: clr
  Register #(.width(32), .trigger("rising"), .Select("low")) register_4 (
    .D(multiplexer_4_out), .en(Enable), .Q(R2_out), .clk(CLK));  // open: clr
  Register #(.width(32), .trigger("rising"), .Select("low")) register_5 (
    .D(multiplexer_5_out), .en(Enable), .Q(Imm_out), .clk(CLK));  // open: clr
  Register #(.width(32), .trigger("rising"), .Select("low")) register_6 (
    .D(multiplexer_6_out), .en(Enable), .Q(Address_out), .clk(CLK));  // open: clr
  Register #(.width(4), .trigger("rising"), .Select("low")) register_7 (
    .D(multiplexer_7_out), .en(Enable), .Q(AluOP_out), .clk(CLK));  // open: clr
  Register #(.width(5), .trigger("rising"), .Select("low")) register_8 (
    .D(multiplexer_8_out), .en(Enable), .Q(Shamt_out), .clk(CLK));  // open: clr
  Register #(.width(1), .trigger("rising"), .Select("low")) register_9 (
    .D(multiplexer_9_out), .en(Enable), .Q(Halt_out), .clk(CLK));  // open: clr
  Register #(.width(1), .trigger("rising"), .Select("low")) register_10 (
    .D(multiplexer_10_out), .en(Enable), .Q(LBU_out), .clk(CLK));  // open: clr
  Register #(.width(1), .trigger("rising"), .Select("low")) register_11 (
    .D(multiplexer_11_out), .en(Enable), .Q(BLTZ_out), .clk(CLK));  // open: clr
  Register #(.width(5), .trigger("rising"), .Select("low")) register_12 (
    .D(multiplexer_12_out), .en(Enable), .Q(W__out), .clk(CLK));  // open: clr
  Register #(.width(2), .trigger("rising"), .Select("low")) register_13 (
    .D(multiplexer_13_out), .en(Enable), .Q(HG_out), .clk(CLK));  // open: clr
  Register #(.width(3), .trigger("rising"), .Select("low")) register_14 (
    .D(multiplexer_14_out), .en(Enable), .Q(Interrupt_out), .clk(CLK));  // open: clr
  Multiplexer #(.select(1), .width(1), .disabled("Z"), .enable("false")) multiplexer_15 (
    .in0(BEQ_in), .in1(1'b0), .out(multiplexer_15_out), .sel(Reset));
  Multiplexer #(.select(1), .width(1), .disabled("Z"), .enable("false")) multiplexer_16 (
    .in0(BNE_in), .in1(1'b0), .out(multiplexer_16_out), .sel(Reset));
  Multiplexer #(.select(1), .width(1), .disabled("Z"), .enable("false")) multiplexer_17 (
    .in0(MemToReg_in), .in1(1'b0), .out(multiplexer_17_out), .sel(Reset));
  Multiplexer #(.select(1), .width(1), .disabled("Z"), .enable("false")) multiplexer_18 (
    .in0(MemWrite_in), .in1(1'b0), .out(multiplexer_18_out), .sel(Reset));
  Multiplexer #(.select(1), .width(1), .disabled("Z"), .enable("false")) multiplexer_19 (
    .in0(AluSrcB_in), .in1(1'b0), .out(multiplexer_19_out), .sel(Reset));
  Multiplexer #(.select(1), .width(1), .disabled("Z"), .enable("false")) multiplexer_20 (
    .in0(RegWrite_in), .in1(1'b0), .out(multiplexer_20_out), .sel(Reset));
  Multiplexer #(.select(1), .width(1), .disabled("Z"), .enable("false")) multiplexer_21 (
    .in0(JAL_in), .in1(1'b0), .out(multiplexer_21_out), .sel(Reset));
  Multiplexer #(.select(1), .width(1), .disabled("Z"), .enable("false")) multiplexer_22 (
    .in0(RegDst_in), .in1(1'b0), .out(multiplexer_22_out), .sel(Reset));
  Multiplexer #(.select(1), .width(1), .disabled("Z"), .enable("false")) multiplexer_23 (
    .in0(Syscall_in), .in1(1'b0), .out(multiplexer_23_out), .sel(Reset));
  Multiplexer #(.select(1), .width(1), .disabled("Z"), .enable("false")) multiplexer_24 (
    .in0(JMP_in), .in1(1'b0), .out(multiplexer_24_out), .sel(Reset));
  Multiplexer #(.select(1), .width(1), .disabled("Z"), .enable("false")) multiplexer_25 (
    .in0(JR_in), .in1(1'b0), .out(multiplexer_25_out), .sel(Reset));
  Multiplexer #(.select(1), .width(32), .disabled("Z"), .enable("false")) multiplexer_26 (
    .in0(PCr_in), .in1({32{1'b0}}), .out(multiplexer_26_out), .sel(Reset));
  Multiplexer #(.select(1), .width(32), .disabled("Z"), .enable("false")) multiplexer_27 (
    .in0(PCG_in), .in1({32{1'b0}}), .out(multiplexer_27_out), .sel(Reset));
  Register #(.width(1), .trigger("rising"), .Select("low")) register_15 (
    .D(multiplexer_15_out), .en(Enable), .Q(BEQ_out), .clk(CLK));  // open: clr
  Register #(.width(1), .trigger("rising"), .Select("low")) register_16 (
    .D(multiplexer_16_out), .en(Enable), .Q(BNE_out), .clk(CLK));  // open: clr
  Register #(.width(1), .trigger("rising"), .Select("low")) register_17 (
    .D(multiplexer_17_out), .en(Enable), .Q(MemToReg_out), .clk(CLK));  // open: clr
  Register #(.width(1), .trigger("rising"), .Select("low")) register_18 (
    .D(multiplexer_18_out), .en(Enable), .Q(MemWrite_out), .clk(CLK));  // open: clr
  Register #(.width(1), .trigger("rising"), .Select("low")) register_19 (
    .D(multiplexer_19_out), .en(Enable), .Q(AluSrcB_out), .clk(CLK));  // open: clr
  Register #(.width(1), .trigger("rising"), .Select("low")) register_20 (
    .D(multiplexer_20_out), .en(Enable), .Q(RegWrite_out), .clk(CLK));  // open: clr
  Register #(.width(1), .trigger("rising"), .Select("low")) register_21 (
    .D(multiplexer_21_out), .en(Enable), .Q(JAL_out), .clk(CLK));  // open: clr
  Register #(.width(1), .trigger("rising"), .Select("low")) register_22 (
    .D(multiplexer_22_out), .en(Enable), .Q(RegDst_out), .clk(CLK));  // open: clr
  Register #(.width(1), .trigger("rising"), .Select("low")) register_23 (
    .D(multiplexer_23_out), .en(Enable), .Q(Syscall_out), .clk(CLK));  // open: clr
  Register #(.width(1), .trigger("rising"), .Select("low")) register_24 (
    .D(multiplexer_24_out), .en(Enable), .Q(JMP_out), .clk(CLK));  // open: clr
  Register #(.width(1), .trigger("rising"), .Select("low")) register_25 (
    .D(multiplexer_25_out), .en(Enable), .Q(JR_out), .clk(CLK));  // open: clr
  Register #(.width(32), .trigger("rising"), .Select("low")) register_26 (
    .D(multiplexer_26_out), .en(Enable), .Q(PCr_out), .clk(CLK));  // open: clr
  Register #(.width(32), .trigger("rising"), .Select("low")) register_27 (
    .D(multiplexer_27_out), .en(Enable), .Q(PCG_out), .clk(CLK));  // open: clr
endmodule

// EX/MEM
module EX_MEM (
  input  MemToReg_in,
  input  [31:0] IR_in,
  input  MemWrite_in,
  input  [31:0] PC_in,
  input  RegWrite_in,
  input  [31:0] R2_in,
  input  JAL_in,
  input  [31:0] AluR_in,
  input  RegDst_in,
  input  Halt_in,
  input  Syscall_in,
  input  LBU_in,
  input  [31:0] PCr_in,
  input  [4:0] W__in,
  input  [2:0] Interrupt_in,
  input  Reset,
  input  Enable,
  input  CLK,
  output MemToReg_out,
  output [31:0] IR_out,
  output MemWrite_out,
  output [31:0] PC_out,
  output RegWrite_out,
  output [31:0] R2_out,
  output JAL_out,
  output [31:0] AluR_out,
  output RegDst_out,
  output Halt_out,
  output Syscall_out,
  output LBU_out,
  output [31:0] PCr_out,
  output [4:0] W__out,
  output [2:0] Interrupt_out
);

  wire multiplexer_5_out, multiplexer_6_out, multiplexer_9_out, multiplexer_10_out, multiplexer_11_out,
       multiplexer_12_out, multiplexer_13_out, multiplexer_14_out;
  wire [2:0] multiplexer_8_out;
  wire [4:0] multiplexer_7_out;
  wire [31:0] multiplexer_1_out, multiplexer_2_out, multiplexer_3_out, multiplexer_4_out, multiplexer_15_out;

  Multiplexer #(.select(1), .width(32), .disabled("Z"), .enable("false")) multiplexer_1 (
    .in0(IR_in), .in1({32{1'b0}}), .out(multiplexer_1_out), .sel(Reset));
  Multiplexer #(.select(1), .width(32), .disabled("Z"), .enable("false")) multiplexer_2 (
    .in0(PC_in), .in1({32{1'b0}}), .out(multiplexer_2_out), .sel(Reset));
  Multiplexer #(.select(1), .width(32), .disabled("Z"), .enable("false")) multiplexer_3 (
    .in0(R2_in), .in1({32{1'b0}}), .out(multiplexer_3_out), .sel(Reset));
  Multiplexer #(.select(1), .width(32), .disabled("Z"), .enable("false")) multiplexer_4 (
    .in0(AluR_in), .in1({32{1'b0}}), .out(multiplexer_4_out), .sel(Reset));
  Multiplexer #(.select(1), .width(1), .disabled("Z"), .enable("false")) multiplexer_5 (
    .in0(Halt_in), .in1(1'b0), .out(multiplexer_5_out), .sel(Reset));
  Multiplexer #(.select(1), .width(1), .disabled("Z"), .enable("false")) multiplexer_6 (
    .in0(LBU_in), .in1(1'b0), .out(multiplexer_6_out), .sel(Reset));
  Multiplexer #(.select(1), .width(5), .disabled("Z"), .enable("false")) multiplexer_7 (
    .in0(W__in), .in1({5{1'b0}}), .out(multiplexer_7_out), .sel(Reset));
  Multiplexer #(.select(1), .width(3), .disabled("Z"), .enable("false")) multiplexer_8 (
    .in0(Interrupt_in), .in1(3'b000), .out(multiplexer_8_out), .sel(Reset));
  Register #(.width(32), .trigger("rising"), .Select("low")) register_1 (
    .D(multiplexer_1_out), .en(Enable), .Q(IR_out), .clk(CLK));  // open: clr
  Register #(.width(32), .trigger("rising"), .Select("low")) register_2 (
    .D(multiplexer_2_out), .en(Enable), .Q(PC_out), .clk(CLK));  // open: clr
  Register #(.width(32), .trigger("rising"), .Select("low")) register_3 (
    .D(multiplexer_3_out), .en(Enable), .Q(R2_out), .clk(CLK));  // open: clr
  Register #(.width(32), .trigger("rising"), .Select("low")) register_4 (
    .D(multiplexer_4_out), .en(Enable), .Q(AluR_out), .clk(CLK));  // open: clr
  Register #(.width(1), .trigger("rising"), .Select("low")) register_5 (
    .D(multiplexer_5_out), .en(Enable), .Q(Halt_out), .clk(CLK));  // open: clr
  Register #(.width(1), .trigger("rising"), .Select("low")) register_6 (
    .D(multiplexer_6_out), .en(Enable), .Q(LBU_out), .clk(CLK));  // open: clr
  Register #(.width(5), .trigger("rising"), .Select("low")) register_7 (
    .D(multiplexer_7_out), .en(Enable), .Q(W__out), .clk(CLK));  // open: clr
  Register #(.width(3), .trigger("rising"), .Select("low")) register_8 (
    .D(multiplexer_8_out), .en(Enable), .Q(Interrupt_out), .clk(CLK));  // open: clr
  Multiplexer #(.select(1), .width(1), .disabled("Z"), .enable("false")) multiplexer_9 (
    .in0(MemToReg_in), .in1(1'b0), .out(multiplexer_9_out), .sel(Reset));
  Multiplexer #(.select(1), .width(1), .disabled("Z"), .enable("false")) multiplexer_10 (
    .in0(MemWrite_in), .in1(1'b0), .out(multiplexer_10_out), .sel(Reset));
  Multiplexer #(.select(1), .width(1), .disabled("Z"), .enable("false")) multiplexer_11 (
    .in0(RegWrite_in), .in1(1'b0), .out(multiplexer_11_out), .sel(Reset));
  Multiplexer #(.select(1), .width(1), .disabled("Z"), .enable("false")) multiplexer_12 (
    .in0(JAL_in), .in1(1'b0), .out(multiplexer_12_out), .sel(Reset));
  Multiplexer #(.select(1), .width(1), .disabled("Z"), .enable("false")) multiplexer_13 (
    .in0(RegDst_in), .in1(1'b0), .out(multiplexer_13_out), .sel(Reset));
  Multiplexer #(.select(1), .width(1), .disabled("Z"), .enable("false")) multiplexer_14 (
    .in0(Syscall_in), .in1(1'b0), .out(multiplexer_14_out), .sel(Reset));
  Multiplexer #(.select(1), .width(32), .disabled("Z"), .enable("false")) multiplexer_15 (
    .in0(PCr_in), .in1({32{1'b0}}), .out(multiplexer_15_out), .sel(Reset));
  Register #(.width(1), .trigger("rising"), .Select("low")) register_9 (
    .D(multiplexer_9_out), .en(Enable), .Q(MemToReg_out), .clk(CLK));  // open: clr
  Register #(.width(1), .trigger("rising"), .Select("low")) register_10 (
    .D(multiplexer_10_out), .en(Enable), .Q(MemWrite_out), .clk(CLK));  // open: clr
  Register #(.width(1), .trigger("rising"), .Select("low")) register_11 (
    .D(multiplexer_11_out), .en(Enable), .Q(RegWrite_out), .clk(CLK));  // open: clr
  Register #(.width(1), .trigger("rising"), .Select("low")) register_12 (
    .D(multiplexer_12_out), .en(Enable), .Q(JAL_out), .clk(CLK));  // open: clr
  Register #(.width(1), .trigger("rising"), .Select("low")) register_13 (
    .D(multiplexer_13_out), .en(Enable), .Q(RegDst_out), .clk(CLK));  // open: clr
  Register #(.width(1), .trigger("rising"), .Select("low")) register_14 (
    .D(multiplexer_14_out), .en(Enable), .Q(Syscall_out), .clk(CLK));  // open: clr
  Register #(.width(32), .trigger("rising"), .Select("low")) register_15 (
    .D(multiplexer_15_out), .en(Enable), .Q(PCr_out), .clk(CLK));  // open: clr
endmodule

// MEM/WB
module MEM_WB (
  input  MemToReg_in,
  input  [31:0] IR_in,
  input  RegWrite_in,
  input  [31:0] PC_in,
  input  JAL_in,
  input  [31:0] MemD_in,
  input  RegDst_in,
  input  [31:0] AluR_in,
  input  Syscall_in,
  input  Halt_in,
  input  [4:0] W__in,
  input  [31:0] PCr_in,
  input  [2:0] Interrupt_in,
  input  [31:0] R2_in,
  input  Reset,
  input  Enable,
  input  CLK,
  output MemToReg_out,
  output [31:0] IR_out,
  output RegWrite_out,
  output [31:0] PC_out,
  output JAL_out,
  output [31:0] MemD_out,
  output RegDst_out,
  output [31:0] AluR_out,
  output Syscall_out,
  output Halt_out,
  output [4:0] W__out,
  output [31:0] PCr_out,
  output [2:0] Interrupt_out,
  output [31:0] R2_out
);

  wire multiplexer_5_out, multiplexer_8_out, multiplexer_9_out, multiplexer_10_out, multiplexer_11_out,
       multiplexer_12_out;
  wire [2:0] multiplexer_7_out;
  wire [4:0] multiplexer_6_out;
  wire [31:0] multiplexer_1_out, multiplexer_2_out, multiplexer_3_out, multiplexer_4_out, multiplexer_13_out,
       multiplexer_14_out;

  Multiplexer #(.select(1), .width(32), .disabled("Z"), .enable("false")) multiplexer_1 (
    .in0(IR_in), .in1({32{1'b0}}), .out(multiplexer_1_out), .sel(Reset));
  Multiplexer #(.select(1), .width(32), .disabled("Z"), .enable("false")) multiplexer_2 (
    .in0(PC_in), .in1({32{1'b0}}), .out(multiplexer_2_out), .sel(Reset));
  Multiplexer #(.select(1), .width(32), .disabled("Z"), .enable("false")) multiplexer_3 (
    .in0(MemD_in), .in1({32{1'b0}}), .out(multiplexer_3_out), .sel(Reset));
  Multiplexer #(.select(1), .width(32), .disabled("Z"), .enable("false")) multiplexer_4 (
    .in0(AluR_in), .in1({32{1'b0}}), .out(multiplexer_4_out), .sel(Reset));
  Multiplexer #(.select(1), .width(1), .disabled("Z"), .enable("false")) multiplexer_5 (
    .in0(Halt_in), .in1(1'b0), .out(multiplexer_5_out), .sel(Reset));
  Multiplexer #(.select(1), .width(5), .disabled("Z"), .enable("false")) multiplexer_6 (
    .in0(W__in), .in1({5{1'b0}}), .out(multiplexer_6_out), .sel(Reset));
  Multiplexer #(.select(1), .width(3), .disabled("Z"), .enable("false")) multiplexer_7 (
    .in0(Interrupt_in), .in1(3'b000), .out(multiplexer_7_out), .sel(Reset));
  Register #(.width(32), .trigger("rising"), .Select("low")) register_1 (
    .D(multiplexer_1_out), .en(Enable), .Q(IR_out), .clk(CLK));  // open: clr
  Register #(.width(32), .trigger("rising"), .Select("low")) register_2 (
    .D(multiplexer_2_out), .en(Enable), .Q(PC_out), .clk(CLK));  // open: clr
  Register #(.width(32), .trigger("rising"), .Select("low")) register_3 (
    .D(multiplexer_3_out), .en(Enable), .Q(MemD_out), .clk(CLK));  // open: clr
  Register #(.width(32), .trigger("rising"), .Select("low")) register_4 (
    .D(multiplexer_4_out), .en(Enable), .Q(AluR_out), .clk(CLK));  // open: clr
  Register #(.width(1), .trigger("rising"), .Select("low")) register_5 (
    .D(multiplexer_5_out), .en(Enable), .Q(Halt_out), .clk(CLK));  // open: clr
  Register #(.width(5), .trigger("rising"), .Select("low")) register_6 (
    .D(multiplexer_6_out), .en(Enable), .Q(W__out), .clk(CLK));  // open: clr
  Register #(.width(3), .trigger("rising"), .Select("low")) register_7 (
    .D(multiplexer_7_out), .en(Enable), .Q(Interrupt_out), .clk(CLK));  // open: clr
  Multiplexer #(.select(1), .width(1), .disabled("Z"), .enable("false")) multiplexer_8 (
    .in0(MemToReg_in), .in1(1'b0), .out(multiplexer_8_out), .sel(Reset));
  Multiplexer #(.select(1), .width(1), .disabled("Z"), .enable("false")) multiplexer_9 (
    .in0(RegWrite_in), .in1(1'b0), .out(multiplexer_9_out), .sel(Reset));
  Multiplexer #(.select(1), .width(1), .disabled("Z"), .enable("false")) multiplexer_10 (
    .in0(JAL_in), .in1(1'b0), .out(multiplexer_10_out), .sel(Reset));
  Multiplexer #(.select(1), .width(1), .disabled("Z"), .enable("false")) multiplexer_11 (
    .in0(RegDst_in), .in1(1'b0), .out(multiplexer_11_out), .sel(Reset));
  Multiplexer #(.select(1), .width(1), .disabled("Z"), .enable("false")) multiplexer_12 (
    .in0(Syscall_in), .in1(1'b0), .out(multiplexer_12_out), .sel(Reset));
  Multiplexer #(.select(1), .width(32), .disabled("Z"), .enable("false")) multiplexer_13 (
    .in0(PCr_in), .in1({32{1'b0}}), .out(multiplexer_13_out), .sel(Reset));
  Multiplexer #(.select(1), .width(32), .disabled("Z"), .enable("false")) multiplexer_14 (
    .in0(R2_in), .in1({32{1'b0}}), .out(multiplexer_14_out), .sel(Reset));
  Register #(.width(1), .trigger("rising"), .Select("low")) register_8 (
    .D(multiplexer_8_out), .en(Enable), .Q(MemToReg_out), .clk(CLK));  // open: clr
  Register #(.width(1), .trigger("rising"), .Select("low")) register_9 (
    .D(multiplexer_9_out), .en(Enable), .Q(RegWrite_out), .clk(CLK));  // open: clr
  Register #(.width(1), .trigger("rising"), .Select("low")) register_10 (
    .D(multiplexer_10_out), .en(Enable), .Q(JAL_out), .clk(CLK));  // open: clr
  Register #(.width(1), .trigger("rising"), .Select("low")) register_11 (
    .D(multiplexer_11_out), .en(Enable), .Q(RegDst_out), .clk(CLK));  // open: clr
  Register #(.width(1), .trigger("rising"), .Select("low")) register_12 (
    .D(multiplexer_12_out), .en(Enable), .Q(Syscall_out), .clk(CLK));  // open: clr
  Register #(.width(32), .trigger("rising"), .Select("low")) register_13 (
    .D(multiplexer_13_out), .en(Enable), .Q(PCr_out), .clk(CLK));  // open: clr
  Register #(.width(32), .trigger("rising"), .Select("low")) register_14 (
    .D(multiplexer_14_out), .en(Enable), .Q(R2_out), .clk(CLK));  // open: clr
endmodule
module \源寄存器使用情况  (
  input  OP0,
  input  OP1,
  input  OP2,
  input  OP3,
  input  OP4,
  input  OP5,
  input  F0,
  input  F1,
  input  F2,
  input  F3,
  input  F4,
  input  F5,
  output R1_Used,
  output R2_Used
);

  wire and_1_out, and_2_out, and_3_out, and_4_out, and_5_out, and_6_out, and_7_out, and_8_out, and_9_out,
       and_10_out, and_11_out, and_12_out, and_13_out, and_14_out, and_15_out, and_16_out, and_17_out,
       and_18_out, and_19_out, and_20_out, and_21_out, and_22_out, and_23_out, and_24_out, and_25_out,
       and_26_out, and_27_out, and_28_out, and_29_out, and_30_out, and_31_out, and_32_out, and_33_out,
       and_34_out, and_35_out, and_36_out, and_37_out, and_38_out, and_39_out, and_40_out, not_1_out,
       not_2_out, not_3_out, not_4_out, not_5_out, not_6_out, not_7_out, not_8_out, not_9_out, not_10_out,
       not_11_out, not_12_out, not_13_out, not_14_out, not_15_out, not_16_out, not_17_out, not_18_out,
       not_19_out, not_20_out, not_21_out, not_22_out, not_23_out, not_24_out, not_25_out, not_26_out,
       not_27_out, not_28_out, not_29_out, not_30_out, not_31_out, not_32_out, not_33_out, not_34_out,
       not_35_out, not_36_out, not_37_out, not_38_out, not_39_out, not_40_out, not_41_out, not_42_out,
       not_43_out, not_44_out, not_45_out, not_46_out, not_47_out, not_48_out, not_49_out, not_50_out,
       not_51_out, not_52_out, not_53_out, not_54_out, not_55_out, not_56_out, not_57_out, not_58_out,
       not_59_out, not_60_out, not_61_out, not_62_out, not_63_out, not_64_out, not_65_out, not_66_out,
       not_67_out, not_68_out, not_69_out, not_70_out, not_71_out, not_72_out, not_73_out, not_74_out,
       not_75_out, not_76_out, not_77_out, not_78_out, not_79_out, not_80_out, not_81_out, not_82_out,
       not_83_out, not_84_out, not_85_out, not_86_out, not_87_out, not_88_out, not_89_out, not_90_out,
       not_91_out, not_92_out, not_93_out, not_94_out, not_95_out, not_96_out, not_97_out, not_98_out,
       not_99_out, not_100_out, not_101_out, not_102_out, not_103_out, not_104_out, not_105_out, not_106_out,
       not_107_out, not_108_out, not_109_out, not_110_out, not_111_out, not_112_out, not_113_out,
       not_114_out, not_115_out, not_116_out, not_117_out, not_118_out, not_119_out, not_120_out,
       not_121_out, not_122_out, not_123_out, not_124_out, not_125_out, not_126_out, not_127_out,
       not_128_out, not_129_out, not_130_out, not_131_out, not_132_out, not_133_out, not_134_out,
       not_135_out, not_136_out, not_137_out, not_138_out, not_139_out, not_140_out, not_141_out,
       not_142_out, not_143_out, not_144_out, not_145_out, not_146_out, not_147_out, not_148_out,
       not_149_out, not_150_out, not_151_out, not_152_out, not_153_out, not_154_out, not_155_out,
       not_156_out, not_157_out, not_158_out, not_159_out, not_160_out, not_161_out, not_162_out,
       not_163_out, not_164_out, not_165_out, not_166_out, not_167_out, not_168_out, not_169_out,
       not_170_out, not_171_out, not_172_out, not_173_out, not_174_out, not_175_out, not_176_out,
       not_177_out, not_178_out, not_179_out, not_180_out, not_181_out, not_182_out, not_183_out,
       not_184_out, not_185_out, not_186_out, not_187_out, not_188_out, not_189_out, not_190_out,
       not_191_out, not_192_out, not_193_out, not_194_out, not_195_out, not_196_out, not_197_out,
       not_198_out, not_199_out, not_200_out, not_201_out, not_202_out, not_203_out, not_204_out,
       not_205_out, not_206_out, not_207_out, not_208_out, not_209_out, not_210_out, not_211_out,
       not_212_out, not_213_out, not_214_out, not_215_out, not_216_out, not_217_out, not_218_out,
       not_219_out, not_220_out, not_221_out, not_222_out, not_223_out, not_224_out, not_225_out,
       not_226_out, not_227_out, not_228_out, not_229_out, not_230_out, not_231_out, not_232_out,
       not_233_out, not_234_out, not_235_out, not_236_out, not_237_out, not_238_out, not_239_out,
       not_240_out, not_241_out, not_242_out, not_243_out, not_244_out, not_245_out, not_246_out,
       not_247_out, not_248_out, not_249_out, not_250_out, not_251_out, not_252_out, not_253_out,
       not_254_out, not_255_out, not_256_out, not_257_out, not_258_out, not_259_out, not_260_out,
       not_261_out, not_262_out, not_263_out, not_264_out, not_265_out, not_266_out, not_267_out,
       not_268_out, not_269_out, not_270_out, not_271_out, not_272_out, not_273_out, not_274_out,
       not_275_out, not_276_out, not_277_out, not_278_out, not_279_out, not_280_out, not_281_out,
       not_282_out, not_283_out, not_284_out, not_285_out, not_286_out, not_287_out, not_288_out,
       not_289_out, not_290_out, not_291_out, not_292_out, not_293_out, not_294_out, not_295_out,
       not_296_out, not_297_out, not_298_out, not_299_out, not_300_out, not_301_out, not_302_out,
       not_303_out, not_304_out;

  not not_1 (not_1_out, OP5);
  not not_2 (not_2_out, OP4);
  not not_3 (not_3_out, OP3);
  not not_4 (not_4_out, OP2);
  not not_5 (not_5_out, OP1);
  not not_6 (not_6_out, OP0);
  not not_7 (not_7_out, F4);
  not not_8 (not_8_out, F3);
  not not_9 (not_9_out, F2);
  not not_10 (not_10_out, F1);
  not not_11 (not_11_out, F0);
  not not_12 (not_12_out, OP5);
  not not_13 (not_13_out, OP4);
  not not_14 (not_14_out, OP3);
  not not_15 (not_15_out, OP2);
  not not_16 (not_16_out, OP1);
  not not_17 (not_17_out, OP0);
  not not_18 (not_18_out, F4);
  not not_19 (not_19_out, F3);
  not not_20 (not_20_out, F2);
  not not_21 (not_21_out, F1);
  not not_22 (not_22_out, OP5);
  not not_23 (not_23_out, OP4);
  not not_24 (not_24_out, OP3);
  not not_25 (not_25_out, OP2);
  not not_26 (not_26_out, OP1);
  not not_27 (not_27_out, OP0);
  not not_28 (not_28_out, F4);
  not not_29 (not_29_out, F3);
  not not_30 (not_30_out, F2);
  not not_31 (not_31_out, F0);
  not not_32 (not_32_out, OP5);
  not not_33 (not_33_out, OP4);
  not not_34 (not_34_out, OP3);
  not not_35 (not_35_out, OP2);
  not not_36 (not_36_out, OP1);
  not not_37 (not_37_out, OP0);
  not not_38 (not_38_out, F4);
  not not_39 (not_39_out, F3);
  not not_40 (not_40_out, F1);
  not not_41 (not_41_out, F0);
  not not_42 (not_42_out, OP5);
  not not_43 (not_43_out, OP4);
  not not_44 (not_44_out, OP3);
  not not_45 (not_45_out, OP2);
  not not_46 (not_46_out, OP1);
  not not_47 (not_47_out, OP0);
  not not_48 (not_48_out, F4);
  not not_49 (not_49_out, F3);
  not not_50 (not_50_out, F1);
  not not_51 (not_51_out, OP5);
  not not_52 (not_52_out, OP4);
  not not_53 (not_53_out, OP3);
  not not_54 (not_54_out, OP2);
  not not_55 (not_55_out, OP1);
  not not_56 (not_56_out, OP0);
  not not_57 (not_57_out, F4);
  not not_58 (not_58_out, F3);
  not not_59 (not_59_out, OP5);
  not not_60 (not_60_out, OP4);
  not not_61 (not_61_out, OP3);
  not not_62 (not_62_out, OP2);
  not not_63 (not_63_out, OP1);
  not not_64 (not_64_out, OP0);
  not not_65 (not_65_out, F4);
  not not_66 (not_66_out, F2);
  not not_67 (not_67_out, F0);
  not not_68 (not_68_out, OP5);
  not not_69 (not_69_out, OP4);
  not not_70 (not_70_out, OP3);
  not not_71 (not_71_out, OP2);
  not not_72 (not_72_out, OP1);
  not not_73 (not_73_out, OP0);
  not not_74 (not_74_out, F4);
  not not_75 (not_75_out, F2);
  not not_76 (not_76_out, OP5);
  not not_77 (not_77_out, OP4);
  not not_78 (not_78_out, OP3);
  not not_79 (not_79_out, OP2);
  not not_80 (not_80_out, OP1);
  not not_81 (not_81_out, OP0);
  not not_82 (not_82_out, F5);
  not not_83 (not_83_out, F4);
  not not_84 (not_84_out, F2);
  not not_85 (not_85_out, F1);
  not not_86 (not_86_out, F0);
  not not_87 (not_87_out, OP5);
  not not_88 (not_88_out, OP4);
  not not_89 (not_89_out, OP3);
  not not_90 (not_90_out, OP2);
  not not_91 (not_91_out, OP1);
  not not_92 (not_92_out, OP0);
  not not_93 (not_93_out, F5);
  not not_94 (not_94_out, F4);
  not not_95 (not_95_out, F1);
  not not_96 (not_96_out, F0);
  not not_97 (not_97_out, OP5);
  not not_98 (not_98_out, OP4);
  not not_99 (not_99_out, OP3);
  not not_100 (not_100_out, OP1);
  not not_101 (not_101_out, OP0);
  not not_102 (not_102_out, OP5);
  not not_103 (not_103_out, OP4);
  not not_104 (not_104_out, OP3);
  not not_105 (not_105_out, OP1);
  not not_106 (not_106_out, OP5);
  not not_107 (not_107_out, OP4);
  not not_108 (not_108_out, OP2);
  not not_109 (not_109_out, OP1);
  not not_110 (not_110_out, OP0);
  not not_111 (not_111_out, OP5);
  not not_112 (not_112_out, OP4);
  not not_113 (not_113_out, OP1);
  not not_114 (not_114_out, OP0);
  not not_115 (not_115_out, OP5);
  not not_116 (not_116_out, OP4);
  not not_117 (not_117_out, OP2);
  not not_118 (not_118_out, OP1);
  not not_119 (not_119_out, OP5);
  not not_120 (not_120_out, OP4);
  not not_121 (not_121_out, OP2);
  not not_122 (not_122_out, OP0);
  not not_123 (not_123_out, OP5);
  not not_124 (not_124_out, OP4);
  not not_125 (not_125_out, OP1);
  not not_126 (not_126_out, OP4);
  not not_127 (not_127_out, OP3);
  not not_128 (not_128_out, OP2);
  not not_129 (not_129_out, OP4);
  not not_130 (not_130_out, OP2);
  not not_131 (not_131_out, OP5);
  not not_132 (not_132_out, OP4);
  not not_133 (not_133_out, OP3);
  not not_134 (not_134_out, OP2);
  not not_135 (not_135_out, OP1);
  not not_136 (not_136_out, OP0);
  not not_137 (not_137_out, F4);
  not not_138 (not_138_out, F3);
  not not_139 (not_139_out, F2);
  not not_140 (not_140_out, OP5);
  not not_141 (not_141_out, OP4);
  not not_142 (not_142_out, OP3);
  not not_143 (not_143_out, OP2);
  not not_144 (not_144_out, OP1);
  not not_145 (not_145_out, OP0);
  not not_146 (not_146_out, F4);
  not not_147 (not_147_out, F3);
  not not_148 (not_148_out, F0);
  not not_149 (not_149_out, OP4);
  not not_150 (not_150_out, OP3);
  not not_151 (not_151_out, OP1);
  not not_152 (not_152_out, OP0);
  not not_153 (not_153_out, OP5);
  not not_154 (not_154_out, OP4);
  not not_155 (not_155_out, OP3);
  not not_156 (not_156_out, OP2);
  not not_157 (not_157_out, OP1);
  not not_158 (not_158_out, OP5);
  not not_159 (not_159_out, OP4);
  not not_160 (not_160_out, OP3);
  not not_161 (not_161_out, OP2);
  not not_162 (not_162_out, OP1);
  not not_163 (not_163_out, OP0);
  not not_164 (not_164_out, F5);
  not not_165 (not_165_out, F4);
  not not_166 (not_166_out, F3);
  not not_167 (not_167_out, F2);
  not not_168 (not_168_out, F1);
  not not_169 (not_169_out, F0);
  not not_170 (not_170_out, OP5);
  not not_171 (not_171_out, OP4);
  not not_172 (not_172_out, OP3);
  not not_173 (not_173_out, OP2);
  not not_174 (not_174_out, OP1);
  not not_175 (not_175_out, OP0);
  not not_176 (not_176_out, F5);
  not not_177 (not_177_out, F4);
  not not_178 (not_178_out, F3);
  not not_179 (not_179_out, F2);
  not not_180 (not_180_out, OP5);
  not not_181 (not_181_out, OP4);
  not not_182 (not_182_out, OP3);
  not not_183 (not_183_out, OP2);
  not not_184 (not_184_out, OP1);
  not not_185 (not_185_out, OP0);
  not not_186 (not_186_out, F5);
  not not_187 (not_187_out, F4);
  not not_188 (not_188_out, F3);
  not not_189 (not_189_out, F2);
  not not_190 (not_190_out, F0);
  not not_191 (not_191_out, OP5);
  not not_192 (not_192_out, OP4);
  not not_193 (not_193_out, OP3);
  not not_194 (not_194_out, OP2);
  not not_195 (not_195_out, OP1);
  not not_196 (not_196_out, OP0);
  not not_197 (not_197_out, F4);
  not not_198 (not_198_out, F3);
  not not_199 (not_199_out, F2);
  not not_200 (not_200_out, F1);
  not not_201 (not_201_out, F0);
  not not_202 (not_202_out, OP5);
  not not_203 (not_203_out, OP4);
  not not_204 (not_204_out, OP3);
  not not_205 (not_205_out, OP2);
  not not_206 (not_206_out, OP1);
  not not_207 (not_207_out, OP0);
  not not_208 (not_208_out, F4);
  not not_209 (not_209_out, F3);
  not not_210 (not_210_out, F2);
  not not_211 (not_211_out, F1);
  not not_212 (not_212_out, OP5);
  not not_213 (not_213_out, OP4);
  not not_214 (not_214_out, OP3);
  not not_215 (not_215_out, OP2);
  not not_216 (not_216_out, OP1);
  not not_217 (not_217_out, OP0);
  not not_218 (not_218_out, F4);
  not not_219 (not_219_out, F3);
  not not_220 (not_220_out, F2);
  not not_221 (not_221_out, F0);
  not not_222 (not_222_out, OP5);
  not not_223 (not_223_out, OP4);
  not not_224 (not_224_out, OP3);
  not not_225 (not_225_out, OP2);
  not not_226 (not_226_out, OP1);
  not not_227 (not_227_out, OP0);
  not not_228 (not_228_out, F4);
  not not_229 (not_229_out, F3);
  not not_230 (not_230_out, F1);
  not not_231 (not_231_out, F0);
  not not_232 (not_232_out, OP5);
  not not_233 (not_233_out, OP4);
  not not_234 (not_234_out, OP3);
  not not_235 (not_235_out, OP2);
  not not_236 (not_236_out, OP1);
  not not_237 (not_237_out, OP0);
  not not_238 (not_238_out, F4);
  not not_239 (not_239_out, F3);
  not not_240 (not_240_out, F1);
  not not_241 (not_241_out, OP5);
  not not_242 (not_242_out, OP4);
  not not_243 (not_243_out, OP3);
  not not_244 (not_244_out, OP2);
  not not_245 (not_245_out, OP1);
  not not_246 (not_246_out, OP0);
  not not_247 (not_247_out, F4);
  not not_248 (not_248_out, F3);
  not not_249 (not_249_out, OP5);
  not not_250 (not_250_out, OP4);
  not not_251 (not_251_out, OP3);
  not not_252 (not_252_out, OP2);
  not not_253 (not_253_out, OP1);
  not not_254 (not_254_out, OP0);
  not not_255 (not_255_out, F4);
  not not_256 (not_256_out, F2);
  not not_257 (not_257_out, F0);
  not not_258 (not_258_out, OP5);
  not not_259 (not_259_out, OP4);
  not not_260 (not_260_out, OP3);
  not not_261 (not_261_out, OP2);
  not not_262 (not_262_out, OP1);
  not not_263 (not_263_out, OP0);
  not not_264 (not_264_out, F4);
  not not_265 (not_265_out, F2);
  not not_266 (not_266_out, OP5);
  not not_267 (not_267_out, OP4);
  not not_268 (not_268_out, OP3);
  not not_269 (not_269_out, OP2);
  not not_270 (not_270_out, OP1);
  not not_271 (not_271_out, OP0);
  not not_272 (not_272_out, F5);
  not not_273 (not_273_out, F4);
  not not_274 (not_274_out, F1);
  not not_275 (not_275_out, F0);
  not not_276 (not_276_out, OP5);
  not not_277 (not_277_out, OP4);
  not not_278 (not_278_out, OP3);
  not not_279 (not_279_out, OP1);
  not not_280 (not_280_out, OP0);
  not not_281 (not_281_out, OP5);
  not not_282 (not_282_out, OP4);
  not not_283 (not_283_out, OP3);
  not not_284 (not_284_out, OP1);
  not not_285 (not_285_out, OP4);
  not not_286 (not_286_out, OP2);
  not not_287 (not_287_out, OP5);
  not not_288 (not_288_out, OP4);
  not not_289 (not_289_out, OP3);
  not not_290 (not_290_out, OP2);
  not not_291 (not_291_out, OP1);
  not not_292 (not_292_out, OP0);
  not not_293 (not_293_out, F4);
  not not_294 (not_294_out, F3);
  not not_295 (not_295_out, F2);
  not not_296 (not_296_out, OP5);
  not not_297 (not_297_out, OP4);
  not not_298 (not_298_out, OP3);
  not not_299 (not_299_out, OP2);
  not not_300 (not_300_out, OP1);
  not not_301 (not_301_out, OP0);
  not not_302 (not_302_out, F4);
  not not_303 (not_303_out, F3);
  not not_304 (not_304_out, F0);
  and and_1 (and_1_out, not_1_out, not_2_out, not_3_out, not_4_out, not_5_out, not_6_out, F5, not_7_out, not_8_out, not_9_out, not_10_out, not_11_out);
  and and_2 (and_2_out, not_12_out, not_13_out, not_14_out, not_15_out, not_16_out, not_17_out, F5, not_18_out, not_19_out, not_20_out, not_21_out, F0);
  and and_3 (and_3_out, not_22_out, not_23_out, not_24_out, not_25_out, not_26_out, not_27_out, F5, not_28_out, not_29_out, not_30_out, F1, not_31_out);
  and and_4 (and_4_out, not_32_out, not_33_out, not_34_out, not_35_out, not_36_out, not_37_out, F5, not_38_out, not_39_out, F2, not_40_out, not_41_out);
  and and_5 (and_5_out, not_42_out, not_43_out, not_44_out, not_45_out, not_46_out, not_47_out, F5, not_48_out, not_49_out, F2, not_50_out, F0);
  and and_6 (and_6_out, not_51_out, not_52_out, not_53_out, not_54_out, not_55_out, not_56_out, F5, not_57_out, not_58_out, F2, F1, F0);
  and and_7 (and_7_out, not_59_out, not_60_out, not_61_out, not_62_out, not_63_out, not_64_out, F5, not_65_out, F3, not_66_out, F1, not_67_out);
  and and_8 (and_8_out, not_68_out, not_69_out, not_70_out, not_71_out, not_72_out, not_73_out, F5, not_74_out, F3, not_75_out, F1, F0);
  and and_9 (and_9_out, not_76_out, not_77_out, not_78_out, not_79_out, not_80_out, not_81_out, not_82_out, not_83_out, F3, not_84_out, not_85_out, not_86_out);
  and and_10 (and_10_out, not_87_out, not_88_out, not_89_out, not_90_out, not_91_out, not_92_out, not_93_out, not_94_out, F3, F2, not_95_out, not_96_out);
  and and_11 (and_11_out, not_97_out, not_98_out, not_99_out, OP2, not_100_out, not_101_out);
  and and_12 (and_12_out, not_102_out, not_103_out, not_104_out, OP2, not_105_out, OP0);
  and and_13 (and_13_out, not_106_out, not_107_out, OP3, not_108_out, not_109_out, not_110_out);
  and and_14 (and_14_out, not_111_out, not_112_out, OP3, OP2, not_113_out, not_114_out);
  and and_15 (and_15_out, not_115_out, not_116_out, OP3, not_117_out, not_118_out, OP0);
  and and_16 (and_16_out, not_119_out, not_120_out, OP3, not_121_out, OP1, not_122_out);
  and and_17 (and_17_out, not_123_out, not_124_out, OP3, OP2, not_125_out, OP0);
  and and_18 (and_18_out, OP5, not_126_out, not_127_out, not_128_out, OP1, OP0);
  and and_19 (and_19_out, OP5, not_129_out, OP3, not_130_out, OP1, OP0);
  and and_20 (and_20_out, not_131_out, not_132_out, not_133_out, not_134_out, not_135_out, not_136_out, F5, not_137_out, not_138_out, not_139_out, F1, F0);
  and and_21 (and_21_out, not_140_out, not_141_out, not_142_out, not_143_out, not_144_out, not_145_out, F5, not_146_out, not_147_out, F2, F1, not_148_out);
  and and_22 (and_22_out, OP5, not_149_out, not_150_out, OP2, not_151_out, not_152_out);
  and and_23 (and_23_out, not_153_out, not_154_out, not_155_out, not_156_out, not_157_out, OP0);
  and and_24 (and_24_out, not_158_out, not_159_out, not_160_out, not_161_out, not_162_out, not_163_out, not_164_out, not_165_out, not_166_out, not_167_out, not_168_out, not_169_out);
  and and_25 (and_25_out, not_170_out, not_171_out, not_172_out, not_173_out, not_174_out, not_175_out, not_176_out, not_177_out, not_178_out, not_179_out, F1, F0);
  and and_26 (and_26_out, not_180_out, not_181_out, not_182_out, not_183_out, not_184_out, not_185_out, not_186_out, not_187_out, not_188_out, not_189_out, F1, not_190_out);
  and and_27 (and_27_out, not_191_out, not_192_out, not_193_out, not_194_out, not_195_out, not_196_out, F5, not_197_out, not_198_out, not_199_out, not_200_out, not_201_out);
  and and_28 (and_28_out, not_202_out, not_203_out, not_204_out, not_205_out, not_206_out, not_207_out, F5, not_208_out, not_209_out, not_210_out, not_211_out, F0);
  and and_29 (and_29_out, not_212_out, not_213_out, not_214_out, not_215_out, not_216_out, not_217_out, F5, not_218_out, not_219_out, not_220_out, F1, not_221_out);
  and and_30 (and_30_out, not_222_out, not_223_out, not_224_out, not_225_out, not_226_out, not_227_out, F5, not_228_out, not_229_out, F2, not_230_out, not_231_out);
  and and_31 (and_31_out, not_232_out, not_233_out, not_234_out, not_235_out, not_236_out, not_237_out, F5, not_238_out, not_239_out, F2, not_240_out, F0);
  and and_32 (and_32_out, not_241_out, not_242_out, not_243_out, not_244_out, not_245_out, not_246_out, F5, not_247_out, not_248_out, F2, F1, F0);
  and and_33 (and_33_out, not_249_out, not_250_out, not_251_out, not_252_out, not_253_out, not_254_out, F5, not_255_out, F3, not_256_out, F1, not_257_out);
  and and_34 (and_34_out, not_258_out, not_259_out, not_260_out, not_261_out, not_262_out, not_263_out, F5, not_264_out, F3, not_265_out, F1, F0);
  and and_35 (and_35_out, not_266_out, not_267_out, not_268_out, not_269_out, not_270_out, not_271_out, not_272_out, not_273_out, F3, F2, not_274_out, not_275_out);
  and and_36 (and_36_out, not_276_out, not_277_out, not_278_out, OP2, not_279_out, not_280_out);
  and and_37 (and_37_out, not_281_out, not_282_out, not_283_out, OP2, not_284_out, OP0);
  and and_38 (and_38_out, OP5, not_285_out, OP3, not_286_out, OP1, OP0);
  and and_39 (and_39_out, not_287_out, not_288_out, not_289_out, not_290_out, not_291_out, not_292_out, F5, not_293_out, not_294_out, not_295_out, F1, F0);
  and and_40 (and_40_out, not_296_out, not_297_out, not_298_out, not_299_out, not_300_out, not_301_out, F5, not_302_out, not_303_out, F2, F1, not_304_out);
  or or_1 (R1_Used, and_1_out, and_2_out, and_3_out, and_4_out, and_5_out, and_6_out, and_7_out, and_8_out, and_9_out, and_10_out, and_11_out, and_12_out, and_13_out, and_14_out, and_15_out, and_16_out, and_17_out, and_18_out, and_19_out, and_20_out, and_21_out, and_22_out, and_23_out);
  or or_2 (R2_Used, and_24_out, and_25_out, and_26_out, and_27_out, and_28_out, and_29_out, and_30_out, and_31_out, and_32_out, and_33_out, and_34_out, and_35_out, and_36_out, and_37_out, and_38_out, and_39_out, and_40_out);
endmodule

module \数据相关检测  (
  input  [5:0] ID_OP,
  input  [5:0] ID_FUNC,
  input  [4:0] ID_R1_num,
  input  [4:0] ID_R2_num,
  input  [4:0] EX_WriteReg_num,
  input  [4:0] MEM_WriteReg_num,
  input  EX_RegWrite,
  input  MEM_RegWrite,
  input  [5:0] EX_OP,
  input  [5:0] MEM_OP,
  output \数据相关 ,
  output \Load_Use相关 ,
  output [1:0] R1_Forward,
  output [1:0] R2_Forward
);

  wire and_1_out, and_2_out, and_3_out, and_4_out, and_5_out, and_6_out, and_7_out, and_8_out,
       comparator_1_eq, comparator_2_eq, comparator_3_eq, comparator_4_eq, comparator_5_eq, comparator_6_eq,
       comparator_7_eq, comparator_8_eq, comparator_9_eq, comparator_10_eq, comparator_11_eq,
       comparator_12_eq, not_1_out, not_2_out, not_3_out, not_4_out, or_1_out, or_2_out, or_4_out, or_5_out,
       or_6_out, \源寄存器使用情况_1_r1_used , \源寄存器使用情况_1_r2_used ;
  wire [1:0] priority_encoder_1_out, priority_encoder_2_out;

  not not_1 (not_1_out, comparator_1_eq);
  Comparator #(.width(5), .mode("twosComplement")) comparator_1 (
    .a(MEM_WriteReg_num), .b({5{1'b0}}), .eq(comparator_1_eq));  // open: gt, lt
  Comparator #(.width(5), .mode("twosComplement")) comparator_2 (
    .a(MEM_WriteReg_num), .b(ID_R1_num), .eq(comparator_2_eq));  // open: gt, lt
  Comparator #(.width(5), .mode("twosComplement")) comparator_3 (
    .a(ID_R1_num), .b(EX_WriteReg_num), .eq(comparator_3_eq));  // open: gt, lt
  not not_2 (not_2_out, comparator_4_eq);
  Comparator #(.width(5), .mode("twosComplement")) comparator_4 (
    .a(EX_WriteReg_num), .b({5{1'b0}}), .eq(comparator_4_eq));  // open: gt, lt
  \源寄存器使用情况  \u_源寄存器使用情况_1  (
    .OP0(ID_OP[0]), .OP1(ID_OP[1]), .OP2(ID_OP[2]), .OP3(ID_OP[3]), .OP4(ID_OP[4]), .OP5(ID_OP[5]),
    .F0(ID_FUNC[0]), .F1(ID_FUNC[1]), .F2(ID_FUNC[2]), .F3(ID_FUNC[3]), .F4(ID_FUNC[4]), .F5(ID_FUNC[5]),
    .R1_Used(\源寄存器使用情况_1_r1_used ), .R2_Used(\源寄存器使用情况_1_r2_used ));
  not not_3 (not_3_out, comparator_5_eq);
  Comparator #(.width(5), .mode("twosComplement")) comparator_5 (
    .a({5{1'b0}}), .b(MEM_WriteReg_num), .eq(comparator_5_eq));  // open: gt, lt
  Comparator #(.width(5), .mode("twosComplement")) comparator_6 (
    .a(MEM_WriteReg_num), .b(ID_R2_num), .eq(comparator_6_eq));  // open: gt, lt
  Comparator #(.width(5), .mode("twosComplement")) comparator_7 (
    .a(ID_R2_num), .b(EX_WriteReg_num), .eq(comparator_7_eq));  // open: gt, lt
  Comparator #(.width(5), .mode("twosComplement")) comparator_8 (
    .a(EX_WriteReg_num), .b({5{1'b0}}), .eq(comparator_8_eq));  // open: gt, lt
  not not_4 (not_4_out, comparator_8_eq);
  and and_1 (and_1_out, not_1_out, MEM_RegWrite, comparator_2_eq);
  and and_2 (and_2_out, comparator_3_eq, EX_RegWrite, not_2_out);
  and and_3 (and_3_out, not_3_out, MEM_RegWrite, comparator_6_eq);
  and and_4 (and_4_out, comparator_7_eq, EX_RegWrite, not_4_out);
  or or_1 (or_1_out, and_1_out, and_2_out);
  or or_2 (or_2_out, and_3_out, and_4_out);
  and and_5 (and_5_out, or_1_out, \源寄存器使用情况_1_r1_used );
  or or_3 (\数据相关 , and_5_out, and_6_out);
  and and_6 (and_6_out, \源寄存器使用情况_1_r2_used , or_2_out);
  Comparator #(.width(6), .mode("twosComplement")) comparator_9 (
    .a(6'b100011), .b(MEM_OP), .eq(comparator_9_eq));  // open: gt, lt
  or or_4 (or_4_out, comparator_9_eq, comparator_10_eq);
  Comparator #(.width(6), .mode("twosComplement")) comparator_10 (
    .a(MEM_OP), .b(6'b100100), .eq(comparator_10_eq));  // open: gt, lt
  and and_7 (and_7_out, and_1_out, or_4_out);
  and and_8 (and_8_out, or_4_out, and_3_out);
  Priority_Encoder #(.select(2), .disabled("Z")) priority_encoder_1 (
    .in0(1'b1), .in1(and_1_out), .in2(and_7_out), .in3(and_2_out), .out(priority_encoder_1_out));  // open: gs, en_out, en_in
  Comparator #(.width(6), .mode("twosComplement")) comparator_11 (
    .a(EX_OP), .b(6'b100011), .eq(comparator_11_eq));  // open: gt, lt
  Comparator #(.width(6), .mode("twosComplement")) comparator_12 (
    .a(EX_OP), .b(6'b100100), .eq(comparator_12_eq));  // open: gt, lt
  Priority_Encoder #(.select(2), .disabled("Z")) priority_encoder_2 (
    .in0(1'b1), .in1(and_3_out), .in2(and_8_out), .in3(and_4_out), .out(priority_encoder_2_out));  // open: gs, en_out, en_in
  Multiplexer #(.select(1), .width(2), .disabled("Z"), .enable("false")) multiplexer_1 (
    .in0(priority_encoder_1_out), .in1(2'b00), .out(R1_Forward), .sel(\Load_Use相关 ));
  or or_5 (or_5_out, and_2_out, and_4_out);
  or or_6 (or_6_out, comparator_11_eq, comparator_12_eq);
  Multiplexer #(.select(1), .width(2), .disabled("Z"), .enable("false")) multiplexer_2 (
    .in0(priority_encoder_2_out), .in1(2'b00), .out(R2_Forward), .sel(\Load_Use相关 ));
  and and_9 (\Load_Use相关 , or_5_out, or_6_out);

  // Notes on the sheet:
  //   忽略0号寄存器
  //   忽略0号寄存器
  //   lw
  //   lbu
  //   lw
  //   lbu
endmodule

module \理想流水线  (
);

  wire and_1_out, and_2_out, and_3_out, and_4_out, and_5_out, BLTZ, CLK, comparator_2_eq, Conbranch, Equal,
       ex_mem_1_halt_out, ex_mem_1_jal_out, ex_mem_1_memtoreg_out, ex_mem_1_regdst_out,
       ex_mem_1_regwrite_out, ex_mem_1_syscall_out, Go, Halt, id_ex_1_alusrcb_out, id_ex_1_beq_out,
       id_ex_1_bne_out, id_ex_1_halt_out, id_ex_1_jal_out, id_ex_1_lbu_out, id_ex_1_memtoreg_out,
       id_ex_1_memwrite_out, id_ex_1_regdst_out, id_ex_1_regwrite_out, id_ex_1_syscall_out, IR1, IR2, IR3,
       JAL, JMP, JR, LBU, mem_wb_1_halt_out, MemToReg, MemWrite, mips_alu_1_equal, not_1_out, or_1_out, RDst,
       RST, RW, SignedExt, Sys, syscall, W1, W2, W3, \单周期硬布线控制器_1_alu_src , \单周期硬布线控制器_1_beq ,
       \单周期硬布线控制器_1_bltz , \单周期硬布线控制器_1_bne , \单周期硬布线控制器_1_jal , \单周期硬布线控制器_1_jmp , \单周期硬布线控制器_1_jr ,
       \单周期硬布线控制器_1_lbu , \单周期硬布线控制器_1_memtoreg , \单周期硬布线控制器_1_memwrite , \单周期硬布线控制器_1_regdst ,
       \单周期硬布线控制器_1_regwrite ;
  wire [1:0] \字节选择 ;
  wire [3:0] id_ex_1_aluop_out, \单周期硬布线控制器_1_alu_op ;
  wire [4:0] id_ex_1_shamt_out, multiplexer_2_out, multiplexer_4_out, multiplexer_10_out, multiplexer_11_out;
  wire [7:0] multiplexer_7_out;
  wire [15:0] \LoadUse次数 , \总周期数 , \插入气泡数 , \无条件分支数 , \条件分支成功数 ;
  wire [25:0] if_id_1_ir_out_2;
  wire [31:0] a0, adder_2_out, bit_extender_1_out, bit_extender_2_out, bit_extender_3_out, ex_mem_1_ir_out,
       ex_mem_1_r2_out, EX_PC, id_ex_1_address_out, id_ex_1_imm_out, id_ex_1_ir_out, id_ex_1_r1_out,
       id_ex_1_r2_out, ID_PC, IF_PC, LedData, MEM_PC, mem_wb_1_alur_out, mem_wb_1_ir_out, mem_wb_1_memd_out,
       mips_alu_1_result, mips_regifile_1_r2, multiplexer_1_out, multiplexer_3_out, multiplexer_5_out,
       multiplexer_6_out, multiplexer_8_out, multiplexer_9_out, PC, ram_1_data, RDin, shifter_1_out, WB_PC,
       \指令存储器_data ;
  wire [31:2] ex_mem_1_alur_out;
  wire [31:26] if_id_1_ir_out;

  Button \u_总复位  (.out(RST));
  Button _1 (.out(IR1));
  Button _2 (.out(IR2));
  Button _3 (.out(IR3));
  Button \u_继续运行  (.out(Go));
  LED #(.active("true")) led_1 (.in(W1));
  LED #(.active("true")) led_2 (.in(W2));
  LED #(.active("true")) led_3 (.in(W3));
  Counter #(.width(16), .max('hffff), .ongoal("wrap"), .trigger("rising"), .behavior("old")) counter_1 (
    .count(JMP), .Q(\无条件分支数 ), .clk(CLK), .clr(RST));  // open: load, D, carry, preset
  Hex_Digit_Display hex_digit_display_1 (.value(LedData[31:28]));  // open: dp
  Multiplexer #(.select(3), .width(32), .disabled("Z"), .enable("false")) multiplexer_1 (
    .in0(IF_PC), .in1({32{1'b0}}), .in2(id_ex_1_address_out), .in3(a0), .in4(adder_2_out), .in5({32{1'b0}}),
    .in6({32{1'b0}}), .in7({32{1'b0}}), .out(multiplexer_1_out), .sel({Conbranch, JMP, JR}));
  Counter #(.width(16), .max('hffff), .ongoal("wrap"), .trigger("rising"), .behavior("old")) counter_2 (
    .count(or_1_out), .Q(\总周期数 ), .clk(CLK), .clr(RST));  // open: load, D, carry, preset
  or or_1 (or_1_out, Halt, Go);
  Hex_Digit_Display hex_digit_display_2 (.value(LedData[23:20]));  // open: dp
  Hex_Digit_Display hex_digit_display_3 (.value(LedData[27:24]));  // open: dp
  Register #(.width(32), .trigger("rising"), .Select("low")) u_PC (
    .D(multiplexer_1_out), .en(or_1_out), .Q(PC), .clk(CLK), .clr(RST));
  Hex_Digit_Display hex_digit_display_4 (.value(LedData[15:12]));  // open: dp
  Hex_Digit_Display hex_digit_display_5 (.value(LedData[19:16]));  // open: dp
  Counter #(.width(16), .max('hffff), .ongoal("wrap"), .trigger("rising"), .behavior("old")) counter_3 (
    .count(Conbranch), .Q(\条件分支成功数 ), .clk(CLK), .clr(RST));  // open: load, D, carry, preset
  Adder #(.width(32)) adder_1 (.a(PC), .b(32'h4), .out(IF_PC));  // open: cin, cout
  Hex_Digit_Display hex_digit_display_6 (.value(LedData[7:4]));  // open: dp
  Hex_Digit_Display hex_digit_display_7 (.value(LedData[11:8]));  // open: dp
  Clock #(.highDuration(1), .lowDuration(1)) clock_1 (.out(CLK));
  ROM #(.addrWidth(10), .dataWidth(32), .Select("high")) \u_指令存储器  (.addr(PC[11:2]), .data(\指令存储器_data ));
  Hex_Digit_Display hex_digit_display_8 (.value(LedData[3:0]));  // open: dp
  IF_ID if_id_1 (
    .PC_in(IF_PC), .IR_in(\指令存储器_data ), .PC_out(ID_PC), .IR_out({if_id_1_ir_out, if_id_1_ir_out_2}),
    .Reset(RST), .CLK(CLK), .Enable(Halt));  // open: PCr_in, PC_G_in, HG_in, PCr_out, PC_G_out, HG_out
  Register #(.width(32), .trigger("rising"), .Select("low")) register_1 (
    .D(a0), .en(and_1_out), .Q(LedData), .clk(CLK), .clr(RST));
  and and_1 (and_1_out, Equal, syscall);
  // Probe on \总周期数 
  // Probe on \无条件分支数 
  // Probe on \条件分支成功数 
  // Probe on \插入气泡数 
  // Probe on \LoadUse次数 
  // Probe on IF_PC[11:0]
  // Probe on if_id_1_ir_out_2[25:21]
  // Probe on if_id_1_ir_out_2[20:16]
  // Probe on if_id_1_ir_out_2[15:11]
  // Probe on ID_PC[11:0]
  // Probe on EX_PC[11:0]
  \单周期硬布线控制器  \u_单周期硬布线控制器_1  (
    .Func(if_id_1_ir_out_2[5:0]), .OP(if_id_1_ir_out), .ALU_OP(\单周期硬布线控制器_1_alu_op ),
    .MemToReg(\单周期硬布线控制器_1_memtoreg ), .MemWrite(\单周期硬布线控制器_1_memwrite ), .ALU_SRC(\单周期硬布线控制器_1_alu_src ),
    .RegWrite(\单周期硬布线控制器_1_regwrite ), .SysCALL(syscall), .SignedExt(SignedExt),
    .RegDst(\单周期硬布线控制器_1_regdst ), .JR(\单周期硬布线控制器_1_jr ), .JMP(\单周期硬布线控制器_1_jmp ), .Beq(\单周期硬布线控制器_1_beq ),
    .JAL(\单周期硬布线控制器_1_jal ), .Bne(\单周期硬布线控制器_1_bne ), .LBU(\单周期硬布线控制器_1_lbu ), .BLTZ(\单周期硬布线控制器_1_bltz ));  // open: MFC0, MTC0, MF, ERET
  Multiplexer #(.select(1), .width(5), .disabled("Z"), .enable("false")) multiplexer_2 (
    .in0(if_id_1_ir_out_2[25:21]), .in1(5'b00100), .out(multiplexer_2_out), .sel(syscall));
  assign bit_extender_1_out = {{16{1'b0}}, if_id_1_ir_out_2[15:0]};  // Bit_Extender bit_extender_1
  Multiplexer #(.select(1), .width(32), .disabled("Z"), .enable("false")) multiplexer_3 (
    .in0(bit_extender_1_out), .in1(bit_extender_2_out), .out(multiplexer_3_out), .sel(SignedExt));
  assign bit_extender_2_out = {{16{if_id_1_ir_out_2[15]}}, if_id_1_ir_out_2[15:0]};  // Bit_Extender bit_extender_2
  // Probe on multiplexer_11_out
  // Probe on MEM_PC[11:0]
  Multiplexer #(.select(1), .width(5), .disabled("Z"), .enable("false")) multiplexer_4 (
    .in0(if_id_1_ir_out_2[20:16]), .in1(5'b00010), .out(multiplexer_4_out), .sel(syscall));
  // Probe on WB_PC[11:0]
  MIPS_Regifile mips_regifile_1 (
    .Din(RDin), .Clk(CLK), .R1(a0), .R2(mips_regifile_1_r2), .WE(RW), .W_num(multiplexer_11_out),
    .R1_num(multiplexer_2_out), .R2_num(multiplexer_4_out));
  // Probe on multiplexer_3_out
  // Probe on RDin
  // Probe on a0
  // Probe on mips_regifile_1_r2
  Comparator #(.width(32), .mode("unsigned")) comparator_1 (
    .a(mips_regifile_1_r2), .b(32'h22), .eq(Equal));  // open: gt, lt
  ID_EX id_ex_1 (
    .BEQ_in(\单周期硬布线控制器_1_beq ), .BEQ_out(id_ex_1_beq_out), .IR_in({if_id_1_ir_out, if_id_1_ir_out_2}),
    .IR_out(id_ex_1_ir_out), .BNE_in(\单周期硬布线控制器_1_bne ), .BNE_out(id_ex_1_bne_out), .PC_in(ID_PC),
    .PC_out(EX_PC), .MemToReg_in(\单周期硬布线控制器_1_memtoreg ), .MemToReg_out(id_ex_1_memtoreg_out), .R1_in(a0),
    .R1_out(id_ex_1_r1_out), .MemWrite_in(\单周期硬布线控制器_1_memwrite ), .MemWrite_out(id_ex_1_memwrite_out),
    .R2_in(mips_regifile_1_r2), .AluSrcB_in(\单周期硬布线控制器_1_alu_src ), .R2_out(id_ex_1_r2_out),
    .AluSrcB_out(id_ex_1_alusrcb_out), .RegWrite_in(\单周期硬布线控制器_1_regwrite ), .Imm_in(multiplexer_3_out),
    .RegWrite_out(id_ex_1_regwrite_out), .Imm_out(id_ex_1_imm_out), .JAL_in(\单周期硬布线控制器_1_jal ),
    .JAL_out(id_ex_1_jal_out), .Address_in({ID_PC[31:28], if_id_1_ir_out_2, 2'b00}),
    .Address_out(id_ex_1_address_out), .RegDst_in(\单周期硬布线控制器_1_regdst ), .RegDst_out(id_ex_1_regdst_out),
    .AluOP_in(\单周期硬布线控制器_1_alu_op ), .AluOP_out(id_ex_1_aluop_out), .Syscall_in(syscall),
    .Syscall_out(id_ex_1_syscall_out), .Shamt_in(if_id_1_ir_out_2[10:6]), .Shamt_out(id_ex_1_shamt_out),
    .JMP_in(\单周期硬布线控制器_1_jmp ), .JMP_out(JMP), .Halt_in(and_2_out), .Halt_out(id_ex_1_halt_out),
    .JR_in(\单周期硬布线控制器_1_jr ), .LBU_in(\单周期硬布线控制器_1_lbu ), .JR_out(JR), .LBU_out(id_ex_1_lbu_out),
    .BLTZ_in(\单周期硬布线控制器_1_bltz ), .BLTZ_out(BLTZ), .Reset(RST), .Enable(Halt), .CLK(CLK));  // open: W__in, W__out, PCr_in, PCr_out, HG_in, HG_out, PCG_in, PCG_out, Interrupt_in, Interrupt_out
  and and_2 (and_2_out, syscall, ~Equal);  // AND_Gate
  Multiplexer #(.select(1), .width(32), .disabled("Z"), .enable("false")) multiplexer_5 (
    .in0(id_ex_1_r2_out), .in1(id_ex_1_imm_out), .out(multiplexer_5_out), .sel(id_ex_1_alusrcb_out));
  and and_3 (and_3_out, id_ex_1_beq_out, mips_alu_1_equal);
  Multiplexer #(.select(1), .width(32), .disabled("Z"), .enable("false")) multiplexer_6 (
    .in0(multiplexer_5_out), .in1({32{1'b0}}), .out(multiplexer_6_out), .sel(BLTZ));
  and and_4 (and_4_out, id_ex_1_bne_out, ~mips_alu_1_equal);  // AND_Gate
  MIPS_ALU mips_alu_1 (
    .X(id_ex_1_r1_out), .Y(multiplexer_6_out), .AluOP(id_ex_1_aluop_out), .Equal(mips_alu_1_equal),
    .Result(mips_alu_1_result), .shamt(id_ex_1_shamt_out));  // open: Result_2
  Shifter #(.width(32), .shift("ll")) shifter_1 (.in(id_ex_1_imm_out), .\dist (5'b00010), .out(shifter_1_out));
  Adder #(.width(32)) adder_2 (.a(shifter_1_out), .b(EX_PC), .out(adder_2_out));  // open: cin, cout
  or or_2 (Conbranch, and_3_out, and_4_out, and_5_out);
  and and_5 (and_5_out, BLTZ, comparator_2_eq);
  Comparator #(.width(32), .mode("twosComplement")) comparator_2 (
    .a(32'h1), .b(mips_alu_1_result), .eq(comparator_2_eq));  // open: gt, lt
  EX_MEM ex_mem_1 (
    .MemToReg_in(id_ex_1_memtoreg_out), .IR_in(id_ex_1_ir_out), .MemToReg_out(ex_mem_1_memtoreg_out),
    .IR_out(ex_mem_1_ir_out), .MemWrite_in(id_ex_1_memwrite_out), .MemWrite_out(MemWrite), .PC_in(EX_PC),
    .PC_out(MEM_PC), .RegWrite_in(id_ex_1_regwrite_out), .RegWrite_out(ex_mem_1_regwrite_out),
    .R2_in(id_ex_1_r2_out), .R2_out(ex_mem_1_r2_out), .JAL_in(id_ex_1_jal_out), .JAL_out(ex_mem_1_jal_out),
    .AluR_in(mips_alu_1_result), .AluR_out({ex_mem_1_alur_out, \字节选择 }), .RegDst_in(id_ex_1_regdst_out),
    .RegDst_out(ex_mem_1_regdst_out), .Halt_in(id_ex_1_halt_out), .Halt_out(ex_mem_1_halt_out),
    .Syscall_in(id_ex_1_syscall_out), .Syscall_out(ex_mem_1_syscall_out), .LBU_in(id_ex_1_lbu_out),
    .LBU_out(LBU), .Reset(RST), .Enable(Halt), .CLK(CLK));  // open: PCr_in, W__in, PCr_out, W__out, Interrupt_in, Interrupt_out
  RAM #(.addrWidth(10), .dataWidth(32), .bus("separate"), .Select("high")) ram_1 (
    .addr(ex_mem_1_alur_out[11:2]), .din(ex_mem_1_r2_out), .data(ram_1_data), .str(MemWrite), .clk(CLK),
    .ld(not_1_out), .clr(RST));  // open: sel
  not not_1 (not_1_out, MemWrite);
  Multiplexer #(.select(2), .width(8), .disabled("Z"), .enable("false")) multiplexer_7 (
    .in0(ram_1_data[7:0]), .in1(ram_1_data[15:8]), .in2(ram_1_data[23:16]), .in3(ram_1_data[31:24]),
    .out(multiplexer_7_out), .sel(\字节选择 ));
  assign bit_extender_3_out = {{24{1'b0}}, multiplexer_7_out};  // Bit_Extender bit_extender_3
  MEM_WB mem_wb_1 (
    .MemToReg_in(ex_mem_1_memtoreg_out), .IR_in(ex_mem_1_ir_out), .MemToReg_out(MemToReg),
    .IR_out(mem_wb_1_ir_out), .RegWrite_in(ex_mem_1_regwrite_out), .PC_in(MEM_PC), .RegWrite_out(RW),
    .PC_out(WB_PC), .JAL_in(ex_mem_1_jal_out), .JAL_out(JAL), .MemD_in(multiplexer_8_out),
    .MemD_out(mem_wb_1_memd_out), .RegDst_in(ex_mem_1_regdst_out), .RegDst_out(RDst),
    .AluR_in({ex_mem_1_alur_out, \字节选择 }), .AluR_out(mem_wb_1_alur_out), .Syscall_in(ex_mem_1_syscall_out),
    .Syscall_out(Sys), .Halt_in(ex_mem_1_halt_out), .Halt_out(mem_wb_1_halt_out), .Reset(RST), .Enable(Halt),
    .CLK(CLK));  // open: W__in, PCr_in, W__out, PCr_out, Interrupt_in, Interrupt_out, R2_in, R2_out
  Multiplexer #(.select(1), .width(32), .disabled("Z"), .enable("false")) multiplexer_8 (
    .in0(ram_1_data), .in1(bit_extender_3_out), .out(multiplexer_8_out), .sel(LBU));
  not not_2 (Halt, mem_wb_1_halt_out);
  Multiplexer #(.select(1), .width(32), .disabled("Z"), .enable("false")) multiplexer_9 (
    .in0(mem_wb_1_alur_out), .in1(mem_wb_1_memd_out), .out(multiplexer_9_out), .sel(MemToReg));
  Multiplexer #(.select(1), .width(5), .disabled("Z"), .enable("false")) multiplexer_10 (
    .in0(mem_wb_1_ir_out[20:16]), .in1(mem_wb_1_ir_out[15:11]), .out(multiplexer_10_out), .sel(RDst));
  Multiplexer #(.select(1), .width(5), .disabled("Z"), .enable("false")) multiplexer_11 (
    .in0(multiplexer_10_out), .in1({5{1'b1}}), .out(multiplexer_11_out), .sel(JAL));
  Multiplexer #(.select(1), .width(32), .disabled("Z"), .enable("false")) multiplexer_12 (
    .in0(multiplexer_9_out), .in1(WB_PC), .out(RDin), .sel(JAL));

  // Notes on the sheet:
  //   中断源
  //   中断等待指示
  //   数码管输出
  //   contents of 指令存储器 (hex, n*v repeats v):
  //   20100000 20110000 20120000 20130000 36100000 36310001 36520002 36730003 ae100000 ae110004 ae120008
  //   ae13000c 2002000a 20110000 20120000 20130000 c
  //   指令字
  //   imm
  //   OP
  //   Func
  //   rs
  //   rt
  //   rd
  //   shamt
  //   JMP
  //   JR
  //   OP
  //   Func
  //   流水调试日志用
  //   Beq
  //   Bne
  //   MemToReg
  //   MemWrite
  //   AluOP
  //   AluSrcB
  //   RegWrite
  //   JAL
  //   RegDst
  //   Syscall
  //   rt
  //   rd
  //   W#
endmodule

module \分支流水线  (
);

  wire and_1_out, and_2_out, and_3_out, and_4_out, and_5_out, BLTZ, CLK, comparator_2_eq, Conbranch, Equal,
       ex_mem_1_halt_out, ex_mem_1_jal_out, ex_mem_1_memtoreg_out, ex_mem_1_regdst_out,
       ex_mem_1_regwrite_out, ex_mem_1_syscall_out, Go, Halt, id_ex_1_alusrcb_out, id_ex_1_beq_out,
       id_ex_1_bne_out, id_ex_1_halt_out, id_ex_1_jal_out, id_ex_1_lbu_out, id_ex_1_memtoreg_out,
       id_ex_1_memwrite_out, id_ex_1_regdst_out, id_ex_1_regwrite_out, id_ex_1_syscall_out, IR1, IR2, IR3,
       JAL, JMP, JR, LBU, mem_wb_1_halt_out, MemToReg, MemWrite, mips_alu_1_equal, Nop, not_1_out, or_1_out,
       or_2_out, or_3_out, RDst, RST, RW, SignedExt, Sys, syscall, W1, W2, W3, \单周期硬布线控制器_1_alu_src ,
       \单周期硬布线控制器_1_beq , \单周期硬布线控制器_1_bltz , \单周期硬布线控制器_1_bne , \单周期硬布线控制器_1_jal , \单周期硬布线控制器_1_jmp ,
       \单周期硬布线控制器_1_jr , \单周期硬布线控制器_1_lbu , \单周期硬布线控制器_1_memtoreg , \单周期硬布线控制器_1_memwrite ,
       \单周期硬布线控制器_1_regdst , \单周期硬布线控制器_1_regwrite ;
  wire [1:0] \字节选择 ;
  wire [3:0] id_ex_1_aluop_out, \单周期硬布线控制器_1_alu_op ;
  wire [4:0] id_ex_1_shamt_out, multiplexer_2_out, multiplexer_4_out, multiplexer_10_out, multiplexer_11_out;
  wire [7:0] multiplexer_7_out;
  wire [15:0] adder_2_out, \LoadUse次数 , \总周期数 , \插入气泡数 , \无条件分支数 , \条件分支成功数 ;
  wire [25:0] if_id_1_ir_out_2;
  wire [31:0] a0, adder_3_out, bit_extender_1_out, bit_extender_2_out, bit_extender_3_out, ex_mem_1_ir_out,
       ex_mem_1_r2_out, EX_PC, id_ex_1_address_out, id_ex_1_imm_out, id_ex_1_ir_out, id_ex_1_r2_out, ID_PC,
       IF_PC, LedData, MEM_PC, mem_wb_1_alur_out, mem_wb_1_ir_out, mem_wb_1_memd_out, mips_alu_1_result,
       mips_regifile_1_r2, multiplexer_1_out, multiplexer_3_out, multiplexer_5_out, multiplexer_6_out,
       multiplexer_8_out, multiplexer_9_out, PC, R1, ram_1_data, RDin, shifter_1_out, WB_PC, \指令存储器_data ;
  wire [31:2] ex_mem_1_alur_out;
  wire [31:26] if_id_1_ir_out;

  Button \u_总复位  (.out(RST));
  Button _1 (.out(IR1));
  Button _2 (.out(IR2));
  Button _3 (.out(IR3));
  Button \u_继续运行  (.out(Go));
  LED #(.active("true")) led_1 (.in(W1));
  LED #(.active("true")) led_2 (.in(W2));
  LED #(.active("true")) led_3 (.in(W3));
  Counter #(.width(16), .max('hffff), .ongoal("wrap"), .trigger("rising"), .behavior("old")) counter_1 (
    .count(JMP), .Q(\无条件分支数 ), .clk(CLK), .clr(RST));  // open: load, D, carry, preset
  Hex_Digit_Display hex_digit_display_1 (.value(LedData[31:28]));  // open: dp
  Multiplexer #(.select(3), .width(32), .disabled("Z"), .enable("false")) multiplexer_1 (
    .in0(IF_PC), .in1({32{1'b0}}), .in2(id_ex_1_address_out), .in3(R1), .in4(adder_3_out), .in5({32{1'b0}}),
    .in6({32{1'b0}}), .in7({32{1'b0}}), .out(multiplexer_1_out), .sel({Conbranch, JMP, JR}));
  Counter #(.width(16), .max('hffff), .ongoal("wrap"), .trigger("rising"), .behavior("old")) counter_2 (
    .count(or_1_out), .Q(\总周期数 ), .clk(CLK), .clr(RST));  // open: load, D, carry, preset
  or or_1 (or_1_out, Halt, Go);
  Hex_Digit_Display hex_digit_display_2 (.value(LedData[27:24]));  // open: dp
  Hex_Digit_Display hex_digit_display_3 (.value(LedData[23:20]));  // open: dp
  Register #(.width(32), .trigger("rising"), .Select("low")) u_PC (
    .D(multiplexer_1_out), .en(or_1_out), .Q(PC), .clk(CLK), .clr(RST));
  Hex_Digit_Display hex_digit_display_4 (.value(LedData[15:12]));  // open: dp
  Hex_Digit_Display hex_digit_display_5 (.value(LedData[19:16]));  // open: dp
  Counter #(.width(16), .max('hffff), .ongoal("wrap"), .trigger("rising"), .behavior("old")) counter_3 (
    .count(Conbranch), .Q(\条件分支成功数 ), .clk(CLK), .clr(RST));  // open: load, D, carry, preset
  Adder #(.width(32)) adder_1 (.a(PC), .b(32'h4), .out(IF_PC));  // open: cin, cout
  Hex_Digit_Display hex_digit_display_6 (.value(LedData[7:4]));  // open: dp
  Hex_Digit_Display hex_digit_display_7 (.value(LedData[11:8]));  // open: dp
  Clock #(.highDuration(1), .lowDuration(1)) clock_1 (.out(CLK));
  ROM #(.addrWidth(10), .dataWidth(32), .Select("high")) \u_指令存储器  (.addr(PC[11:2]), .data(\指令存储器_data ));
  Hex_Digit_Display hex_digit_display_8 (.value(LedData[3:0]));  // open: dp
  or or_2 (or_2_out, RST, Nop);
  IF_ID if_id_1 (
    .PC_in(IF_PC), .IR_in(\指令存储器_data ), .PC_out(ID_PC), .IR_out({if_id_1_ir_out, if_id_1_ir_out_2}),
    .Reset(or_2_out), .CLK(CLK), .Enable(Halt));  // open: PCr_in, PC_G_in, HG_in, PCr_out, PC_G_out, HG_out
  Register #(.width(32), .trigger("rising"), .Select("low")) register_1 (
    .D(a0), .en(and_1_out), .Q(LedData), .clk(CLK), .clr(RST));
  and and_1 (and_1_out, Equal, syscall);
  // Probe on \总周期数 
  // Probe on \无条件分支数 
  // Probe on \条件分支成功数 
  // Probe on \插入气泡数 
  // Probe on \LoadUse次数 
  // Probe on IF_PC[11:0]
  // Probe on if_id_1_ir_out_2[25:21]
  // Probe on if_id_1_ir_out_2[20:16]
  // Probe on if_id_1_ir_out_2[15:11]
  // Probe on EX_PC[11:0]
  // Probe on ID_PC[11:0]
  \单周期硬布线控制器  \u_单周期硬布线控制器_1  (
    .Func(if_id_1_ir_out_2[5:0]), .OP(if_id_1_ir_out), .ALU_OP(\单周期硬布线控制器_1_alu_op ),
    .MemToReg(\单周期硬布线控制器_1_memtoreg ), .MemWrite(\单周期硬布线控制器_1_memwrite ), .ALU_SRC(\单周期硬布线控制器_1_alu_src ),
    .RegWrite(\单周期硬布线控制器_1_regwrite ), .SysCALL(syscall), .SignedExt(SignedExt),
    .RegDst(\单周期硬布线控制器_1_regdst ), .JR(\单周期硬布线控制器_1_jr ), .JMP(\单周期硬布线控制器_1_jmp ), .Beq(\单周期硬布线控制器_1_beq ),
    .JAL(\单周期硬布线控制器_1_jal ), .Bne(\单周期硬布线控制器_1_bne ), .LBU(\单周期硬布线控制器_1_lbu ), .BLTZ(\单周期硬布线控制器_1_bltz ));  // open: MFC0, MTC0, MF, ERET
  Multiplexer #(.select(1), .width(5), .disabled("Z"), .enable("false")) multiplexer_2 (
    .in0(if_id_1_ir_out_2[25:21]), .in1(5'b00100), .out(multiplexer_2_out), .sel(syscall));
  assign bit_extender_1_out = {{16{1'b0}}, if_id_1_ir_out_2[15:0]};  // Bit_Extender bit_extender_1
  Multiplexer #(.select(1), .width(32), .disabled("Z"), .enable("false")) multiplexer_3 (
    .in0(bit_extender_1_out), .in1(bit_extender_2_out), .out(multiplexer_3_out), .sel(SignedExt));
  assign bit_extender_2_out = {{16{if_id_1_ir_out_2[15]}}, if_id_1_ir_out_2[15:0]};  // Bit_Extender bit_extender_2
  // Probe on multiplexer_11_out
  // Probe on MEM_PC[11:0]
  Adder #(.width(16)) adder_2 (.a(\无条件分支数 ), .b(\条件分支成功数 ), .out(adder_2_out));  // open: cin, cout
  Multiplexer #(.select(1), .width(5), .disabled("Z"), .enable("false")) multiplexer_4 (
    .in0(if_id_1_ir_out_2[20:16]), .in1(5'b00010), .out(multiplexer_4_out), .sel(syscall));
  // Probe on WB_PC[11:0]
  Multiplier #(.width(16)) multiplier_1 (.a(adder_2_out), .b(16'h2), .out(\插入气泡数 ));  // open: cin, cout
  MIPS_Regifile mips_regifile_1 (
    .Din(RDin), .Clk(CLK), .R1(a0), .R2(mips_regifile_1_r2), .WE(RW), .W_num(multiplexer_11_out),
    .R1_num(multiplexer_2_out), .R2_num(multiplexer_4_out));
  // Probe on multiplexer_3_out
  // Probe on RDin
  // Probe on a0
  // Probe on mips_regifile_1_r2
  Comparator #(.width(32), .mode("unsigned")) comparator_1 (
    .a(mips_regifile_1_r2), .b(32'h22), .eq(Equal));  // open: gt, lt
  or or_3 (or_3_out, RST, Nop);
  ID_EX id_ex_1 (
    .BEQ_in(\单周期硬布线控制器_1_beq ), .BEQ_out(id_ex_1_beq_out), .IR_in({if_id_1_ir_out, if_id_1_ir_out_2}),
    .IR_out(id_ex_1_ir_out), .BNE_in(\单周期硬布线控制器_1_bne ), .BNE_out(id_ex_1_bne_out), .PC_in(ID_PC),
    .PC_out(EX_PC), .MemToReg_in(\单周期硬布线控制器_1_memtoreg ), .MemToReg_out(id_ex_1_memtoreg_out), .R1_in(a0),
    .R1_out(R1), .MemWrite_in(\单周期硬布线控制器_1_memwrite ), .MemWrite_out(id_ex_1_memwrite_out),
    .R2_in(mips_regifile_1_r2), .AluSrcB_in(\单周期硬布线控制器_1_alu_src ), .R2_out(id_ex_1_r2_out),
    .AluSrcB_out(id_ex_1_alusrcb_out), .RegWrite_in(\单周期硬布线控制器_1_regwrite ), .Imm_in(multiplexer_3_out),
    .RegWrite_out(id_ex_1_regwrite_out), .Imm_out(id_ex_1_imm_out), .JAL_in(\单周期硬布线控制器_1_jal ),
    .JAL_out(id_ex_1_jal_out), .Address_in({ID_PC[31:28], if_id_1_ir_out_2, 2'b00}),
    .Address_out(id_ex_1_address_out), .RegDst_in(\单周期硬布线控制器_1_regdst ), .RegDst_out(id_ex_1_regdst_out),
    .AluOP_in(\单周期硬布线控制器_1_alu_op ), .AluOP_out(id_ex_1_aluop_out), .Syscall_in(syscall),
    .Syscall_out(id_ex_1_syscall_out), .Shamt_in(if_id_1_ir_out_2[10:6]), .Shamt_out(id_ex_1_shamt_out),
    .JMP_in(\单周期硬布线控制器_1_jmp ), .JMP_out(JMP), .Halt_in(and_2_out), .Halt_out(id_ex_1_halt_out),
    .JR_in(\单周期硬布线控制器_1_jr ), .LBU_in(\单周期硬布线控制器_1_lbu ), .JR_out(JR), .LBU_out(id_ex_1_lbu_out),
    .BLTZ_in(\单周期硬布线控制器_1_bltz ), .BLTZ_out(BLTZ), .Reset(or_3_out), .Enable(Halt), .CLK(CLK));  // open: W__in, W__out, PCr_in, PCr_out, HG_in, HG_out, PCG_in, PCG_out, Interrupt_in, Interrupt_out
  and and_2 (and_2_out, syscall, ~Equal);  // AND_Gate
  Multiplexer #(.select(1), .width(32), .disabled("Z"), .enable("false")) multiplexer_5 (
    .in0(id_ex_1_r2_out), .in1(id_ex_1_imm_out), .out(multiplexer_5_out), .sel(id_ex_1_alusrcb_out));
  and and_3 (and_3_out, id_ex_1_beq_out, mips_alu_1_equal);
  Multiplexer #(.select(1), .width(32), .disabled("Z"), .enable("false")) multiplexer_6 (
    .in0(multiplexer_5_out), .in1({32{1'b0}}), .out(multiplexer_6_out), .sel(BLTZ));
  and and_4 (and_4_out, id_ex_1_bne_out, ~mips_alu_1_equal);  // AND_Gate
  MIPS_ALU mips_alu_1 (
    .X(R1), .Y(multiplexer_6_out), .AluOP(id_ex_1_aluop_out), .Equal(mips_alu_1_equal),
    .Result(mips_alu_1_result), .shamt(id_ex_1_shamt_out));  // open: Result_2
  Shifter #(.width(32), .shift("ll")) shifter_1 (.in(id_ex_1_imm_out), .\dist (5'b00010), .out(shifter_1_out));
  Adder #(.width(32)) adder_3 (.a(shifter_1_out), .b(EX_PC), .out(adder_3_out));  // open: cin, cout
  or or_4 (Conbranch, and_3_out, and_4_out, and_5_out);
  and and_5 (and_5_out, BLTZ, comparator_2_eq);
  Comparator #(.width(32), .mode("twosComplement")) comparator_2 (
    .a(32'h1), .b(mips_alu_1_result), .eq(comparator_2_eq));  // open: gt, lt
  or or_5 (Nop, JR, JMP, Conbranch);
  EX_MEM ex_mem_1 (
    .MemToReg_in(id_ex_1_memtoreg_out), .IR_in(id_ex_1_ir_out), .MemToReg_out(ex_mem_1_memtoreg_out),
    .IR_out(ex_mem_1_ir_out), .MemWrite_in(id_ex_1_memwrite_out), .MemWrite_out(MemWrite), .PC_in(EX_PC),
    .PC_out(MEM_PC), .RegWrite_in(id_ex_1_regwrite_out), .RegWrite_out(ex_mem_1_regwrite_out),
    .R2_in(id_ex_1_r2_out), .R2_out(ex_mem_1_r2_out), .JAL_in(id_ex_1_jal_out), .JAL_out(ex_mem_1_jal_out),
    .AluR_in(mips_alu_1_result), .AluR_out({ex_mem_1_alur_out, \字节选择 }), .RegDst_in(id_ex_1_regdst_out),
    .RegDst_out(ex_mem_1_regdst_out), .Halt_in(id_ex_1_halt_out), .Halt_out(ex_mem_1_halt_out),
    .Syscall_in(id_ex_1_syscall_out), .Syscall_out(ex_mem_1_syscall_out), .LBU_in(id_ex_1_lbu_out),
    .LBU_out(LBU), .Reset(RST), .Enable(Halt), .CLK(CLK));  // open: PCr_in, W__in, PCr_out, W__out, Interrupt_in, Interrupt_out
  RAM #(.addrWidth(10), .dataWidth(32), .bus("separate"), .Select("high")) ram_1 (
    .addr(ex_mem_1_alur_out[11:2]), .din(ex_mem_1_r2_out), .data(ram_1_data), .str(MemWrite), .clk(CLK),
    .ld(not_1_out), .clr(RST));  // open: sel
  not not_1 (not_1_out, MemWrite);
  Multiplexer #(.select(2), .width(8), .disabled("Z"), .enable("false")) multiplexer_7 (
    .in0(ram_1_data[7:0]), .in1(ram_1_data[15:8]), .in2(ram_1_data[23:16]), .in3(ram_1_data[31:24]),
    .out(multiplexer_7_out), .sel(\字节选择 ));
  assign bit_extender_3_out = {{24{1'b0}}, multiplexer_7_out};  // Bit_Extender bit_extender_3
  MEM_WB mem_wb_1 (
    .MemToReg_in(ex_mem_1_memtoreg_out), .IR_in(ex_mem_1_ir_out), .MemToReg_out(MemToReg),
    .IR_out(mem_wb_1_ir_out), .RegWrite_in(ex_mem_1_regwrite_out), .PC_in(MEM_PC), .RegWrite_out(RW),
    .PC_out(WB_PC), .JAL_in(ex_mem_1_jal_out), .JAL_out(JAL), .MemD_in(multiplexer_8_out),
    .MemD_out(mem_wb_1_memd_out), .RegDst_in(ex_mem_1_regdst_out), .RegDst_out(RDst),
    .AluR_in({ex_mem_1_alur_out, \字节选择 }), .AluR_out(mem_wb_1_alur_out), .Syscall_in(ex_mem_1_syscall_out),
    .Syscall_out(Sys), .Halt_in(ex_mem_1_halt_out), .Halt_out(mem_wb_1_halt_out), .Reset(RST), .Enable(Halt),
    .CLK(CLK));  // open: W__in, PCr_in, W__out, PCr_out, Interrupt_in, Interrupt_out, R2_in, R2_out
  Multiplexer #(.select(1), .width(32), .disabled("Z"), .enable("false")) multiplexer_8 (
    .in0(ram_1_data), .in1(bit_extender_3_out), .out(multiplexer_8_out), .sel(LBU));
  not not_2 (Halt, mem_wb_1_halt_out);
  Multiplexer #(.select(1), .width(32), .disabled("Z"), .enable("false")) multiplexer_9 (
    .in0(mem_wb_1_alur_out), .in1(mem_wb_1_memd_out), .out(multiplexer_9_out), .sel(MemToReg));
  Multiplexer #(.select(1), .width(5), .disabled("Z"), .enable("false")) multiplexer_10 (
    .in0(mem_wb_1_ir_out[20:16]), .in1(mem_wb_1_ir_out[15:11]), .out(multiplexer_10_out), .sel(RDst));
  Multiplexer #(.select(1), .width(5), .disabled("Z"), .enable("false")) multiplexer_11 (
    .in0(multiplexer_10_out), .in1({5{1'b1}}), .out(multiplexer_11_out), .sel(JAL));
  Multiplexer #(.select(1), .width(32), .disabled("Z"), .enable("false")) multiplexer_12 (
    .in0(multiplexer_9_out), .in1(WB_PC), .out(RDin), .sel(JAL));

  // Notes on the sheet:
  //   中断源
  //   中断等待指示
  //   数码管输出
  //   contents of 指令存储器 (hex, n*v repeats v):
  //   20110100 20020022 8000006 20110004 20120005 20130006 10000003 20110007 20120008 20130009 14110003
  //   2011000a 2012000b 2013000c c000014 2002000a 0 0 0 c 2231ffff 0 0 0 112020 0 0 0 c 1620fff6 3e00008
  //   指令字
  //   imm
  //   OP
  //   Func
  //   rs
  //   rt
  //   rd
  //   shamt
  //   JMP
  //   JR
  //   OP
  //   Func
  //   流水调试日志用
  //   Beq
  //   Bne
  //   MemToReg
  //   MemWrite
  //   AluOP
  //   AluSrcB
  //   RegWrite
  //   JAL
  //   RegDst
  //   Syscall
  //   rt
  //   rd
  //   W#
endmodule

module \气泡流水线  (
);

  wire and_1_out, and_2_out, and_3_out, and_4_out, and_5_out, and_6_out, and_7_out, and_8_out, BLTZ,
       BranchNop, CLK, comparator_2_eq, Conbranch, Equal, ex_mem_1_halt_out, ex_mem_1_jal_out,
       ex_mem_1_memtoreg_out, ex_mem_1_regdst_out, ex_mem_1_syscall_out, EX_RegWrite, Go, Halt,
       id_ex_1_alusrcb_out, id_ex_1_beq_out, id_ex_1_bne_out, id_ex_1_jal_out, id_ex_1_lbu_out,
       id_ex_1_memtoreg_out, id_ex_1_memwrite_out, id_ex_1_regdst_out, ID_JAL, ID_RDst, IR1, IR2, IR3, JAL,
       JMP, JR, LBU, MEM_RegWrite, mem_wb_1_halt_out, MemToReg, MemWrite, mips_alu_1_equal, not_1_out,
       not_2_out, or_1_out, or_2_out, RDst, RST, RW, SignedExt, Sys, syscall, W1, W2, W3,
       \单周期硬布线控制器_1_alu_src , \单周期硬布线控制器_1_beq , \单周期硬布线控制器_1_bltz , \单周期硬布线控制器_1_bne , \单周期硬布线控制器_1_jmp ,
       \单周期硬布线控制器_1_jr , \单周期硬布线控制器_1_lbu , \单周期硬布线控制器_1_memtoreg , \单周期硬布线控制器_1_memwrite ,
       \单周期硬布线控制器_1_regwrite , \单周期硬布线控制器_1_syscall , \数据相关 ;
  wire [1:0] \字节选择 ;
  wire [3:0] id_ex_1_aluop_out, \单周期硬布线控制器_1_alu_op ;
  wire [4:0] EX_WriteReg_num, id_ex_1_shamt_out, ID_R1_num, ID_R2_num, MEM_WriteReg_num, multiplexer_2_out,
       multiplexer_4_out, multiplexer_12_out, multiplexer_13_out;
  wire [5:0] Func, OP;
  wire [7:0] multiplexer_9_out;
  wire [15:0] \LoadUse次数 , \总周期数 , \插入气泡数 , \无条件分支数 , \条件分支成功数 ;
  wire [25:6] if_id_1_ir_out;
  wire [31:0] a0, adder_1_out, adder_2_out, bit_extender_1_out, bit_extender_2_out, bit_extender_3_out,
       ex_mem_1_ir_out, ex_mem_1_pc_out, ex_mem_1_r2_out, EX_PC, id_ex_1_address_out, id_ex_1_imm_out,
       id_ex_1_ir_out, id_ex_1_pc_out, id_ex_1_r2_out, ID_PC, if_id_1_pc_out, IF_PC, LedData, MEM_PC,
       mem_wb_1_alur_out, mem_wb_1_ir_out, mem_wb_1_memd_out, mem_wb_1_pc_out, mips_alu_1_result,
       mips_regifile_1_r1, mips_regifile_1_r2, multiplexer_1_out, multiplexer_5_out, multiplexer_7_out,
       multiplexer_8_out, multiplexer_10_out, multiplexer_11_out, ram_1_data, RDin, shifter_1_out, WB_PC,
       \指令存储器_data ;
  wire [31:2] ex_mem_1_alur_out;

  Button \u_总复位  (.out(RST));
  Button _1 (.out(IR1));
  Button _2 (.out(IR2));
  Button _3 (.out(IR3));
  Button \u_继续运行  (.out(Go));
  LED #(.active("true")) led_1 (.in(W1));
  LED #(.active("true")) led_2 (.in(W2));
  LED #(.active("true")) led_3 (.in(W3));
  Counter #(.width(16), .max('hffff), .ongoal("wrap"), .trigger("rising"), .behavior("old")) counter_1 (
    .count(JMP), .Q(\无条件分支数 ), .clk(CLK), .clr(RST));  // open: load, D, carry, preset
  Counter #(.width(16), .max('hffff), .ongoal("wrap"), .trigger("rising"), .behavior("old")) counter_2 (
    .count(Halt), .Q(\总周期数 ), .clk(CLK), .clr(RST));  // open: load, D, carry, preset
  Hex_Digit_Display hex_digit_display_1 (.value(LedData[31:28]));  // open: dp
  Multiplexer #(.select(3), .width(32), .disabled("Z"), .enable("false")) multiplexer_1 (
    .in0(adder_1_out), .in1({32{1'b0}}), .in2(id_ex_1_address_out), .in3(a0), .in4(adder_2_out),
    .in5({32{1'b0}}), .in6({32{1'b0}}), .in7({32{1'b0}}), .out(multiplexer_1_out), .sel({Conbranch, JMP, JR}));
  and and_1 (and_1_out, Halt, ~\数据相关 );  // AND_Gate
  Hex_Digit_Display hex_digit_display_2 (.value(LedData[23:20]));  // open: dp
  Hex_Digit_Display hex_digit_display_3 (.value(LedData[27:24]));  // open: dp
  and and_2 (and_2_out, Equal, syscall);
  Register #(.width(32), .trigger("rising"), .Select("low")) PC (
    .D(multiplexer_1_out), .en(and_1_out), .Q(IF_PC), .clk(CLK), .clr(RST));
  Hex_Digit_Display hex_digit_display_4 (.value(LedData[19:16]));  // open: dp
  Hex_Digit_Display hex_digit_display_5 (.value(LedData[15:12]));  // open: dp
  Counter #(.width(16), .max('hffff), .ongoal("wrap"), .trigger("rising"), .behavior("old")) counter_3 (
    .count(Conbranch), .Q(\条件分支成功数 ), .clk(CLK), .clr(RST));  // open: load, D, carry, preset
  Register #(.width(32), .trigger("rising"), .Select("low")) register_1 (
    .D(a0), .en(and_2_out), .Q(LedData), .clk(CLK), .clr(RST));
  Adder #(.width(32)) adder_1 (.a(IF_PC), .b(32'h4), .out(adder_1_out));  // open: cin, cout
  Hex_Digit_Display hex_digit_display_6 (.value(LedData[11:8]));  // open: dp
  Hex_Digit_Display hex_digit_display_7 (.value(LedData[7:4]));  // open: dp
  Clock #(.highDuration(1), .lowDuration(1)) clock_1 (.out(CLK));
  ROM #(.addrWidth(10), .dataWidth(32), .Select("high")) \u_指令存储器  (.addr(IF_PC[11:2]), .data(\指令存储器_data ));
  Hex_Digit_Display hex_digit_display_8 (.value(LedData[3:0]));  // open: dp
  or or_1 (or_1_out, RST, BranchNop);
  IF_ID if_id_1 (
    .PCr_in(IF_PC), .PC_in(adder_1_out), .IR_in(\指令存储器_data ), .PCr_out(ID_PC), .PC_out(if_id_1_pc_out),
    .IR_out({OP, if_id_1_ir_out, Func}), .Reset(or_1_out), .CLK(CLK), .Enable(and_3_out));  // open: PC_G_in, HG_in, PC_G_out, HG_out
  and and_3 (and_3_out, ~\数据相关 , Halt);  // AND_Gate
  // Probe on \总周期数 
  // Probe on \无条件分支数 
  // Probe on \条件分支成功数 
  // Probe on \插入气泡数 
  // Probe on \LoadUse次数 
  // Probe on IF_PC[11:0]
  \数据相关检测  \u_数据相关检测_1  (
    .ID_OP(OP), .ID_FUNC(Func), .ID_R1_num(ID_R1_num), .ID_R2_num(ID_R2_num),
    .EX_WriteReg_num(EX_WriteReg_num), .MEM_WriteReg_num(MEM_WriteReg_num), .EX_RegWrite(EX_RegWrite),
    .MEM_RegWrite(MEM_RegWrite), .\数据相关 (\数据相关 ));  // open: EX_OP, Load_Use相关, R1_Forward, R2_Forward, MEM_OP
  Multiplexer #(.select(1), .width(5), .disabled("Z"), .enable("false")) multiplexer_2 (
    .in0(if_id_1_ir_out[20:16]), .in1(if_id_1_ir_out[15:11]), .out(multiplexer_2_out), .sel(ID_RDst));
  // Probe on ID_PC[11:0]
  // Probe on EX_PC[11:0]
  \单周期硬布线控制器  \u_单周期硬布线控制器_1  (
    .Func(Func), .OP(OP), .ALU_OP(\单周期硬布线控制器_1_alu_op ), .MemToReg(\单周期硬布线控制器_1_memtoreg ),
    .MemWrite(\单周期硬布线控制器_1_memwrite ), .ALU_SRC(\单周期硬布线控制器_1_alu_src ), .RegWrite(\单周期硬布线控制器_1_regwrite ),
    .SysCALL(\单周期硬布线控制器_1_syscall ), .SignedExt(SignedExt), .RegDst(ID_RDst), .JR(\单周期硬布线控制器_1_jr ),
    .JMP(\单周期硬布线控制器_1_jmp ), .Beq(\单周期硬布线控制器_1_beq ), .JAL(ID_JAL), .Bne(\单周期硬布线控制器_1_bne ),
    .LBU(\单周期硬布线控制器_1_lbu ), .BLTZ(\单周期硬布线控制器_1_bltz ));  // open: MFC0, MTC0, MF, ERET
  Multiplexer #(.select(1), .width(5), .disabled("Z"), .enable("false")) multiplexer_3 (
    .in0(if_id_1_ir_out[25:21]), .in1(5'b00100), .out(ID_R1_num), .sel(\单周期硬布线控制器_1_syscall ));
  Multiplexer #(.select(1), .width(5), .disabled("Z"), .enable("false")) multiplexer_4 (
    .in0(multiplexer_2_out), .in1({5{1'b1}}), .out(multiplexer_4_out), .sel(ID_JAL));
  assign bit_extender_1_out = {{16{1'b0}}, {if_id_1_ir_out[15:6], Func}};  // Bit_Extender bit_extender_1
  Multiplexer #(.select(1), .width(32), .disabled("Z"), .enable("false")) multiplexer_5 (
    .in0(bit_extender_1_out), .in1(bit_extender_2_out), .out(multiplexer_5_out), .sel(SignedExt));
  assign bit_extender_2_out = {{16{if_id_1_ir_out[15]}}, {if_id_1_ir_out[15:6], Func}};  // Bit_Extender bit_extender_2
  // Probe on multiplexer_13_out
  // Probe on MEM_PC[11:0]
  Multiplexer #(.select(1), .width(5), .disabled("Z"), .enable("false")) multiplexer_6 (
    .in0(if_id_1_ir_out[20:16]), .in1(5'b00010), .out(ID_R2_num), .sel(\单周期硬布线控制器_1_syscall ));
  // Probe on WB_PC[11:0]
  and and_4 (and_4_out, Halt, \数据相关 );
  MIPS_Regifile mips_regifile_1 (
    .Din(RDin), .Clk(CLK), .R1(mips_regifile_1_r1), .R2(mips_regifile_1_r2), .WE(RW),
    .W_num(multiplexer_13_out), .R1_num(ID_R1_num), .R2_num(ID_R2_num));
  // Probe on multiplexer_5_out
  // Probe on RDin
  Counter #(.width(16), .max('hffff), .ongoal("wrap"), .trigger("rising"), .behavior("old")) counter_4 (
    .count(and_4_out), .Q(\插入气泡数 ), .clk(CLK), .clr(RST));  // open: load, D, carry, preset
  or or_2 (or_2_out, RST, \数据相关 , BranchNop);
  ID_EX id_ex_1 (
    .BEQ_in(\单周期硬布线控制器_1_beq ), .BEQ_out(id_ex_1_beq_out), .IR_in({OP, if_id_1_ir_out, Func}),
    .IR_out(id_ex_1_ir_out), .BNE_in(\单周期硬布线控制器_1_bne ), .BNE_out(id_ex_1_bne_out), .PC_in(if_id_1_pc_out),
    .PC_out(id_ex_1_pc_out), .MemToReg_in(\单周期硬布线控制器_1_memtoreg ), .MemToReg_out(id_ex_1_memtoreg_out),
    .R1_in(mips_regifile_1_r1), .R1_out(a0), .MemWrite_in(\单周期硬布线控制器_1_memwrite ),
    .MemWrite_out(id_ex_1_memwrite_out), .R2_in(mips_regifile_1_r2), .AluSrcB_in(\单周期硬布线控制器_1_alu_src ),
    .R2_out(id_ex_1_r2_out), .AluSrcB_out(id_ex_1_alusrcb_out), .RegWrite_in(\单周期硬布线控制器_1_regwrite ),
    .Imm_in(multiplexer_5_out), .RegWrite_out(EX_RegWrite), .Imm_out(id_ex_1_imm_out), .JAL_in(ID_JAL),
    .JAL_out(id_ex_1_jal_out), .Address_in({if_id_1_pc_out[31:28], if_id_1_ir_out, Func, 2'b00}),
    .Address_out(id_ex_1_address_out), .RegDst_in(ID_RDst), .RegDst_out(id_ex_1_regdst_out),
    .AluOP_in(\单周期硬布线控制器_1_alu_op ), .AluOP_out(id_ex_1_aluop_out), .Syscall_in(\单周期硬布线控制器_1_syscall ),
    .Syscall_out(syscall), .Shamt_in(if_id_1_ir_out[10:6]), .Shamt_out(id_ex_1_shamt_out),
    .JMP_in(\单周期硬布线控制器_1_jmp ), .JMP_out(JMP), .JR_in(\单周期硬布线控制器_1_jr ), .LBU_in(\单周期硬布线控制器_1_lbu ),
    .JR_out(JR), .LBU_out(id_ex_1_lbu_out), .BLTZ_in(\单周期硬布线控制器_1_bltz ), .BLTZ_out(BLTZ),
    .W__in(multiplexer_4_out), .W__out(EX_WriteReg_num), .PCr_in(ID_PC), .PCr_out(EX_PC), .Reset(or_2_out),
    .Enable(Halt), .CLK(CLK));  // open: Halt_in, Halt_out, HG_in, HG_out, PCG_in, PCG_out, Interrupt_in, Interrupt_out
  Multiplexer #(.select(1), .width(32), .disabled("Z"), .enable("false")) multiplexer_7 (
    .in0(id_ex_1_r2_out), .in1(id_ex_1_imm_out), .out(multiplexer_7_out), .sel(id_ex_1_alusrcb_out));
  ROM #(.addrWidth(10), .dataWidth(32), .Select("high")) u_BLTZ ();  // open: addr, data
  ROM #(.addrWidth(10), .dataWidth(32), .Select("high")) u_LBU ();  // open: addr, data
  Comparator #(.width(32), .mode("unsigned")) comparator_1 (
    .a(multiplexer_7_out), .b(32'h22), .eq(Equal));  // open: gt, lt
  and and_5 (and_5_out, id_ex_1_beq_out, mips_alu_1_equal);
  Multiplexer #(.select(1), .width(32), .disabled("Z"), .enable("false")) multiplexer_8 (
    .in0(multiplexer_7_out), .in1({32{1'b0}}), .out(multiplexer_8_out), .sel(BLTZ));
  and and_6 (and_6_out, id_ex_1_bne_out, ~mips_alu_1_equal);  // AND_Gate
  MIPS_ALU mips_alu_1 (
    .X(a0), .Y(multiplexer_8_out), .AluOP(id_ex_1_aluop_out), .Equal(mips_alu_1_equal),
    .Result(mips_alu_1_result), .shamt(id_ex_1_shamt_out));  // open: Result_2
  Shifter #(.width(32), .shift("ll")) shifter_1 (.in(id_ex_1_imm_out), .\dist (5'b00010), .out(shifter_1_out));
  Adder #(.width(32)) adder_2 (.a(shifter_1_out), .b(id_ex_1_pc_out), .out(adder_2_out));  // open: cin, cout
  ROM #(.addrWidth(10), .dataWidth(32), .Select("high")) SUBU ();  // open: addr, data
  ROM #(.addrWidth(10), .dataWidth(32), .Select("high")) XOR ();  // open: addr, data
  or or_3 (Conbranch, and_5_out, and_6_out, and_7_out);
  and and_7 (and_7_out, BLTZ, comparator_2_eq);
  Comparator #(.width(32), .mode("twosComplement")) comparator_2 (
    .a(32'h1), .b(mips_alu_1_result), .eq(comparator_2_eq));  // open: gt, lt
  or or_4 (BranchNop, JR, JMP, Conbranch);
  EX_MEM ex_mem_1 (
    .MemToReg_in(id_ex_1_memtoreg_out), .IR_in(id_ex_1_ir_out), .MemToReg_out(ex_mem_1_memtoreg_out),
    .IR_out(ex_mem_1_ir_out), .MemWrite_in(id_ex_1_memwrite_out), .MemWrite_out(MemWrite),
    .PC_in(id_ex_1_pc_out), .PC_out(ex_mem_1_pc_out), .RegWrite_in(EX_RegWrite), .RegWrite_out(MEM_RegWrite),
    .R2_in(id_ex_1_r2_out), .R2_out(ex_mem_1_r2_out), .JAL_in(id_ex_1_jal_out), .JAL_out(ex_mem_1_jal_out),
    .AluR_in(mips_alu_1_result), .AluR_out({ex_mem_1_alur_out, \字节选择 }), .RegDst_in(id_ex_1_regdst_out),
    .RegDst_out(ex_mem_1_regdst_out), .Halt_in(and_8_out), .Halt_out(ex_mem_1_halt_out),
    .Syscall_in(syscall), .Syscall_out(ex_mem_1_syscall_out), .LBU_in(id_ex_1_lbu_out), .LBU_out(LBU),
    .PCr_in(EX_PC), .W__in(EX_WriteReg_num), .PCr_out(MEM_PC), .W__out(MEM_WriteReg_num), .Reset(RST),
    .Enable(Halt), .CLK(CLK));  // open: Interrupt_in, Interrupt_out
  and and_8 (and_8_out, syscall, ~Equal);  // AND_Gate
  ROM #(.addrWidth(10), .dataWidth(32), .Select("high")) Benchmark_ccmb ();  // open: addr, data
  RAM #(.addrWidth(10), .dataWidth(32), .bus("separate"), .Select("high")) ram_1 (
    .addr(ex_mem_1_alur_out[11:2]), .din(ex_mem_1_r2_out), .data(ram_1_data), .str(MemWrite), .clk(CLK),
    .ld(not_1_out), .clr(RST));  // open: sel
  not not_1 (not_1_out, MemWrite);
  Multiplexer #(.select(2), .width(8), .disabled("Z"), .enable("false")) multiplexer_9 (
    .in0(ram_1_data[7:0]), .in1(ram_1_data[15:8]), .in2(ram_1_data[23:16]), .in3(ram_1_data[31:24]),
    .out(multiplexer_9_out), .sel(\字节选择 ));
  assign bit_extender_3_out = {{24{1'b0}}, multiplexer_9_out};  // Bit_Extender bit_extender_3
  MEM_WB mem_wb_1 (
    .MemToReg_in(ex_mem_1_memtoreg_out), .IR_in(ex_mem_1_ir_out), .MemToReg_out(MemToReg),
    .IR_out(mem_wb_1_ir_out), .RegWrite_in(MEM_RegWrite), .PC_in(ex_mem_1_pc_out), .RegWrite_out(RW),
    .PC_out(mem_wb_1_pc_out), .JAL_in(ex_mem_1_jal_out), .JAL_out(JAL), .MemD_in(multiplexer_10_out),
    .MemD_out(mem_wb_1_memd_out), .RegDst_in(ex_mem_1_regdst_out), .RegDst_out(RDst),
    .AluR_in({ex_mem_1_alur_out, \字节选择 }), .AluR_out(mem_wb_1_alur_out), .Syscall_in(ex_mem_1_syscall_out),
    .Syscall_out(Sys), .Halt_in(ex_mem_1_halt_out), .Halt_out(mem_wb_1_halt_out), .W__in(MEM_WriteReg_num),
    .PCr_in(MEM_PC), .PCr_out(WB_PC), .Reset(RST), .Enable(Halt), .CLK(CLK));  // open: W__out, Interrupt_in, Interrupt_out, R2_in, R2_out
  Multiplexer #(.select(1), .width(32), .disabled("Z"), .enable("false")) multiplexer_10 (
    .in0(ram_1_data), .in1(bit_extender_3_out), .out(multiplexer_10_out), .sel(LBU));
  not not_2 (not_2_out, mem_wb_1_halt_out);
  Multiplexer #(.select(1), .width(32), .disabled("Z"), .enable("false")) multiplexer_11 (
    .in0(mem_wb_1_alur_out), .in1(mem_wb_1_memd_out), .out(multiplexer_11_out), .sel(MemToReg));
  Multiplexer #(.select(1), .width(5), .disabled("Z"), .enable("false")) multiplexer_12 (
    .in0(mem_wb_1_ir_out[20:16]), .in1(mem_wb_1_ir_out[15:11]), .out(multiplexer_12_out), .sel(RDst));
  or or_5 (Halt, Go, RST, not_2_out);
  Multiplexer #(.select(1), .width(5), .disabled("Z"), .enable("false")) multiplexer_13 (
    .in0(multiplexer_12_out), .in1({5{1'b1}}), .out(multiplexer_13_out), .sel(JAL));
  Multiplexer #(.select(1), .width(32), .disabled("Z"), .enable("false")) multiplexer_14 (
    .in0(multiplexer_11_out), .in1(mem_wb_1_pc_out), .out(RDin), .sel(JAL));

  // Other names for the same wires on the sheet: R1[31:0] = a0; PC[31:0] = IF_PC

  // Notes on the sheet:
  //   中断源
  //   中断等待指示
  //   数码管输出
  //   contents of 指令存储器 (hex, n*v repeats v):
  //   20110001 8000c05 20110001 20120002 20130003 8000c09 20110001 20120002 20130003 8000c0d 20110001
  //   20120002 20130003 8000c11 20110001 20120002 20130003 c000cb8 20100001 20110001 118fc0 112020
  //   20020022 c 118882 12200001 8000c15 112020 20020022 c 20110001 118880 112020 20020022 c 12200001
  //   8000c1f 20110001 118fc0 112020 20020022 c 1188c3 112020 20020022 c 118903 112020 20020022 c 118903
  //   112020 20020022 c 118903 112020 20020022 c 118903 112020 20020022 c 118903 112020 20020022 c 118903
  //   112020 20020022 c 118903 112020 20020022 c 20100001 109fc0 139fc3 8021 2012000c 24160003 26100001
  //   3210000f 20080008 20090001 139900 2709825 132020 20020022 c 1094022 1500fff9 22100001 2018000f
  //   2188024 108700 20080008 20090001 139902 2709825 132021 20020022 c 1094022 1500fff9 108702 2c9b022
  //   12c00001 8000c50 4020 1084027 84400 3508ffff 82021 20020022 c 2010ffff 20110000 ae300000 22100001
  //   22310004 ae300000 22100001 22310004 ae300000 22100001 22310004 ae300000 22100001 22310004 ae300000
  //   22100001 22310004 ae300000 22100001 22310004 ae300000 22100001 22310004 ae300000 22100001 22310004
  //   ae300000 22100001 22310004 ae300000 22100001 22310004 ae300000 22100001 22310004 ae300000 22100001
  //   22310004 ae300000 22100001 22310004 ae300000 22100001 22310004 ae300000 22100001 22310004 ae300000
  //   22100001 22310004 22100001 8020 2011003c 8e130000 8e340000 274402a 11000002 ae330000 ae140000
  //   2231fffc 1611fff8 102020 20020022 c 22100004 2011003c 1611fff2 20020032 c 20100000 22100001 102020
  //   20020022 c 22100002 102020 20020022 c 22100003 102020 20020022 c 22100004 102020 20020022 c 22100005
  //   102020 20020022 c 22100006 102020 20020022 c 22100007 102020 20020022 c 22100008 102020 20020022
  //   20020022 c 3e00008
  //   指令字
  //   imm
  //   OP
  //   Func
  //   rs
  //   rt
  //   rd
  //   shamt
  //   JMP
  //   JR
  //   OP
  //   Func
  //   流水调试日志用
  //   Beq
  //   Bne
  //   MemToReg
  //   MemWrite
  //   AluOP
  //   AluSrcB
  //   RegWrite
  //   JAL
  //   RegDst
  //   Syscall
  //   contents of BLTZ (hex, n*v repeats v):
  //   2011fff1 112020 20020022 c 22310001 620fffb 2002000a c
  //   contents of LBU (hex, n*v repeats v):
  //   20090000 200b0010 34118483 20120404 118c00 129400 36318281 22520404 ad310000 2328820 21290004
  //   216bffff 1560fffb 200b0020 20090000 91310000 112020 20020022 c 21290001 216bffff 1560fff9 2002000a c
  //   contents of SUBU (hex, n*v repeats v):
  //   20080001 20110010 112020 20020022 c 200b0020 2288823 112020 20020022 c 216bffff 1560fffa 2002000a c
  //   contents of XOR (hex, n*v repeats v):
  //   2008ffff 20117777 112020 20020022 c 200b0010 2288826 112020 20020022 c 216bffff 1560fffa 2002000a c
  //   contents of Benchmark_ccmb (hex, n*v repeats v):
  //   20110001 8000c05 20110001 20120002 20130003 8000c09 20110001 20120002 20130003 8000c0d 20110001
  //   20120002 20130003 8000c11 20110001 20120002 20130003 c000cf6 20100001 20110001 118fc0 112020
  //   20020022 c 118882 12200001 8000c15 112020 20020022 c 20110001 118880 112020 20020022 c 12200001
  //   8000c1f 20110001 118fc0 112020 20020022 c 1188c3 112020 20020022 c 118903 112020 20020022 c 118903
  //   112020 20020022 c 118903 112020 20020022 c 118903 112020 20020022 c 118903 112020 20020022 c 118903
  //   112020 20020022 c 118903 112020 20020022 c 20100001 109fc0 139fc3 8021 2012000c 24160003 26100001
  //   3210000f 20080008 20090001 139900 2709825 132020 20020022 c 1094022 1500fff9 22100001 2018000f
  //   2188024 108700 20080008 20090001 139902 2709825 132021 20020022 c 1094022 1500fff9 108702 2c9b022
  //   12c00001 8000c50 4020 1084027 84400 3508ffff 82021 20020022 c 2010ffff 20110000 ae300000 22100001
  //   22310004 ae300000 22100001 22310004 ae300000 22100001 22310004 ae300000 22100001 22310004 ae300000
  //   22100001 22310004 ae300000 22100001 22310004 ae300000 22100001 22310004 ae300000 22100001 22310004
  //   ae300000 22100001 22310004 ae300000 22100001 22310004 ae300000 22100001 22310004 ae300000 22100001
  //   22310004 ae300000 22100001 22310004 ae300000 22100001 22310004 ae300000 22100001 22310004 ae300000
  //   22100001 22310004 22100001 8020 2011003c 8e130000 8e340000 274402a 11000002 ae330000 ae140000
  //   2231fffc 1611fff8 102020 20020022 c 22100004 2011003c 1611fff2 20020032 c 20080001 20110010 112020
  //   20020022 c 200b0020 2288823 112020 20020022 c 216bffff 1560fffa 2002000a c 2008ffff 20117777 112020
  //   20020022 c 200b0010 2288826 112020 20020022 c 216bffff 1560fffa 2002000a c 20090000 200b0010
  //   34118483 20120404 118c00 129400 36318281 22520404 ad310000 2328820 21290004 216bffff 1560fffb
  //   200b0020 20090000 91310000 112020 20020022 c 21290001 216bffff 1560fff9 2002000a c 2011fff1 112020
  //   20020022 c 22310001 620fffb 2002000a c 2002000a c 20100000 22100001 102020 20020022 c 22100002
  //   102020 20020022 c 22100003 102020 20020022 c 22100004 102020 20020022 c 22100005 102020 20020022 c
  //   22100006 102020 20020022 c 22100007 102020 20020022 c 22100008 102020 20020022 20020022 c 3e00008
  //   rt
  //   rd
  //   W#
endmodule

module \重定向流水线  (
);

  wire and_1_out, and_2_out, and_3_out, and_4_out, and_5_out, and_6_out, and_7_out, and_8_out, BLTZ,
       BranchNop, CLK, comparator_2_eq, Conbranch, Equal, ex_mem_1_halt_out, ex_mem_1_jal_out,
       ex_mem_1_memtoreg_out, ex_mem_1_regdst_out, ex_mem_1_syscall_out, EX_RegWrite, Go, Halt,
       id_ex_1_alusrcb_out, id_ex_1_beq_out, id_ex_1_bne_out, id_ex_1_jal_out, id_ex_1_lbu_out,
       id_ex_1_memtoreg_out, id_ex_1_memwrite_out, id_ex_1_regdst_out, ID_JAL, ID_RDst, IR1, IR2, IR3, JAL,
       JMP, JR, LBU, Loaduse, MEM_RegWrite, mem_wb_1_halt_out, MemToReg, MemWrite, mips_alu_1_equal,
       not_1_out, or_1_out, or_2_out, RDst, RST, SignedExt, Sys, syscall, W1, W2, W3, WB_RegWrite,
       \单周期硬布线控制器_1_alu_src , \单周期硬布线控制器_1_beq , \单周期硬布线控制器_1_bltz , \单周期硬布线控制器_1_bne , \单周期硬布线控制器_1_jmp ,
       \单周期硬布线控制器_1_jr , \单周期硬布线控制器_1_lbu , \单周期硬布线控制器_1_memtoreg , \单周期硬布线控制器_1_memwrite ,
       \单周期硬布线控制器_1_regwrite , \单周期硬布线控制器_1_syscall , \数据相关 ;
  wire [1:0] R1_Forward, R2_Forward, \数据相关检测_1_r1_forward , \数据相关检测_1_r2_forward ;
  wire [3:0] id_ex_1_aluop_out, \单周期硬布线控制器_1_alu_op ;
  wire [4:0] EX_WriteReg_num, id_ex_1_shamt_out, ID_R1_num, ID_R2_num, MEM_WriteReg_num, multiplexer_2_out,
       multiplexer_4_out, multiplexer_14_out, multiplexer_15_out;
  wire [5:0] EX_Func, EX_OP, Func, MEM_OP, OP;
  wire [7:0] multiplexer_11_out;
  wire [15:0] adder_1_out, \LoadUse次数 , multiplier_1_out, \总周期数 , \插入气泡数 , \无条件分支数 , \条件分支成功数 ;
  wire [25:0] ex_mem_1_ir_out;
  wire [25:6] id_ex_1_ir_out, if_id_1_ir_out;
  wire [31:0] a0, adder_3_out, adder_4_out, Benchmark_ccmb_data, bit_extender_1_out, bit_extender_2_out,
       bit_extender_3_out, ex_mem_1_pc_out, ex_mem_1_r2_out, EX_PC, id_ex_1_address_out, id_ex_1_imm_out,
       id_ex_1_pc_out, id_ex_1_r1_out, id_ex_1_r2_out, ID_PC, if_id_1_pc_out, IF_PC, LedData, MEM_Alu,
       MEM_PC, mem_wb_1_ir_out, mem_wb_1_pc_out, mips_alu_1_result, mips_ram_1_p6, mips_regifile_1_r1,
       mips_regifile_1_r2, multiplexer_1_out, multiplexer_5_out, multiplexer_8_out, multiplexer_9_out,
       multiplexer_10_out, multiplexer_12_out, multiplexer_13_out, RDin, shifter_1_out, WB_Alu, WB_MD, WB_PC;

  Button \u_总复位  (.out(RST));
  Button _1 (.out(IR1));
  Button _2 (.out(IR2));
  Button _3 (.out(IR3));
  Button \u_继续运行  (.out(Go));
  LED #(.active("true")) led_1 (.in(W1));
  LED #(.active("true")) led_2 (.in(W2));
  LED #(.active("true")) led_3 (.in(W3));
  Counter #(.width(16), .max('hffff), .ongoal("wrap"), .trigger("rising"), .behavior("old")) counter_1 (
    .count(JMP), .Q(\无条件分支数 ), .clk(CLK), .clr(RST));  // open: load, D, carry, preset
  Counter #(.width(16), .max('hffff), .ongoal("wrap"), .trigger("rising"), .behavior("old")) counter_2 (
    .count(Halt), .Q(\总周期数 ), .clk(CLK), .clr(RST));  // open: load, D, carry, preset
  Hex_Digit_Display hex_digit_display_1 (.value(LedData[31:28]));  // open: dp
  Adder #(.width(16)) adder_1 (.a(\无条件分支数 ), .b(\条件分支成功数 ), .out(adder_1_out));  // open: cin, cout
  Multiplexer #(.select(3), .width(32), .disabled("Z"), .enable("false")) multiplexer_1 (
    .in0(adder_3_out), .in1({32{1'b0}}), .in2(id_ex_1_address_out), .in3(a0), .in4(adder_4_out),
    .in5({32{1'b0}}), .in6({32{1'b0}}), .in7({32{1'b0}}), .out(multiplexer_1_out), .sel({Conbranch, JMP, JR}));
  and and_1 (and_1_out, Halt, ~Loaduse);  // AND_Gate
  Hex_Digit_Display hex_digit_display_2 (.value(LedData[23:20]));  // open: dp
  Hex_Digit_Display hex_digit_display_3 (.value(LedData[27:24]));  // open: dp
  and and_2 (and_2_out, Equal, syscall);
  Multiplier #(.width(16)) multiplier_1 (.a(adder_1_out), .b(16'h2), .out(multiplier_1_out));  // open: cin, cout
  Register #(.width(32), .trigger("rising"), .Select("low")) PC (
    .D(multiplexer_1_out), .en(and_1_out), .Q(IF_PC), .clk(CLK), .clr(RST));
  Hex_Digit_Display hex_digit_display_4 (.value(LedData[19:16]));  // open: dp
  Hex_Digit_Display hex_digit_display_5 (.value(LedData[15:12]));  // open: dp
  Counter #(.width(16), .max('hffff), .ongoal("wrap"), .trigger("rising"), .behavior("old")) counter_3 (
    .count(Conbranch), .Q(\条件分支成功数 ), .clk(CLK), .clr(RST));  // open: load, D, carry, preset
  Register #(.width(32), .trigger("rising"), .Select("low")) register_1 (
    .D(a0), .en(and_2_out), .Q(LedData), .clk(CLK), .clr(RST));
  Adder #(.width(16)) adder_2 (.a(multiplier_1_out), .b(\LoadUse次数 ), .out(\插入气泡数 ));  // open: cin, cout
  Adder #(.width(32)) adder_3 (.a(IF_PC), .b(32'h4), .out(adder_3_out));  // open: cin, cout
  Hex_Digit_Display hex_digit_display_6 (.value(LedData[7:4]));  // open: dp
  Hex_Digit_Display hex_digit_display_7 (.value(LedData[11:8]));  // open: dp
  Clock #(.highDuration(1), .lowDuration(1)) clock_1 (.out(CLK));
  ROM #(.addrWidth(10), .dataWidth(32), .Select("high")) Benchmark_ccmb (
    .addr(IF_PC[11:2]), .data(Benchmark_ccmb_data));
  Hex_Digit_Display hex_digit_display_8 (.value(LedData[3:0]));  // open: dp
  or or_1 (or_1_out, RST, BranchNop);
  IF_ID if_id_1 (
    .PCr_in(IF_PC), .PC_in(adder_3_out), .IR_in(Benchmark_ccmb_data), .PCr_out(ID_PC),
    .PC_out(if_id_1_pc_out), .IR_out({OP, if_id_1_ir_out, Func}), .Reset(or_1_out), .CLK(CLK),
    .Enable(and_3_out));  // open: PC_G_in, HG_in, PC_G_out, HG_out
  and and_3 (and_3_out, ~Loaduse, Halt);  // AND_Gate
  // Probe on {OP, if_id_1_ir_out, Func}
  // Probe on \总周期数 
  // Probe on \无条件分支数 
  // Probe on \条件分支成功数 
  // Probe on \插入气泡数 
  // Probe on \LoadUse次数 
  // Probe on IF_PC[11:0]
  // Probe on if_id_1_ir_out[20:16]
  Multiplexer #(.select(1), .width(5), .disabled("Z"), .enable("false")) multiplexer_2 (
    .in0(if_id_1_ir_out[20:16]), .in1(if_id_1_ir_out[15:11]), .out(multiplexer_2_out), .sel(ID_RDst));
  // Probe on ID_PC[11:0]
  // Probe on EX_PC[11:0]
  \数据相关检测  \u_数据相关检测_1  (
    .ID_OP(OP), .ID_FUNC(Func), .ID_R1_num(ID_R1_num), .ID_R2_num(ID_R2_num),
    .EX_WriteReg_num(EX_WriteReg_num), .MEM_WriteReg_num(MEM_WriteReg_num), .EX_RegWrite(EX_RegWrite),
    .MEM_RegWrite(MEM_RegWrite), .EX_OP(EX_OP), .\数据相关 (\数据相关 ), .\Load_Use相关 (Loaduse),
    .R1_Forward(\数据相关检测_1_r1_forward ), .R2_Forward(\数据相关检测_1_r2_forward ), .MEM_OP(MEM_OP));
  \单周期硬布线控制器  \u_单周期硬布线控制器_1  (
    .Func(Func), .OP(OP), .ALU_OP(\单周期硬布线控制器_1_alu_op ), .MemToReg(\单周期硬布线控制器_1_memtoreg ),
    .MemWrite(\单周期硬布线控制器_1_memwrite ), .ALU_SRC(\单周期硬布线控制器_1_alu_src ), .RegWrite(\单周期硬布线控制器_1_regwrite ),
    .SysCALL(\单周期硬布线控制器_1_syscall ), .SignedExt(SignedExt), .RegDst(ID_RDst), .JR(\单周期硬布线控制器_1_jr ),
    .JMP(\单周期硬布线控制器_1_jmp ), .Beq(\单周期硬布线控制器_1_beq ), .JAL(ID_JAL), .Bne(\单周期硬布线控制器_1_bne ),
    .LBU(\单周期硬布线控制器_1_lbu ), .BLTZ(\单周期硬布线控制器_1_bltz ));  // open: MFC0, MTC0, MF, ERET
  // Probe on if_id_1_ir_out[25:21]
  Multiplexer #(.select(1), .width(5), .disabled("Z"), .enable("false")) multiplexer_3 (
    .in0(if_id_1_ir_out[25:21]), .in1(5'b00100), .out(ID_R1_num), .sel(\单周期硬布线控制器_1_syscall ));
  Multiplexer #(.select(1), .width(5), .disabled("Z"), .enable("false")) multiplexer_4 (
    .in0(multiplexer_2_out), .in1({5{1'b1}}), .out(multiplexer_4_out), .sel(ID_JAL));
  assign bit_extender_1_out = {{16{1'b0}}, {if_id_1_ir_out[15:6], Func}};  // Bit_Extender bit_extender_1
  Multiplexer #(.select(1), .width(32), .disabled("Z"), .enable("false")) multiplexer_5 (
    .in0(bit_extender_1_out), .in1(bit_extender_2_out), .out(multiplexer_5_out), .sel(SignedExt));
  assign bit_extender_2_out = {{16{if_id_1_ir_out[15]}}, {if_id_1_ir_out[15:6], Func}};  // Bit_Extender bit_extender_2
  // Probe on MEM_PC[11:0]
  Register #(.width(4), .trigger("rising"), .Select("low")) register_2 (
    .D({\数据相关检测_1_r2_forward , \数据相关检测_1_r1_forward }), .Q({R2_Forward, R1_Forward}), .clk(CLK), .clr(RST));  // open: en
  Multiplexer #(.select(1), .width(5), .disabled("Z"), .enable("false")) multiplexer_6 (
    .in0(if_id_1_ir_out[20:16]), .in1(5'b00010), .out(ID_R2_num), .sel(\单周期硬布线控制器_1_syscall ));
  // Probe on WB_PC[11:0]
  and and_4 (and_4_out, Halt, Loaduse);
  Counter #(.width(16), .max('hffff), .ongoal("wrap"), .trigger("rising"), .behavior("old")) counter_4 (
    .count(and_4_out), .Q(\LoadUse次数 ), .clk(CLK), .clr(RST));  // open: load, D, carry, preset
  MIPS_Regifile mips_regifile_1 (
    .Din(RDin), .Clk(CLK), .R1(mips_regifile_1_r1), .R2(mips_regifile_1_r2), .WE(WB_RegWrite),
    .W_num(multiplexer_15_out), .R1_num(ID_R1_num), .R2_num(ID_R2_num));
  or or_2 (or_2_out, RST, Loaduse, BranchNop);
  ID_EX id_ex_1 (
    .BEQ_in(\单周期硬布线控制器_1_beq ), .BEQ_out(id_ex_1_beq_out), .IR_in({OP, if_id_1_ir_out, Func}),
    .IR_out({EX_OP, id_ex_1_ir_out, EX_Func}), .BNE_in(\单周期硬布线控制器_1_bne ), .BNE_out(id_ex_1_bne_out),
    .PC_in(if_id_1_pc_out), .PC_out(id_ex_1_pc_out), .MemToReg_in(\单周期硬布线控制器_1_memtoreg ),
    .MemToReg_out(id_ex_1_memtoreg_out), .R1_in(mips_regifile_1_r1), .R1_out(id_ex_1_r1_out),
    .MemWrite_in(\单周期硬布线控制器_1_memwrite ), .MemWrite_out(id_ex_1_memwrite_out), .R2_in(mips_regifile_1_r2),
    .AluSrcB_in(\单周期硬布线控制器_1_alu_src ), .R2_out(id_ex_1_r2_out), .AluSrcB_out(id_ex_1_alusrcb_out),
    .RegWrite_in(\单周期硬布线控制器_1_regwrite ), .Imm_in(multiplexer_5_out), .RegWrite_out(EX_RegWrite),
    .Imm_out(id_ex_1_imm_out), .JAL_in(ID_JAL), .JAL_out(id_ex_1_jal_out),
    .Address_in({if_id_1_pc_out[31:28], if_id_1_ir_out, Func, 2'b00}), .Address_out(id_ex_1_address_out),
    .RegDst_in(ID_RDst), .RegDst_out(id_ex_1_regdst_out), .AluOP_in(\单周期硬布线控制器_1_alu_op ),
    .AluOP_out(id_ex_1_aluop_out), .Syscall_in(\单周期硬布线控制器_1_syscall ), .Syscall_out(syscall),
    .Shamt_in(if_id_1_ir_out[10:6]), .Shamt_out(id_ex_1_shamt_out), .JMP_in(\单周期硬布线控制器_1_jmp ),
    .JMP_out(JMP), .JR_in(\单周期硬布线控制器_1_jr ), .LBU_in(\单周期硬布线控制器_1_lbu ), .JR_out(JR),
    .LBU_out(id_ex_1_lbu_out), .BLTZ_in(\单周期硬布线控制器_1_bltz ), .BLTZ_out(BLTZ), .W__in(multiplexer_4_out),
    .W__out(EX_WriteReg_num), .PCr_in(ID_PC), .PCr_out(EX_PC), .Reset(or_2_out), .Enable(Halt), .CLK(CLK));  // open: Halt_in, Halt_out, HG_in, HG_out, PCG_in, PCG_out, Interrupt_in, Interrupt_out
  ROM #(.addrWidth(10), .dataWidth(32), .Select("high")) u_BLTZ ();  // open: addr, data
  ROM #(.addrWidth(10), .dataWidth(32), .Select("high")) u_LBU ();  // open: addr, data
  Shifter #(.width(32), .shift("ll")) shifter_1 (.in(id_ex_1_imm_out), .\dist (5'b00010), .out(shifter_1_out));
  Multiplexer #(.select(2), .width(32), .disabled("Z"), .enable("false")) multiplexer_7 (
    .in0(id_ex_1_r1_out), .in1(WB_Alu), .in2(WB_MD), .in3(MEM_Alu), .out(a0), .sel(R1_Forward));
  Multiplexer #(.select(2), .width(32), .disabled("Z"), .enable("false")) multiplexer_8 (
    .in0(id_ex_1_r2_out), .in1(WB_Alu), .in2(WB_MD), .in3(MEM_Alu), .out(multiplexer_8_out), .sel(R2_Forward));
  Adder #(.width(32)) adder_4 (.a(id_ex_1_pc_out), .b(shifter_1_out), .out(adder_4_out));  // open: cin, cout
  Multiplexer #(.select(1), .width(32), .disabled("Z"), .enable("false")) multiplexer_9 (
    .in0(multiplexer_8_out), .in1(id_ex_1_imm_out), .out(multiplexer_9_out), .sel(id_ex_1_alusrcb_out));
  // Probe on {EX_OP, id_ex_1_ir_out, EX_Func}
  ROM #(.addrWidth(10), .dataWidth(32), .Select("high")) SUBU ();  // open: addr, data
  ROM #(.addrWidth(10), .dataWidth(32), .Select("high")) XOR ();  // open: addr, data
  Multiplexer #(.select(1), .width(32), .disabled("Z"), .enable("false")) multiplexer_10 (
    .in0(multiplexer_9_out), .in1({32{1'b0}}), .out(multiplexer_10_out), .sel(BLTZ));
  // Probe on id_ex_1_aluop_out
  Comparator #(.width(32), .mode("unsigned")) comparator_1 (
    .a(32'h22), .b(multiplexer_10_out), .eq(Equal));  // open: gt, lt
  ROM #(.addrWidth(10), .dataWidth(32), .Select("high")) Benchmark_test ();  // open: addr, data
  and and_5 (and_5_out, id_ex_1_beq_out, mips_alu_1_equal);
  and and_6 (and_6_out, id_ex_1_bne_out, ~mips_alu_1_equal);  // AND_Gate
  MIPS_ALU mips_alu_1 (
    .X(a0), .Y(multiplexer_10_out), .AluOP(id_ex_1_aluop_out), .Equal(mips_alu_1_equal),
    .Result(mips_alu_1_result), .shamt(id_ex_1_shamt_out));  // open: Result_2
  or or_3 (Conbranch, and_5_out, and_6_out, and_7_out);
  and and_7 (and_7_out, BLTZ, comparator_2_eq);
  Comparator #(.width(32), .mode("twosComplement")) comparator_2 (
    .a(32'h1), .b(mips_alu_1_result), .eq(comparator_2_eq));  // open: gt, lt
  // Probe on mips_alu_1_result
  or or_4 (BranchNop, JR, JMP, Conbranch);
  EX_MEM ex_mem_1 (
    .MemToReg_in(id_ex_1_memtoreg_out), .IR_in({EX_OP, id_ex_1_ir_out, EX_Func}),
    .MemToReg_out(ex_mem_1_memtoreg_out), .IR_out({MEM_OP, ex_mem_1_ir_out}),
    .MemWrite_in(id_ex_1_memwrite_out), .MemWrite_out(MemWrite), .PC_in(id_ex_1_pc_out),
    .PC_out(ex_mem_1_pc_out), .RegWrite_in(EX_RegWrite), .RegWrite_out(MEM_RegWrite),
    .R2_in(multiplexer_8_out), .R2_out(ex_mem_1_r2_out), .JAL_in(id_ex_1_jal_out),
    .JAL_out(ex_mem_1_jal_out), .AluR_in(mips_alu_1_result), .AluR_out(MEM_Alu),
    .RegDst_in(id_ex_1_regdst_out), .RegDst_out(ex_mem_1_regdst_out), .Halt_in(and_8_out),
    .Halt_out(ex_mem_1_halt_out), .Syscall_in(syscall), .Syscall_out(ex_mem_1_syscall_out),
    .LBU_in(id_ex_1_lbu_out), .LBU_out(LBU), .PCr_in(EX_PC), .W__in(EX_WriteReg_num), .PCr_out(MEM_PC),
    .W__out(MEM_WriteReg_num), .Reset(RST), .Enable(Halt), .CLK(CLK));  // open: Interrupt_in, Interrupt_out
  and and_8 (and_8_out, syscall, ~Equal);  // AND_Gate
  // Probe on MEM_Alu
  // Probe on R1_Forward
  // Probe on {MEM_OP, ex_mem_1_ir_out}
  // MIPS_RAM mips_ram_1: pin names not known; wires that end beside it: MEM_Alu[11:2], ex_mem_1_r2_out, MemWrite, CLK, RST, mips_ram_1_p6
  Multiplexer #(.select(2), .width(8), .disabled("Z"), .enable("false")) multiplexer_11 (
    .in0(mips_ram_1_p6[7:0]), .in1(mips_ram_1_p6[15:8]), .in2(mips_ram_1_p6[23:16]),
    .in3(mips_ram_1_p6[31:24]), .out(multiplexer_11_out), .sel(MEM_Alu[1:0]));
  assign bit_extender_3_out = {{24{1'b0}}, multiplexer_11_out};  // Bit_Extender bit_extender_3
  MEM_WB mem_wb_1 (
    .MemToReg_in(ex_mem_1_memtoreg_out), .IR_in({MEM_OP, ex_mem_1_ir_out}), .MemToReg_out(MemToReg),
    .IR_out(mem_wb_1_ir_out), .RegWrite_in(MEM_RegWrite), .PC_in(ex_mem_1_pc_out),
    .RegWrite_out(WB_RegWrite), .PC_out(mem_wb_1_pc_out), .JAL_in(ex_mem_1_jal_out), .JAL_out(JAL),
    .MemD_in(multiplexer_12_out), .MemD_out(WB_MD), .RegDst_in(ex_mem_1_regdst_out), .RegDst_out(RDst),
    .AluR_in(MEM_Alu), .AluR_out(WB_Alu), .Syscall_in(ex_mem_1_syscall_out), .Syscall_out(Sys),
    .Halt_in(ex_mem_1_halt_out), .Halt_out(mem_wb_1_halt_out), .W__in(MEM_WriteReg_num), .PCr_in(MEM_PC),
    .PCr_out(WB_PC), .Reset(RST), .Enable(Halt), .CLK(CLK));  // open: W__out, Interrupt_in, Interrupt_out, R2_in, R2_out
  Multiplexer #(.select(1), .width(32), .disabled("Z"), .enable("false")) multiplexer_12 (
    .in0(mips_ram_1_p6), .in1(bit_extender_3_out), .out(multiplexer_12_out), .sel(LBU));
  not not_1 (not_1_out, mem_wb_1_halt_out);
  Multiplexer #(.select(1), .width(32), .disabled("Z"), .enable("false")) multiplexer_13 (
    .in0(WB_Alu), .in1(WB_MD), .out(multiplexer_13_out), .sel(MemToReg));
  Multiplexer #(.select(1), .width(5), .disabled("Z"), .enable("false")) multiplexer_14 (
    .in0(mem_wb_1_ir_out[20:16]), .in1(mem_wb_1_ir_out[15:11]), .out(multiplexer_14_out), .sel(RDst));
  Multiplexer #(.select(1), .width(5), .disabled("Z"), .enable("false")) multiplexer_15 (
    .in0(multiplexer_14_out), .in1({5{1'b1}}), .out(multiplexer_15_out), .sel(JAL));
  or or_5 (Halt, Go, RST, not_1_out);
  Multiplexer #(.select(1), .width(32), .disabled("Z"), .enable("false")) multiplexer_16 (
    .in0(multiplexer_13_out), .in1(mem_wb_1_pc_out), .out(RDin), .sel(JAL));

  // Other names for the same wires on the sheet: R1[31:0] = a0; 字节选择[1:0] = MEM_Alu[1:0]; PC[31:0] = IF_PC

  // Notes on the sheet:
  //   中断源
  //   中断等待指示
  //   数码管输出
  //   contents of Benchmark_ccmb (hex, n*v repeats v):
  //   20110001 8000c05 20110001 20120002 20130003 8000c09 20110001 20120002 20130003 8000c0d 20110001
  //   20120002 20130003 8000c11 20110001 20120002 20130003 c000cf6 20100001 20110001 118fc0 112020
  //   20020022 c 118882 12200001 8000c15 112020 20020022 c 20110001 118880 112020 20020022 c 12200001
  //   8000c1f 20110001 118fc0 112020 20020022 c 1188c3 112020 20020022 c 118903 112020 20020022 c 118903
  //   112020 20020022 c 118903 112020 20020022 c 118903 112020 20020022 c 118903 112020 20020022 c 118903
  //   112020 20020022 c 118903 112020 20020022 c 20100001 109fc0 139fc3 8021 2012000c 24160003 26100001
  //   3210000f 20080008 20090001 139900 2709825 132020 20020022 c 1094022 1500fff9 22100001 2018000f
  //   2188024 108700 20080008 20090001 139902 2709825 132021 20020022 c 1094022 1500fff9 108702 2c9b022
  //   12c00001 8000c50 4020 1084027 84400 3508ffff 82021 20020022 c 2010ffff 20110000 ae300000 22100001
  //   22310004 ae300000 22100001 22310004 ae300000 22100001 22310004 ae300000 22100001 22310004 ae300000
  //   22100001 22310004 ae300000 22100001 22310004 ae300000 22100001 22310004 ae300000 22100001 22310004
  //   ae300000 22100001 22310004 ae300000 22100001 22310004 ae300000 22100001 22310004 ae300000 22100001
  //   22310004 ae300000 22100001 22310004 ae300000 22100001 22310004 ae300000 22100001 22310004 ae300000
  //   22100001 22310004 22100001 8020 2011003c 8e130000 8e340000 274402a 11000002 ae330000 ae140000
  //   2231fffc 1611fff8 102020 20020022 c 22100004 2011003c 1611fff2 20020032 c 20080001 20110010 112020
  //   20020022 c 200b0020 2288823 112020 20020022 c 216bffff 1560fffa 2002000a c 2008ffff 20117777 112020
  //   20020022 c 200b0010 2288826 112020 20020022 c 216bffff 1560fffa 2002000a c 20090000 200b0010
  //   34118483 20120404 118c00 129400 36318281 22520404 ad310000 2328820 21290004 216bffff 1560fffb
  //   200b0020 20090000 91310000 112020 20020022 c 21290001 216bffff 1560fff9 2002000a c 2011fff1 112020
  //   20020022 c 22310001 620fffb 2002000a c 2002000a c 20100000 22100001 102020 20020022 c 22100002
  //   102020 20020022 c 22100003 102020 20020022 c 22100004 102020 20020022 c 22100005 102020 20020022 c
  //   22100006 102020 20020022 c 22100007 102020 20020022 c 22100008 102020 20020022 20020022 c 3e00008
  //   指令字
  //   imm
  //   OP
  //   Func
  //   rs
  //   rt
  //   rd
  //   shamt
  //   JMP
  //   JR
  //   OP
  //   Func
  //   流水调试日志用
  //   Beq
  //   Bne
  //   MemToReg
  //   MemWrite
  //   AluOP
  //   AluSrcB
  //   RegWrite
  //   JAL
  //   RegDst
  //   Syscall
  //   contents of BLTZ (hex, n*v repeats v):
  //   2011fff1 112020 20020022 c 22310001 620fffb 2002000a c
  //   contents of LBU (hex, n*v repeats v):
  //   20090000 200b0010 34118483 20120404 118c00 129400 36318281 22520404 ad310000 2328820 21290004
  //   216bffff 1560fffb 200b0020 20090000 91310000 112020 20020022 c 21290001 216bffff 1560fff9 2002000a c
  //   contents of SUBU (hex, n*v repeats v):
  //   20080001 20110010 112020 20020022 c 200b0020 2288823 112020 20020022 c 216bffff 1560fffa 2002000a c
  //   contents of XOR (hex, n*v repeats v):
  //   2008ffff 20117777 112020 20020022 c 200b0010 2288826 112020 20020022 c 216bffff 1560fffa 2002000a c
  //   contents of Benchmark_test (hex, n*v repeats v):
  //   20110001 8000c05 20110001 20120002 20130003 8000c09 20110001 20120002 20130003 8000c0d 20110001
  //   20120002 20130003 8000c11 20110001 20120002 20130003 c000cb8 20100001 20110001 118fc0 112020
  //   20020022 c 118882 12200001 8000c15 112020 20020022 c 20110001 118880 112020 20020022 c 12200001
  //   8000c1f 20110001 118fc0 112020 20020022 c 1188c3 112020 20020022 c 118903 112020 20020022 c 118903
  //   112020 20020022 c 118903 112020 20020022 c 118903 112020 20020022 c 118903 112020 20020022 c 118903
  //   112020 20020022 c 118903 112020 20020022 c 20100001 109fc0 139fc3 8021 2012000c 24160003 26100001
  //   3210000f 20080008 20090001 139900 2709825 132020 20020022 c 1094022 1500fff9 22100001 2018000f
  //   2188024 108700 20080008 20090001 139902 2709825 132021 20020022 c 1094022 1500fff9 108702 2c9b022
  //   12c00001 8000c50 4020 1084027 84400 3508ffff 82021 20020022 c 2010ffff 20110000 ae300000 22100001
  //   22310004 ae300000 22100001 22310004 ae300000 22100001 22310004 ae300000 22100001 22310004 ae300000
  //   22100001 22310004 ae300000 22100001 22310004 ae300000 22100001 22310004 ae300000 22100001 22310004
  //   ae300000 22100001 22310004 ae300000 22100001 22310004 ae300000 22100001 22310004 ae300000 22100001
  //   22310004 ae300000 22100001 22310004 ae300000 22100001 22310004 ae300000 22100001 22310004 ae300000
  //   22100001 22310004 22100001 8020 2011003c 8e130000 8e340000 274402a 11000002 ae330000 ae140000
  //   2231fffc 1611fff8 102020 20020022 c 22100004 2011003c 1611fff2 20020032 c 20100000 22100001 102020
  //   20020022 c 22100002 102020 20020022 c 22100003 102020 20020022 c 22100004 102020 20020022 c 22100005
  //   102020 20020022 c 22100006 102020 20020022 c 22100007 102020 20020022 c 22100008 102020 20020022
  //   20020022 c 3e00008
  //   rt
  //   rd
  //   W#
endmodule

module \中断按键参考电路  (
  input  \同步清零信号 ,
  output \与中断屏蔽位与 
);

  wire \_1号中断_out , and_1_out, clock_1_out, d_ff_1_q, or_1_out, or_2_out;

  Clock #(.highDuration(1), .lowDuration(1)) clock_1 (.out(clock_1_out));
  Button \_1号中断  (.out(\_1号中断_out ));
  or or_1 (or_1_out, \与中断屏蔽位与 , d_ff_1_q);
  LED #(.active("true")) \_1号中断等待指示灯  (.in(or_1_out));
  D_Flip_Flop #(.trigger("rising"), .Pre_Clr_Positions("LEGACY"), .NegatePresetClear("false"), .enable("true"), .NewFFLayout("false")) d_ff_1 (
    .clk(\_1号中断_out ), .D(1'b1), .Q(d_ff_1_q), .reset(\与中断屏蔽位与 ));  // open: Qn, preset, en
  or or_2 (or_2_out, d_ff_1_q, \与中断屏蔽位与 );
  and and_1 (and_1_out, or_2_out, ~\同步清零信号 );  // AND_Gate
  D_Flip_Flop #(.trigger("rising"), .Pre_Clr_Positions("LEGACY"), .NegatePresetClear("false"), .enable("true"), .NewFFLayout("false")) IR1 (
    .clk(clock_1_out), .D(and_1_out), .Q(\与中断屏蔽位与 ));  // open: Qn, preset, en, reset

  // Notes on the sheet:
  //   中断信号采样参考电路
  //   Reset 
endmodule
module \单级中断  (
  output RegWrite,
  output MemWrite,
  output [31:0] PC,
  output [31:0] IR,
  output [31:0] RDin,
  output [31:0] MDin
);

  wire AluSrcB, and_1_out, and_2_out, and_3_out, and_4_out, and_5_out, and_6_out, and_7_out, and_8_out,
       and_9_out, and_10_out, and_11_out, and_12_out, and_13_out, BLTZ, CLK, comparator_1_eq,
       comparator_2_eq, d_ff_1_q, d_ff_2_q, d_ff_3_q, ERET, Go, IR1, IR1_q, IR2, IR2_q, IR3, IR3_q, JAL, LBU,
       MemToReg, mips_alu_1_equal, multiplexer_5_out, not_1_out, not_2_out, or_4_out, or_5_out, or_6_out,
       or_7_out, priority_encoder_1_gs, RST, SignedExt, stop, Syscall, W1, W2, W3, \中断状态_q ,
       \单周期硬布线控制器_1_beq , \单周期硬布线控制器_1_bne , \单周期硬布线控制器_1_regdst ;
  wire [1:0] IR_now, priority_encoder_1_out;
  wire [2:0] \单周期硬布线控制器_1_jr ;
  wire [3:0] adder_1_out_2, \单周期硬布线控制器_1_alu_op ;
  wire [4:0] multiplexer_2_out, multiplexer_3_out, multiplexer_6_out, multiplexer_7_out;
  wire [7:0] multiplexer_17_out;
  wire [15:0] \总周期数 , \无条件分支数 , \条件分支成功数 ;
  wire [27:0] adder_1_out;
  wire [31:0] a0, adder_2_out, bit_extender_1_out, bit_extender_2_out, bit_extender_3_out, EPC_q, LedData,
       mips_alu_1_result, multiplexer_8_out, multiplexer_9_out, multiplexer_10_out, multiplexer_12_out,
       multiplexer_13_out, multiplexer_14_out, multiplexer_16_out, multiplexer_18_out, nextPC, PCout,
       ram_1_data, shifter_1_out;

  Clock #(.highDuration(1), .lowDuration(1)) clock_1 (.out(CLK));
  Button \u_继续运行  (.out(Go));
  Button \u_总复位  (.out(RST));
  Button _1 (.out(IR1));
  Button _2 (.out(IR2));
  Button _3 (.out(IR3));
  // Probe on IR_now
  or or_1 (W1, IR1_q, d_ff_1_q);
  or or_2 (W2, IR2_q, d_ff_2_q);
  or or_3 (W3, IR3_q, d_ff_3_q);
  LED #(.active("true")) led_1 (.in(W1));
  LED #(.active("true")) led_2 (.in(W2));
  LED #(.active("true")) led_3 (.in(W3));
  Multiplexer #(.select(3), .width(32), .disabled("Z"), .enable("false")) multiplexer_1 (
    .in0({adder_1_out_2, adder_1_out}), .in1({32{1'b0}}), .in2({adder_1_out_2, IR[25:0], 2'b00}), .in3(a0),
    .in4(adder_2_out), .in5({32{1'b0}}), .in6({32{1'b0}}), .in7({32{1'b0}}), .out(nextPC),
    .sel(\单周期硬布线控制器_1_jr ));
  D_Flip_Flop #(.trigger("rising"), .Pre_Clr_Positions("LEGACY"), .NegatePresetClear("false"), .enable("true"), .NewFFLayout("false")) d_ff_1 (
    .clk(IR1), .D(1'b1), .Q(d_ff_1_q), .reset(IR1_q));  // open: Qn, preset, en
  D_Flip_Flop #(.trigger("rising"), .Pre_Clr_Positions("LEGACY"), .NegatePresetClear("false"), .enable("true"), .NewFFLayout("false")) d_ff_2 (
    .clk(IR2), .D(1'b1), .Q(d_ff_2_q), .reset(IR2_q));  // open: Qn, preset, en
  D_Flip_Flop #(.trigger("rising"), .Pre_Clr_Positions("LEGACY"), .NegatePresetClear("false"), .enable("true"), .NewFFLayout("false")) d_ff_3 (
    .clk(IR3), .D(1'b1), .Q(d_ff_3_q), .reset(IR3_q));  // open: Qn, preset, en
  Hex_Digit_Display hex_digit_display_1 (.value(LedData[31:28]));  // open: dp
  Register #(.width(32), .trigger("rising"), .Select("low")) u_PC (.D(PCout), .en(stop), .Q(PC), .clk(CLK), .clr(RST));
  or or_4 (or_4_out, d_ff_1_q, IR1_q);
  or or_5 (or_5_out, d_ff_2_q, IR2_q);
  or or_6 (or_6_out, d_ff_3_q, IR3_q);
  Hex_Digit_Display hex_digit_display_2 (.value(LedData[27:24]));  // open: dp
  Hex_Digit_Display hex_digit_display_3 (.value(LedData[23:20]));  // open: dp
  Adder #(.width(32)) adder_1 (.a(PC), .b(32'h4), .out({adder_1_out_2, adder_1_out}));  // open: cin, cout
  and and_1 (and_1_out, ERET, IR_now[0], ~IR_now[1]);  // AND_Gate
  and and_2 (and_2_out, ERET, ~IR_now[0], IR_now[1]);  // AND_Gate
  and and_3 (and_3_out, ERET, IR_now[0], IR_now[1]);
  Hex_Digit_Display hex_digit_display_4 (.value(LedData[19:16]));  // open: dp
  Hex_Digit_Display hex_digit_display_5 (.value(LedData[15:12]));  // open: dp
  ROM #(.addrWidth(10), .dataWidth(32), .Select("high")) rom_1 (.addr(PC[11:2]), .data(IR));
  and and_4 (and_4_out, or_4_out, ~and_1_out);  // AND_Gate
  and and_5 (and_5_out, or_5_out, ~and_2_out);  // AND_Gate
  and and_6 (and_6_out, or_6_out, ~and_3_out);  // AND_Gate
  Hex_Digit_Display hex_digit_display_6 (.value(LedData[7:4]));  // open: dp
  Hex_Digit_Display hex_digit_display_7 (.value(LedData[11:8]));  // open: dp
  D_Flip_Flop #(.trigger("rising"), .Pre_Clr_Positions("LEGACY"), .NegatePresetClear("false"), .enable("true"), .NewFFLayout("false")) u_IR1 (
    .clk(CLK), .D(and_4_out), .Q(IR1_q));  // open: Qn, preset, en, reset
  D_Flip_Flop #(.trigger("rising"), .Pre_Clr_Positions("LEGACY"), .NegatePresetClear("false"), .enable("true"), .NewFFLayout("false")) u_IR2 (
    .clk(CLK), .D(and_5_out), .Q(IR2_q));  // open: Qn, preset, en, reset
  D_Flip_Flop #(.trigger("rising"), .Pre_Clr_Positions("LEGACY"), .NegatePresetClear("false"), .enable("true"), .NewFFLayout("false")) u_IR3 (
    .clk(CLK), .D(and_6_out), .Q(IR3_q));  // open: Qn, preset, en, reset
  Hex_Digit_Display hex_digit_display_8 (.value(LedData[3:0]));  // open: dp
  Priority_Encoder #(.select(2), .disabled("Z")) priority_encoder_1 (
    .in0(1'b1), .in1(IR1_q), .in2(IR2_q), .in3(IR3_q), .out(priority_encoder_1_out),
    .gs(priority_encoder_1_gs));  // open: en_out, en_in
  // Probe on \总周期数 
  // Probe on \无条件分支数 
  // Probe on \条件分支成功数 
  \单周期硬布线控制器  \u_单周期硬布线控制器_1  (
    .Func(IR[5:0]), .OP(IR[31:26]), .ALU_OP(\单周期硬布线控制器_1_alu_op ), .MemToReg(MemToReg), .MemWrite(MemWrite),
    .ALU_SRC(AluSrcB), .RegWrite(RegWrite), .SysCALL(Syscall), .SignedExt(SignedExt),
    .RegDst(\单周期硬布线控制器_1_regdst ), .JR(\单周期硬布线控制器_1_jr [0]), .JMP(\单周期硬布线控制器_1_jr [1]),
    .Beq(\单周期硬布线控制器_1_beq ), .JAL(JAL), .Bne(\单周期硬布线控制器_1_bne ), .LBU(LBU), .BLTZ(BLTZ), .ERET(ERET));  // open: MFC0, MTC0, MF
  Multiplexer #(.select(1), .width(5), .disabled("Z"), .enable("false")) multiplexer_2 (
    .in0(IR[25:21]), .in1(5'b00100), .out(multiplexer_2_out), .sel(Syscall));
  Multiplexer #(.select(1), .width(5), .disabled("Z"), .enable("false")) multiplexer_3 (
    .in0(IR[20:16]), .in1(5'b00010), .out(multiplexer_3_out), .sel(Syscall));
  Multiplexer #(.select(1), .width(32), .disabled("Z"), .enable("false")) multiplexer_4 (
    .in0(multiplexer_18_out), .in1({adder_1_out_2, adder_1_out}), .out(RDin), .sel(JAL));
  assign bit_extender_1_out = {{16{1'b0}}, IR[15:0]};  // Bit_Extender bit_extender_1
  assign bit_extender_2_out = {{16{IR[15]}}, IR[15:0]};  // Bit_Extender bit_extender_2
  // Probe on priority_encoder_1_out
  Multiplexer #(.select(2), .width(1), .disabled("Z"), .enable("false")) multiplexer_5 (
    .in0(1'b0), .in1(priority_encoder_1_gs), .in2(priority_encoder_1_gs), .in3(priority_encoder_1_gs),
    .out(multiplexer_5_out), .sel(priority_encoder_1_out));
  Multiplexer #(.select(1), .width(5), .disabled("Z"), .enable("false")) multiplexer_6 (
    .in0(IR[20:16]), .in1(IR[15:11]), .out(multiplexer_6_out), .sel(\单周期硬布线控制器_1_regdst ));
  Multiplexer #(.select(1), .width(5), .disabled("Z"), .enable("false")) multiplexer_7 (
    .in0(multiplexer_6_out), .in1({5{1'b1}}), .out(multiplexer_7_out), .sel(JAL));
  Multiplexer #(.select(1), .width(32), .disabled("Z"), .enable("false")) multiplexer_8 (
    .in0(bit_extender_1_out), .in1(bit_extender_2_out), .out(multiplexer_8_out), .sel(SignedExt));
  Shifter #(.width(32), .shift("ll")) shifter_1 (.in(bit_extender_2_out), .\dist (5'b00010), .out(shifter_1_out));
  Multiplexer #(.select(2), .width(32), .disabled("Z"), .enable("false")) multiplexer_9 (
    .in0(nextPC), .in1(32'h4), .in2(32'h1c8), .in3(32'h38c), .out(multiplexer_9_out),
    .sel(priority_encoder_1_out));
  and and_7 (and_7_out, multiplexer_5_out, ~\中断状态_q );  // AND_Gate
  Adder #(.width(32)) adder_2 (
    .a(shifter_1_out), .b({adder_1_out_2, adder_1_out}), .out(adder_2_out));  // open: cin, cout
  Multiplexer #(.select(1), .width(32), .disabled("Z"), .enable("false")) multiplexer_10 (
    .in0(nextPC), .in1(multiplexer_9_out), .out(multiplexer_10_out), .sel(and_7_out));
  and and_8 (and_8_out, and_7_out, ~ERET);  // AND_Gate
  or or_7 (or_7_out, and_7_out, \中断状态_q );
  MIPS_Regifile mips_regifile_1 (
    .Din(RDin), .Clk(CLK), .R1(a0), .R2(MDin), .WE(RegWrite), .W_num(multiplexer_7_out),
    .R1_num(multiplexer_2_out), .R2_num(multiplexer_3_out));
  Multiplexer #(.select(1), .width(32), .disabled("Z"), .enable("false")) multiplexer_11 (
    .in0(multiplexer_10_out), .in1(EPC_q), .out(PCout), .sel(ERET));
  Register #(.width(32), .trigger("rising"), .Select("low")) EPC (
    .D(PC), .en(and_7_out), .Q(EPC_q), .clk(CLK));  // open: clr
  Register #(.width(1), .trigger("rising"), .Select("low")) \u_中断状态  (
    .D(or_7_out), .Q(\中断状态_q ), .clk(CLK), .clr(ERET));  // open: en
  Multiplexer #(.select(1), .width(32), .disabled("Z"), .enable("false")) multiplexer_12 (
    .in0(a0), .in1(32'h22), .out(multiplexer_12_out), .sel(Syscall));
  Multiplexer #(.select(1), .width(32), .disabled("Z"), .enable("false")) multiplexer_13 (
    .in0(MDin), .in1(multiplexer_8_out), .out(multiplexer_13_out), .sel(AluSrcB));
  // Probe on PCout
  Register #(.width(2), .trigger("rising"), .Select("low")) cause (
    .D(priority_encoder_1_out), .en(and_8_out), .Q(IR_now), .clk(CLK), .clr(comparator_1_eq));
  and and_9 (and_9_out, \单周期硬布线控制器_1_bne , not_1_out);
  and and_10 (and_10_out, \单周期硬布线控制器_1_beq , mips_alu_1_equal);
  not not_1 (not_1_out, mips_alu_1_equal);
  Multiplexer #(.select(1), .width(32), .disabled("Z"), .enable("false")) multiplexer_14 (
    .in0(multiplexer_13_out), .in1({32{1'b0}}), .out(multiplexer_14_out), .sel(BLTZ));
  Comparator #(.width(2), .mode("twosComplement")) comparator_1 (
    .a(priority_encoder_1_out), .b(2'b00), .eq(comparator_1_eq));  // open: gt, lt
  or or_8 (\单周期硬布线控制器_1_jr [2], and_10_out, and_9_out, and_11_out);
  and and_11 (and_11_out, comparator_2_eq, BLTZ);
  MIPS_ALU mips_alu_1 (
    .X(multiplexer_12_out), .Y(multiplexer_14_out), .AluOP(\单周期硬布线控制器_1_alu_op ), .Equal(mips_alu_1_equal),
    .Result(mips_alu_1_result), .shamt(IR[10:6]));  // open: Result_2
  // Probe on mips_alu_1_result
  Counter #(.width(16), .max('hffff), .ongoal("wrap"), .trigger("rising"), .behavior("old")) counter_1 (
    .count(\单周期硬布线控制器_1_jr [1]), .Q(\无条件分支数 ), .clk(CLK), .clr(RST));  // open: load, D, carry, preset
  Counter #(.width(16), .max('hffff), .ongoal("wrap"), .trigger("rising"), .behavior("old")) counter_2 (
    .count(\单周期硬布线控制器_1_jr [2]), .Q(\条件分支成功数 ), .clk(CLK), .clr(RST));  // open: load, D, carry, preset
  Register #(.width(32), .trigger("rising"), .Select("low")) register_1 (
    .D(a0), .en(and_12_out), .Q(LedData), .clk(CLK), .clr(RST));
  and and_12 (and_12_out, mips_alu_1_equal, Syscall);
  Multiplexer #(.select(1), .width(1), .disabled("Z"), .enable("false")) multiplexer_15 (
    .in0(1'b1), .in1(Go), .out(stop), .sel(and_13_out));
  and and_13 (and_13_out, Syscall, ~mips_alu_1_equal);  // AND_Gate
  Counter #(.width(16), .max('hffff), .ongoal("wrap"), .trigger("rising"), .behavior("old")) counter_3 (
    .count(stop), .Q(\总周期数 ), .clk(CLK), .clr(RST));  // open: load, D, carry, preset
  Comparator #(.width(32), .mode("twosComplement")) comparator_2 (
    .a(32'h1), .b(mips_alu_1_result), .eq(comparator_2_eq));  // open: gt, lt
  not not_2 (not_2_out, MemWrite);
  RAM #(.addrWidth(10), .dataWidth(32), .bus("separate"), .Select("high")) ram_1 (
    .addr(mips_alu_1_result[11:2]), .din(MDin), .data(ram_1_data), .str(MemWrite), .clk(CLK), .ld(not_2_out),
    .clr(RST));  // open: sel
  Multiplexer #(.select(1), .width(32), .disabled("Z"), .enable("false")) multiplexer_16 (
    .in0(mips_alu_1_result), .in1(ram_1_data), .out(multiplexer_16_out), .sel(MemToReg));
  Multiplexer #(.select(2), .width(8), .disabled("Z"), .enable("false")) multiplexer_17 (
    .in0(multiplexer_16_out[7:0]), .in1(multiplexer_16_out[15:8]), .in2(multiplexer_16_out[23:16]),
    .in3(multiplexer_16_out[31:24]), .out(multiplexer_17_out), .sel(mips_alu_1_result[1:0]));
  assign bit_extender_3_out = {{24{1'b0}}, multiplexer_17_out};  // Bit_Extender bit_extender_3
  Multiplexer #(.select(1), .width(32), .disabled("Z"), .enable("false")) multiplexer_18 (
    .in0(multiplexer_16_out), .in1(bit_extender_3_out), .out(multiplexer_18_out), .sel(LBU));

  // Notes on the sheet:
  //   中断源
  //   总复位信号应将除ROM以外所有存储组件全部清零
  //   中断等待指示
  //   中断优先级3>2>1>CPU(0）)
  //   数码管输出
  //   数码管输出应该用寄存器锁存，否则显示数据只能一闪而过
  //   指令存储器
  //   contents of rom_1 (hex, n*v repeats v):
  //   8000d54 23bdfffc afa10000 23bdfffc afa20000 23bdfffc afa30000 23bdfffc afa40000 23bdfffc afa50000
  //   23bdfffc afa60000 23bdfffc afa70000 23bdfffc afa80000 23bdfffc afa90000 23bdfffc afaa0000 23bdfffc
  //   afab0000 23bdfffc afac0000 23bdfffc afad0000 23bdfffc afae0000 23bdfffc afaf0000 23bdfffc afb00000
  //   23bdfffc afb10000 23bdfffc afb20000 23bdfffc afb30000 23bdfffc afb40000 23bdfffc afb50000 23bdfffc
  //   afb60000 23bdfffc afb70000 23bdfffc afb80000 23bdfffc afb90000 20160001 20140006 20150001 168020
  //   108100 2149825 132020 20020022 c 1600fffa 295a022 1680fff7 8fb90000 23bd0004 8fb80000 23bd0004
  //   8fb70000 23bd0004 8fb60000 23bd0004 8fb50000 23bd0004 8fb40000 23bd0004 8fb30000 23bd0004 8fb20000
  //   23bd0004 8fb10000 23bd0004 8fb00000 23bd0004 8faf0000 23bd0004 8fae0000 23bd0004 8fad0000 23bd0004
  //   8fac0000 23bd0004 8fab0000 23bd0004 8faa0000 23bd0004 8fa90000 23bd0004 8fa80000 23bd0004 8fa70000
  //   23bd0004 8fa60000 23bd0004 8fa50000 23bd0004 8fa40000 23bd0004 8fa30000 23bd0004 8fa20000 23bd0004
  //   8fa10000 23bd0004 42000018 23bdfffc afa10000 23bdfffc afa20000 23bdfffc afa30000 23bdfffc afa40000
  //   23bdfffc afa50000 23bdfffc afa60000 23bdfffc afa70000 23bdfffc afa80000 23bdfffc afa90000 23bdfffc
  //   afaa0000 23bdfffc afab0000 23bdfffc afac0000 23bdfffc afad0000 23bdfffc afae0000 23bdfffc afaf0000
  //   23bdfffc afb00000 23bdfffc afb10000 23bdfffc afb20000 23bdfffc afb30000 23bdfffc afb40000 23bdfffc
  //   afb50000 23bdfffc afb60000 23bdfffc afb70000 23bdfffc afb80000 23bdfffc afb90000 20160002 20140006
  //   20150001 168020 108100 2149825 132020 20020022 c 1600fffa 295a022 1680fff7 8fb90000 23bd0004
  //   8fb80000 23bd0004 8fb70000 23bd0004 8fb60000 23bd0004 8fb50000 23bd0004 8fb40000 23bd0004 8fb30000
  //   23bd0004 8fb20000 23bd0004 8fb10000 23bd0004 8fb00000 23bd0004 8faf0000 23bd0004 8fae0000 23bd0004
  //   8fad0000 23bd0004 8fac0000 23bd0004 8fab0000 23bd0004 8faa0000 23bd0004 8fa90000 23bd0004 8fa80000
  //   23bd0004 8fa70000 23bd0004 8fa60000 23bd0004 8fa50000 23bd0004 8fa40000 23bd0004 8fa30000 23bd0004
  //   8fa20000 23bd0004 8fa10000 23bd0004 42000018 23bdfffc afa10000 23bdfffc afa20000 23bdfffc afa30000
  //   23bdfffc afa40000 23bdfffc afa50000 23bdfffc afa60000 23bdfffc afa70000 23bdfffc afa80000 23bdfffc
  //   afa90000 23bdfffc afaa0000 23bdfffc afab0000 23bdfffc afac0000 23bdfffc afad0000 23bdfffc afae0000
  //   23bdfffc afaf0000 23bdfffc afb00000 23bdfffc afb10000 23bdfffc afb20000 23bdfffc afb30000 23bdfffc
  //   afb40000 23bdfffc afb50000 23bdfffc afb60000 23bdfffc afb70000 23bdfffc afb80000 23bdfffc afb90000
  //   20160003 20140006 20150001 168020 108100 2149825 132020 20020022 c 1600fffa 295a022 1680fff7
  //   8fb90000 23bd0004 8fb80000 23bd0004 8fb70000 23bd0004 8fb60000 23bd0004 8fb50000 23bd0004 8fb40000
  //   23bd0004 8fb3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
  //   Reset 
  //   Reset 
  //   Reset 
  //   OP
  //   Func
  //   rs
  //   指令字
  //   rt
  //   rd
  //   shamt
  //   imm
  //   JMP
  //   JR
  //   OP
  //   Func
  //   Beq
  //   Bne
  //   AluOP
  //   AluSrcB
  //   RegWrite
  //   JAL
  //   RegDst
  //   Syscall
  //   MemToReg
  //   MemWrite
  //   关中断信号
  //   为方便自动评测，需要输出PC，IR，寄存器文件写入端口RDin，内存写入端口MDin等信号
endmodule

module \多级中断  (
  output RegWrite,
  output MemWrite,
  output [31:0] PC,
  output [31:0] IR,
  output [31:0] RDin,
  output [31:0] MDin
);

  wire AluSrcB, and_1_out, and_2_out, and_3_out, and_7_out, and_8_out, and_9_out, and_10_out, and_11_out,
       and_12_out, and_13_out, and_14_out, and_15_out, and_16_out, and_17_out, and_18_out, and_19_out,
       and_20_out, and_21_out, and_22_out, BLTZ, CLK, comparator_1_eq, comparator_2_eq, comparator_3_eq,
       comparator_4_gt, comparator_5_eq, comparator_6_eq, comparator_7_eq, comparator_8_eq, comparator_9_gt,
       d_ff_1_q, d_ff_2_q, d_ff_3_q, d_ff_4_qn, d_ff_5_qn, d_ff_6_qn, d_ff_7_qn, d_ff_8_q, decoder_1_out1,
       decoder_1_out2, decoder_1_out3, decoder_2_out0, decoder_2_out1, ERET, Go, IE_q, IR1, ir1_t, IR2,
       ir2_t, IR3, ir3_t, JAL, LBU, MemToReg, MFC_0, mips_alu_1_equal, MTC_0, multiplexer_12_out,
       multiplexer_13_out, multiplexer_14_out, multiplexer_15_out, multiplexer_20_out, multiplexer_21_out,
       not_1_out, not_2_out, not_3_out, or_4_out, or_5_out, or_6_out, or_8_out, or_9_out, or_10_out,
       or_11_out, priority_encoder_3_gs, RST, Rst1, Rst2, Rst3, SignedExt, stop, Syscall, W1, W2, W3,
       \单周期硬布线控制器_1_beq , \单周期硬布线控制器_1_bne , \单周期硬布线控制器_1_regdst ;
  wire [1:0] IR_now, priority_encoder_1_out, priority_encoder_2_out, priority_encoder_4_out;
  wire [1:1] IE_sel;
  wire [2:0] \单周期硬布线控制器_1_jr ;
  wire [3:0] \单周期硬布线控制器_1_alu_op , \屏蔽字R ;
  wire [4:0] multiplexer_2_out, multiplexer_3_out, multiplexer_5_out, multiplexer_6_out;
  wire [7:0] multiplexer_18_out;
  wire [15:0] \总周期数 , \无条件分支数 , \条件分支成功数 ;
  wire [27:0] adder_1_out_2;
  wire [31:0] a0, adder_2_out, bit_extender_1_out, bit_extender_2_out, bit_extender_3_out,
       demultiplexer_1_out1, demultiplexer_1_out2, EPC_q, LedData, mips_alu_1_result, multiplexer_4_out,
       multiplexer_8_out, multiplexer_9_out, multiplexer_10_out, multiplexer_11_out, multiplexer_17_out,
       multiplexer_19_out, multiplexer_22_out, multiplexer_23_out, multiplexer_24_out, nextPC, PCout,
       ram_1_data, shifter_1_out, siteData, \屏蔽字 ;
  wire [31:28] adder_1_out;

  Clock #(.highDuration(1), .lowDuration(1)) clock_1 (.out(CLK));
  Button \u_继续运行  (.out(Go));
  Button \u_总复位  (.out(RST));
  Button _1 (.out(IR1));
  Button _2 (.out(IR2));
  Button _3 (.out(IR3));
  // Probe on IR_now
  LED #(.active("true")) led_1 (.in(W1));
  LED #(.active("true")) led_2 (.in(W2));
  LED #(.active("true")) led_3 (.in(W3));
  Multiplexer #(.select(3), .width(32), .disabled("Z"), .enable("false")) multiplexer_1 (
    .in0({adder_1_out, adder_1_out_2}), .in1({32{1'b0}}), .in2({adder_1_out, IR[25:0], 2'b00}), .in3(a0),
    .in4(adder_2_out), .in5({32{1'b0}}), .in6({32{1'b0}}), .in7({32{1'b0}}), .out(nextPC),
    .sel(\单周期硬布线控制器_1_jr ));
  or or_1 (W1, ir1_t, d_ff_3_q);
  D_Flip_Flop #(.trigger("rising"), .Pre_Clr_Positions("LEGACY"), .NegatePresetClear("false"), .enable("true"), .NewFFLayout("false")) d_ff_1 (
    .clk(IR2), .D(1'b1), .Q(d_ff_1_q), .reset(ir2_t));  // open: Qn, preset, en
  or or_2 (W2, ir2_t, d_ff_1_q);
  D_Flip_Flop #(.trigger("rising"), .Pre_Clr_Positions("LEGACY"), .NegatePresetClear("false"), .enable("true"), .NewFFLayout("false")) d_ff_2 (
    .clk(IR3), .D(1'b1), .Q(d_ff_2_q), .reset(ir3_t));  // open: Qn, preset, en
  or or_3 (W3, ir3_t, d_ff_2_q);
  Hex_Digit_Display hex_digit_display_1 (.value(LedData[31:28]));  // open: dp
  Register #(.width(32), .trigger("rising"), .Select("low")) u_PC (.D(PCout), .en(stop), .Q(PC), .clk(CLK), .clr(RST));
  D_Flip_Flop #(.trigger("rising"), .Pre_Clr_Positions("LEGACY"), .NegatePresetClear("false"), .enable("true"), .NewFFLayout("false")) d_ff_3 (
    .clk(IR1), .D(1'b1), .Q(d_ff_3_q), .reset(ir1_t));  // open: Qn, preset, en
  Hex_Digit_Display hex_digit_display_2 (.value(LedData[23:20]));  // open: dp
  Hex_Digit_Display hex_digit_display_3 (.value(LedData[27:24]));  // open: dp
  Adder #(.width(32)) adder_1 (.a(PC), .b(32'h4), .out({adder_1_out, adder_1_out_2}));  // open: cin, cout
  or or_4 (or_4_out, d_ff_3_q, ir1_t);
  or or_5 (or_5_out, d_ff_1_q, ir2_t);
  or or_6 (or_6_out, d_ff_2_q, ir3_t);
  Hex_Digit_Display hex_digit_display_4 (.value(LedData[19:16]));  // open: dp
  Hex_Digit_Display hex_digit_display_5 (.value(LedData[15:12]));  // open: dp
  ROM #(.addrWidth(10), .dataWidth(32), .Select("high")) rom_1 (.addr(PC[11:2]), .data(IR));
  and and_1 (and_1_out, or_4_out, ~Rst1);  // AND_Gate
  and and_2 (and_2_out, or_5_out, ~Rst2);  // AND_Gate
  and and_3 (and_3_out, or_6_out, ~Rst3);  // AND_Gate
  Hex_Digit_Display hex_digit_display_6 (.value(LedData[7:4]));  // open: dp
  Hex_Digit_Display hex_digit_display_7 (.value(LedData[11:8]));  // open: dp
  D_Flip_Flop #(.trigger("rising"), .Pre_Clr_Positions("LEGACY"), .NegatePresetClear("false"), .enable("true"), .NewFFLayout("false")) u_IR1 (
    .clk(CLK), .D(and_1_out), .Q(ir1_t));  // open: Qn, preset, en, reset
  D_Flip_Flop #(.trigger("rising"), .Pre_Clr_Positions("LEGACY"), .NegatePresetClear("false"), .enable("true"), .NewFFLayout("false")) u_IR2 (
    .clk(CLK), .D(and_2_out), .Q(ir2_t));  // open: Qn, preset, en, reset
  D_Flip_Flop #(.trigger("rising"), .Pre_Clr_Positions("LEGACY"), .NegatePresetClear("false"), .enable("true"), .NewFFLayout("false")) u_IR3 (
    .clk(CLK), .D(and_3_out), .Q(ir3_t));  // open: Qn, preset, en, reset
  Hex_Digit_Display hex_digit_display_8 (.value(LedData[3:0]));  // open: dp
  // Probe on \总周期数 
  // Probe on \无条件分支数 
  // Probe on \条件分支成功数 
  \单周期硬布线控制器  \u_单周期硬布线控制器_1  (
    .Func(IR[5:0]), .OP(IR[31:26]), .ALU_OP(\单周期硬布线控制器_1_alu_op ), .MemToReg(MemToReg), .MemWrite(MemWrite),
    .ALU_SRC(AluSrcB), .RegWrite(RegWrite), .SysCALL(Syscall), .SignedExt(SignedExt),
    .RegDst(\单周期硬布线控制器_1_regdst ), .JR(\单周期硬布线控制器_1_jr [0]), .JMP(\单周期硬布线控制器_1_jr [1]),
    .Beq(\单周期硬布线控制器_1_beq ), .JAL(JAL), .Bne(\单周期硬布线控制器_1_bne ), .LBU(LBU), .BLTZ(BLTZ), .MFC0(MFC_0),
    .MTC0(MTC_0), .MF(IR[25:21]), .ERET(ERET));
  Multiplexer #(.select(1), .width(5), .disabled("Z"), .enable("false")) multiplexer_2 (
    .in0(IR[25:21]), .in1(5'b00100), .out(multiplexer_2_out), .sel(Syscall));
  Multiplexer #(.select(1), .width(5), .disabled("Z"), .enable("false")) multiplexer_3 (
    .in0(IR[20:16]), .in1(5'b00010), .out(multiplexer_3_out), .sel(Syscall));
  Multiplexer #(.select(1), .width(32), .disabled("Z"), .enable("false")) multiplexer_4 (
    .in0(multiplexer_19_out), .in1({adder_1_out, adder_1_out_2}), .out(multiplexer_4_out), .sel(JAL));
  assign bit_extender_1_out = {{16{1'b0}}, IR[15:0]};  // Bit_Extender bit_extender_1
  assign bit_extender_2_out = {{16{IR[15]}}, IR[15:0]};  // Bit_Extender bit_extender_2
  Decoder #(.select(2), .tristate("false"), .disabled("Z"), .enable("false")) decoder_1 (
    .out1(decoder_1_out1), .out2(decoder_1_out2), .out3(decoder_1_out3), .sel(priority_encoder_1_out));  // open: out0
  Priority_Encoder #(.select(2), .disabled("Z")) priority_encoder_1 (
    .in0(1'b0), .in1(ir1_t), .in2(ir2_t), .in3(ir3_t), .out(priority_encoder_1_out));  // open: gs, en_out, en_in
  Multiplexer #(.select(1), .width(5), .disabled("Z"), .enable("false")) multiplexer_5 (
    .in0(IR[20:16]), .in1(IR[15:11]), .out(multiplexer_5_out), .sel(\单周期硬布线控制器_1_regdst ));
  Multiplexer #(.select(1), .width(5), .disabled("Z"), .enable("false")) multiplexer_6 (
    .in0(multiplexer_5_out), .in1({5{1'b1}}), .out(multiplexer_6_out), .sel(JAL));
  Multiplexer #(.select(1), .width(32), .disabled("Z"), .enable("false")) multiplexer_7 (
    .in0(multiplexer_4_out), .in1(siteData), .out(RDin), .sel(MFC_0));
  Multiplexer #(.select(1), .width(32), .disabled("Z"), .enable("false")) multiplexer_8 (
    .in0(bit_extender_1_out), .in1(bit_extender_2_out), .out(multiplexer_8_out), .sel(SignedExt));
  Shifter #(.width(32), .shift("ll")) shifter_1 (.in(bit_extender_2_out), .\dist (5'b00010), .out(shifter_1_out));
  and and_4 (Rst1, ERET, decoder_1_out1);
  and and_5 (Rst2, ERET, decoder_1_out2);
  and and_6 (Rst3, ERET, decoder_1_out3);
  Adder #(.width(32)) adder_2 (
    .a(shifter_1_out), .b({adder_1_out, adder_1_out_2}), .out(adder_2_out));  // open: cin, cout
  // Probe on Rst1
  MIPS_Regifile mips_regifile_1 (
    .Din(RDin), .Clk(CLK), .R1(a0), .R2(MDin), .WE(RegWrite), .W_num(multiplexer_6_out),
    .R1_num(multiplexer_2_out), .R2_num(multiplexer_3_out));
  Multiplexer #(.select(1), .width(32), .disabled("Z"), .enable("false")) multiplexer_9 (
    .in0(a0), .in1(32'h22), .out(multiplexer_9_out), .sel(Syscall));
  Multiplexer #(.select(1), .width(32), .disabled("Z"), .enable("false")) multiplexer_10 (
    .in0(MDin), .in1(multiplexer_8_out), .out(multiplexer_10_out), .sel(AluSrcB));
  and and_7 (and_7_out, \单周期硬布线控制器_1_beq , mips_alu_1_equal);
  and and_8 (and_8_out, \单周期硬布线控制器_1_bne , not_1_out);
  not not_1 (not_1_out, mips_alu_1_equal);
  Multiplexer #(.select(1), .width(32), .disabled("Z"), .enable("false")) multiplexer_11 (
    .in0(multiplexer_10_out), .in1({32{1'b0}}), .out(multiplexer_11_out), .sel(BLTZ));
  Multiplexer #(.select(1), .width(1), .disabled("Z"), .enable("false")) multiplexer_12 (
    .in0(1'b0), .in1(\屏蔽字 [0]), .out(multiplexer_12_out), .sel(decoder_2_out0));
  Multiplexer #(.select(1), .width(1), .disabled("Z"), .enable("false")) multiplexer_13 (
    .in0(1'b0), .in1(\屏蔽字 [1]), .out(multiplexer_13_out), .sel(decoder_2_out0));
  Multiplexer #(.select(1), .width(1), .disabled("Z"), .enable("false")) multiplexer_14 (
    .in0(1'b0), .in1(\屏蔽字 [2]), .out(multiplexer_14_out), .sel(decoder_2_out0));
  Multiplexer #(.select(1), .width(1), .disabled("Z"), .enable("false")) multiplexer_15 (
    .in0(1'b0), .in1(\屏蔽字 [3]), .out(multiplexer_15_out), .sel(decoder_2_out0));
  or or_7 (\单周期硬布线控制器_1_jr [2], and_7_out, and_8_out, and_9_out);
  and and_9 (and_9_out, comparator_5_eq, BLTZ);
  MIPS_ALU mips_alu_1 (
    .X(multiplexer_9_out), .Y(multiplexer_11_out), .AluOP(\单周期硬布线控制器_1_alu_op ), .Equal(mips_alu_1_equal),
    .Result(mips_alu_1_result), .shamt(IR[10:6]));  // open: Result_2
  // Probe on mips_alu_1_result
  Comparator #(.width(5), .mode("twosComplement")) comparator_1 (
    .a(IR[15:11]), .b(5'b00001), .eq(comparator_1_eq));  // open: gt, lt
  and and_10 (and_10_out, comparator_1_eq, MTC_0);
  Comparator #(.width(5), .mode("twosComplement")) comparator_2 (
    .a(IR[15:11]), .b(5'b00010), .eq(comparator_2_eq));  // open: gt, lt
  and and_11 (and_11_out, comparator_2_eq, MTC_0);
  Comparator #(.width(5), .mode("twosComplement")) comparator_3 (
    .a(IR[15:11]), .b(5'b00011), .eq(comparator_3_eq));  // open: gt, lt
  and and_12 (and_12_out, comparator_3_eq, MTC_0);
  or or_8 (or_8_out, ~MTC_0, comparator_4_gt);  // OR_Gate
  Comparator #(.width(5), .mode("twosComplement")) comparator_4 (
    .a(IR[15:11]), .b(5'b00011), .gt(comparator_4_gt));  // open: eq, lt
  Counter #(.width(16), .max('hffff), .ongoal("wrap"), .trigger("rising"), .behavior("old")) counter_1 (
    .count(\单周期硬布线控制器_1_jr [1]), .Q(\无条件分支数 ), .clk(CLK), .clr(RST));  // open: load, D, carry, preset
  Counter #(.width(16), .max('hffff), .ongoal("wrap"), .trigger("rising"), .behavior("old")) counter_2 (
    .count(\单周期硬布线控制器_1_jr [2]), .Q(\条件分支成功数 ), .clk(CLK), .clr(RST));  // open: load, D, carry, preset
  Register #(.width(32), .trigger("rising"), .Select("low")) register_1 (
    .D(a0), .en(and_13_out), .Q(LedData), .clk(CLK), .clr(RST));
  and and_13 (and_13_out, mips_alu_1_equal, Syscall);
  Multiplexer #(.select(1), .width(1), .disabled("Z"), .enable("false")) multiplexer_16 (
    .in0(1'b1), .in1(Go), .out(stop), .sel(and_14_out));
  and and_14 (and_14_out, Syscall, ~mips_alu_1_equal);  // AND_Gate
  D_Flip_Flop #(.trigger("rising"), .Pre_Clr_Positions("LEGACY"), .NegatePresetClear("false"), .enable("true"), .NewFFLayout("false")) d_ff_4 (
    .clk(CLK), .D(multiplexer_12_out), .Q(\屏蔽字R [0]), .Qn(d_ff_4_qn), .en(decoder_2_out0));  // open: preset, reset
  D_Flip_Flop #(.trigger("rising"), .Pre_Clr_Positions("LEGACY"), .NegatePresetClear("false"), .enable("true"), .NewFFLayout("false")) d_ff_5 (
    .clk(CLK), .D(multiplexer_13_out), .Q(\屏蔽字R [1]), .Qn(d_ff_5_qn), .en(decoder_2_out0));  // open: preset, reset
  D_Flip_Flop #(.trigger("rising"), .Pre_Clr_Positions("LEGACY"), .NegatePresetClear("false"), .enable("true"), .NewFFLayout("false")) d_ff_6 (
    .clk(CLK), .D(multiplexer_14_out), .Q(\屏蔽字R [2]), .Qn(d_ff_6_qn), .en(decoder_2_out0));  // open: preset, reset
  D_Flip_Flop #(.trigger("rising"), .Pre_Clr_Positions("LEGACY"), .NegatePresetClear("false"), .enable("true"), .NewFFLayout("false")) d_ff_7 (
    .clk(CLK), .D(multiplexer_15_out), .Q(\屏蔽字R [3]), .Qn(d_ff_7_qn), .en(decoder_2_out0));  // open: preset, reset
  Priority_Encoder #(.select(2), .disabled("Z")) priority_encoder_2 (
    .in0(and_10_out), .in1(and_11_out), .in2(and_12_out), .in3(or_8_out), .out(priority_encoder_2_out));  // open: gs, en_out, en_in
  Counter #(.width(16), .max('hffff), .ongoal("wrap"), .trigger("rising"), .behavior("old")) counter_3 (
    .count(stop), .Q(\总周期数 ), .clk(CLK), .clr(RST));  // open: load, D, carry, preset
  Comparator #(.width(32), .mode("twosComplement")) comparator_5 (
    .a(32'h1), .b(mips_alu_1_result), .eq(comparator_5_eq));  // open: gt, lt
  not not_2 (not_2_out, MemWrite);
  and and_15 (and_15_out, 1'b0, d_ff_4_qn);
  and and_16 (and_16_out, ir1_t, d_ff_5_qn);
  and and_17 (and_17_out, ir2_t, d_ff_6_qn);
  and and_18 (and_18_out, ir3_t, d_ff_7_qn);
  RAM #(.addrWidth(10), .dataWidth(32), .bus("separate"), .Select("high")) ram_1 (
    .addr(mips_alu_1_result[11:2]), .din(MDin), .data(ram_1_data), .str(MemWrite), .clk(CLK), .ld(not_2_out),
    .clr(RST));  // open: sel
  Priority_Encoder #(.select(2), .disabled("Z")) priority_encoder_3 (
    .in0(and_15_out), .in1(and_16_out), .in2(and_17_out), .in3(and_18_out), .out(IR_now),
    .gs(priority_encoder_3_gs));  // open: en_out, en_in
  Multiplexer #(.select(1), .width(32), .disabled("Z"), .enable("false")) multiplexer_17 (
    .in0(mips_alu_1_result), .in1(ram_1_data), .out(multiplexer_17_out), .sel(MemToReg));
  // Probe on IR_now
  Decoder #(.select(2), .tristate("false"), .disabled("Z"), .enable("false")) decoder_2 (
    .out0(decoder_2_out0), .out1(decoder_2_out1), .out2(IE_sel[1]), .sel(priority_encoder_2_out));  // open: out3
  Demultiplexer #(.select(2), .width(32), .tristate("false"), .disabled("Z"), .enable("false")) demultiplexer_1 (
    .out0(\屏蔽字 ), .out1(demultiplexer_1_out1), .out2(demultiplexer_1_out2), .in(MDin),
    .sel(priority_encoder_2_out));  // open: out3
  Multiplexer #(.select(2), .width(8), .disabled("Z"), .enable("false")) multiplexer_18 (
    .in0(multiplexer_17_out[7:0]), .in1(multiplexer_17_out[15:8]), .in2(multiplexer_17_out[23:16]),
    .in3(multiplexer_17_out[31:24]), .out(multiplexer_18_out), .sel(mips_alu_1_result[1:0]));
  assign bit_extender_3_out = {{24{1'b0}}, multiplexer_18_out};  // Bit_Extender bit_extender_3
  Multiplexer #(.select(1), .width(32), .disabled("Z"), .enable("false")) multiplexer_19 (
    .in0(multiplexer_17_out), .in1(bit_extender_3_out), .out(multiplexer_19_out), .sel(LBU));
  Multiplexer #(.select(2), .width(1), .disabled("Z"), .enable("false")) multiplexer_20 (
    .in0(1'b0), .in1(1'b1), .in2(demultiplexer_1_out2[0]), .in3(1'b0), .out(multiplexer_20_out),
    .sel({IE_sel[1], ERET}));
  not not_3 (not_3_out, d_ff_8_q);
  D_Flip_Flop #(.trigger("rising"), .Pre_Clr_Positions("LEGACY"), .NegatePresetClear("false"), .enable("true"), .NewFFLayout("false")) d_ff_8 (
    .clk(CLK), .D(1'b1), .Q(d_ff_8_q));  // open: Qn, preset, en, reset
  Multiplexer #(.select(1), .width(1), .disabled("Z"), .enable("false")) multiplexer_21 (
    .in0(multiplexer_20_out), .in1(1'b1), .out(multiplexer_21_out), .sel(not_3_out));
  Multiplexer #(.select(2), .width(32), .disabled("Z"), .enable("false")) multiplexer_22 (
    .in1(32'h4), .in2(32'h20c), .in3(32'h414), .out(multiplexer_22_out), .sel(IR_now));  // open: in0
  and and_19 (and_19_out, priority_encoder_3_gs, IE_q);
  D_Flip_Flop #(.trigger("rising"), .Pre_Clr_Positions("LEGACY"), .NegatePresetClear("false"), .enable("true"), .NewFFLayout("false")) IE (
    .clk(CLK), .D(multiplexer_21_out), .Q(IE_q), .en(or_9_out));  // open: Qn, preset, reset
  or or_9 (or_9_out, not_3_out, IE_sel[1], ERET, and_19_out);
  Multiplexer #(.select(1), .width(32), .disabled("Z"), .enable("false")) multiplexer_23 (
    .in0(nextPC), .in1(multiplexer_22_out), .out(multiplexer_23_out), .sel(and_19_out));
  Multiplexer #(.select(1), .width(32), .disabled("Z"), .enable("false")) multiplexer_24 (
    .in0(PC), .in1(demultiplexer_1_out1), .out(multiplexer_24_out), .sel(decoder_2_out1));
  or or_10 (or_10_out, decoder_2_out1, and_19_out);
  Comparator #(.width(5), .mode("twosComplement")) comparator_6 (
    .a(IR[15:11]), .b(5'b00001), .eq(comparator_6_eq));  // open: gt, lt
  Comparator #(.width(5), .mode("twosComplement")) comparator_7 (
    .a(IR[15:11]), .b(5'b00010), .eq(comparator_7_eq));  // open: gt, lt
  Comparator #(.width(5), .mode("twosComplement")) comparator_8 (
    .a(IR[15:11]), .b(5'b00011), .eq(comparator_8_eq));  // open: gt, lt
  Comparator #(.width(5), .mode("twosComplement")) comparator_9 (
    .a(IR[15:11]), .b(5'b00011), .gt(comparator_9_gt));  // open: eq, lt
  Multiplexer #(.select(1), .width(32), .disabled("Z"), .enable("false")) multiplexer_25 (
    .in0(multiplexer_23_out), .in1(EPC_q), .out(PCout), .sel(ERET));
  Register #(.width(32), .trigger("rising"), .Select("low")) EPC (
    .D(multiplexer_24_out), .en(or_10_out), .Q(EPC_q), .clk(CLK));  // open: clr
  and and_20 (and_20_out, comparator_6_eq, MFC_0);
  and and_21 (and_21_out, comparator_7_eq, MFC_0);
  and and_22 (and_22_out, comparator_8_eq, MFC_0);
  or or_11 (or_11_out, ~MFC_0, comparator_9_gt);  // OR_Gate
  Priority_Encoder #(.select(2), .disabled("Z")) priority_encoder_4 (
    .in0(and_20_out), .in1(and_21_out), .in2(and_22_out), .in3(or_11_out), .out(priority_encoder_4_out));  // open: gs, en_out, en_in
  Multiplexer #(.select(2), .width(32), .disabled("Z"), .enable("false")) multiplexer_26 (
    .in0({{28{1'b0}}, \屏蔽字R }), .in1(EPC_q), .in2({32{1'b0}}), .in3({32{1'b0}}), .out(siteData),
    .sel(priority_encoder_4_out));

  // Other names for the same wires on the sheet: Rd[4:0] = IR[15:11]; IE_sel[0] = ERET; R2[31:0] = MDin

  // Notes on the sheet:
  //   中断源
  //   总复位信号应将除ROM以外所有存储组件全部清零
  //   中断等待指示
  //   中断优先级3>2>1>CPU(0）)
  //   数码管输出
  //   数码管输出应该用寄存器锁存，否则显示数据只能一闪而过
  //   指令存储器
  //   contents of rom_1 (hex, n*v repeats v):
  //   8000d87 23bdfffc afa10000 23bdfffc afa20000 23bdfffc afa30000 23bdfffc afa40000 23bdfffc afa50000
  //   23bdfffc afa60000 23bdfffc afa70000 23bdfffc afa80000 23bdfffc afa90000 23bdfffc afaa0000 23bdfffc
  //   afab0000 23bdfffc afac0000 23bdfffc afad0000 23bdfffc afae0000 23bdfffc afaf0000 23bdfffc afb00000
  //   23bd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
  //   Reset 
  //   Reset 
  //   MF
  //   OP
  //   Func
  //   rs
  //   指令字
  //   rt
  //   rd
  //   shamt
  //   imm
  //   Reset 
  //   JMP
  //   JR
  //   OP
  //   Func
  //   Beq
  //   Bne
  //   AluOP
  //   AluSrcB
  //   RegWrite
  //   JAL
  //   RegDst
  //   Syscall
  //   MemToReg
  //   MemWrite
  //   为方便自动评测，需要输出PC，IR，寄存器文件写入端口RDin，内存写入端口MDin等信号
endmodule

module \流水单级中断  (
);

  wire and_1_out, and_2_out, and_3_out, and_4_out, and_5_out, and_6_out, and_7_out, and_8_out, and_9_out,
       and_10_out, and_11_out, and_12_out, and_13_out, and_14_out, and_15_out, and_16_out, BLTZ, BranchNop,
       CLK, comparator_1_eq, comparator_3_eq, Conbranch, d_ff_1_q, d_ff_2_q, d_ff_3_q, Equal, ERET,
       ex_mem_1_halt_out, ex_mem_1_jal_out, ex_mem_1_memtoreg_out, ex_mem_1_regdst_out, ex_mem_1_syscall_out,
       EX_RegWrite, Go, Halt, id_ex_1_alusrcb_out, id_ex_1_beq_out, id_ex_1_bne_out, id_ex_1_jal_out,
       id_ex_1_lbu_out, id_ex_1_memtoreg_out, id_ex_1_memwrite_out, id_ex_1_regdst_out, ID_JAL, ID_RDst, IR1,
       IR1_q, IR2, IR2_q, IR3, IR3_q, JAL, JMP, JR, LBU, Loaduse, MEM_RegWrite, mem_wb_1_halt_out, MemToReg,
       MemWrite, mips_alu_1_equal, multiplexer_2_out, not_1_out, or_4_out, or_5_out, or_6_out, or_7_out,
       or_8_out, or_9_out, priority_encoder_1_gs, RDst, RST, SignedExt, Sys, syscall, W1, W2, W3,
       WB_RegWrite, \中断状态_q , \单周期硬布线控制器_1_alu_src , \单周期硬布线控制器_1_beq , \单周期硬布线控制器_1_bltz ,
       \单周期硬布线控制器_1_bne , \单周期硬布线控制器_1_jmp , \单周期硬布线控制器_1_jr , \单周期硬布线控制器_1_lbu , \单周期硬布线控制器_1_memtoreg ,
       \单周期硬布线控制器_1_memwrite , \单周期硬布线控制器_1_regwrite , \单周期硬布线控制器_1_syscall , \数据相关 ;
  wire [1:0] IR_now, priority_encoder_1_out, R1_Forward, R2_Forward, \数据相关检测_1_r1_forward ,
       \数据相关检测_1_r2_forward ;
  wire [3:0] id_ex_1_aluop_out, \单周期硬布线控制器_1_alu_op ;
  wire [4:0] EX_WriteReg_num, id_ex_1_shamt_out, ID_R1_num, ID_R2_num, MEM_WriteReg_num, multiplexer_3_out,
       multiplexer_6_out, multiplexer_18_out, multiplexer_19_out;
  wire [5:0] EX_Func, EX_OP, Func, MEM_OP, OP;
  wire [7:0] multiplexer_15_out;
  wire [15:0] adder_1_out, \LoadUse次数 , multiplier_1_out, \总周期数 , \插入气泡数 , \无条件分支数 , \条件分支成功数 ;
  wire [25:0] ex_mem_1_ir_out;
  wire [25:6] id_ex_1_ir_out, if_id_1_ir_out;
  wire [31:0] a0, adder_3_out, adder_4_out, bit_extender_1_out, bit_extender_2_out, bit_extender_3_out,
       EPC_q, ex_mem_1_pc_out, ex_mem_1_r2_out, EX_PC, id_ex_1_address_out, id_ex_1_imm_out, id_ex_1_pc_out,
       id_ex_1_r1_out, id_ex_1_r2_out, ID_PC, if_id_1_pc_out, IF_PC, LedData, MEM_Alu, MEM_PC,
       mem_wb_1_ir_out, mem_wb_1_pc_out, mips_alu_1_result, mips_ram_1_p6, mips_regifile_1_r1,
       mips_regifile_1_r2, multiplexer_4_out, multiplexer_7_out, multiplexer_8_out, multiplexer_12_out,
       multiplexer_13_out, multiplexer_14_out, multiplexer_16_out, multiplexer_17_out, nextPC, PCout, RDin,
       shifter_1_out, WB_Alu, WB_MD, WB_PC, \单级中断_Benchmark_data ;

  Button \u_总复位  (.out(RST));
  Button \u_继续运行  (.out(Go));
  Clock #(.highDuration(1), .lowDuration(1)) clock_1 (.out(CLK));
  Button _1 (.out(IR1));
  Button _2 (.out(IR2));
  Button _3 (.out(IR3));
  // Probe on IR_now
  Counter #(.width(16), .max('hffff), .ongoal("wrap"), .trigger("rising"), .behavior("old")) counter_1 (
    .count(JMP), .Q(\无条件分支数 ), .clk(CLK), .clr(RST));  // open: load, D, carry, preset
  Counter #(.width(16), .max('hffff), .ongoal("wrap"), .trigger("rising"), .behavior("old")) counter_2 (
    .count(Halt), .Q(\总周期数 ), .clk(CLK), .clr(RST));  // open: load, D, carry, preset
  or or_1 (W1, IR1_q, d_ff_1_q);
  or or_2 (W2, IR2_q, d_ff_2_q);
  or or_3 (W3, IR3_q, d_ff_3_q);
  LED #(.active("true")) led_1 (.in(W1));
  LED #(.active("true")) led_2 (.in(W2));
  LED #(.active("true")) led_3 (.in(W3));
  Adder #(.width(16)) adder_1 (.a(\无条件分支数 ), .b(\条件分支成功数 ), .out(adder_1_out));  // open: cin, cout
  Multiplexer #(.select(3), .width(32), .disabled("Z"), .enable("false")) multiplexer_1 (
    .in0(adder_3_out), .in1({32{1'b0}}), .in2(id_ex_1_address_out), .in3(a0), .in4(adder_4_out),
    .in5({32{1'b0}}), .in6({32{1'b0}}), .in7({32{1'b0}}), .out(nextPC), .sel({Conbranch, JMP, JR}));
  and and_1 (and_1_out, Halt, ~Loaduse);  // AND_Gate
  D_Flip_Flop #(.trigger("rising"), .Pre_Clr_Positions("LEGACY"), .NegatePresetClear("false"), .enable("true"), .NewFFLayout("false")) d_ff_1 (
    .clk(IR1), .D(1'b1), .Q(d_ff_1_q), .reset(IR1_q));  // open: Qn, preset, en
  D_Flip_Flop #(.trigger("rising"), .Pre_Clr_Positions("LEGACY"), .NegatePresetClear("false"), .enable("true"), .NewFFLayout("false")) d_ff_2 (
    .clk(IR2), .D(1'b1), .Q(d_ff_2_q), .reset(IR2_q));  // open: Qn, preset, en
  D_Flip_Flop #(.trigger("rising"), .Pre_Clr_Positions("LEGACY"), .NegatePresetClear("false"), .enable("true"), .NewFFLayout("false")) d_ff_3 (
    .clk(IR3), .D(1'b1), .Q(d_ff_3_q), .reset(IR3_q));  // open: Qn, preset, en
  and and_2 (and_2_out, Equal, syscall);
  Multiplier #(.width(16)) multiplier_1 (.a(adder_1_out), .b(16'h2), .out(multiplier_1_out));  // open: cin, cout
  Register #(.width(32), .trigger("rising"), .Select("low")) PC (
    .D(PCout), .en(and_1_out), .Q(IF_PC), .clk(CLK), .clr(RST));
  or or_4 (or_4_out, d_ff_1_q, IR1_q);
  or or_5 (or_5_out, d_ff_2_q, IR2_q);
  or or_6 (or_6_out, d_ff_3_q, IR3_q);
  Hex_Digit_Display hex_digit_display_1 (.value(LedData[27:24]));  // open: dp
  Hex_Digit_Display hex_digit_display_2 (.value(LedData[31:28]));  // open: dp
  Counter #(.width(16), .max('hffff), .ongoal("wrap"), .trigger("rising"), .behavior("old")) counter_3 (
    .count(Conbranch), .Q(\条件分支成功数 ), .clk(CLK), .clr(RST));  // open: load, D, carry, preset
  Register #(.width(32), .trigger("rising"), .Select("low")) register_1 (
    .D(a0), .en(and_2_out), .Q(LedData), .clk(CLK), .clr(RST));
  Adder #(.width(16)) adder_2 (.a(multiplier_1_out), .b(\LoadUse次数 ), .out(\插入气泡数 ));  // open: cin, cout
  Adder #(.width(32)) adder_3 (.a(IF_PC), .b(32'h4), .out(adder_3_out));  // open: cin, cout
  and and_3 (and_3_out, ERET, IR_now[0], ~IR_now[1]);  // AND_Gate
  and and_4 (and_4_out, ERET, ~IR_now[0], IR_now[1]);  // AND_Gate
  and and_5 (and_5_out, ERET, IR_now[0], IR_now[1]);
  Hex_Digit_Display hex_digit_display_3 (.value(LedData[19:16]));  // open: dp
  Hex_Digit_Display hex_digit_display_4 (.value(LedData[23:20]));  // open: dp
  ROM #(.addrWidth(10), .dataWidth(32), .Select("high")) \u_单级中断_Benchmark  (
    .addr(IF_PC[11:2]), .data(\单级中断_Benchmark_data ));
  and and_6 (and_6_out, or_4_out, ~and_3_out);  // AND_Gate
  and and_7 (and_7_out, or_5_out, ~and_4_out);  // AND_Gate
  and and_8 (and_8_out, or_6_out, ~and_5_out);  // AND_Gate
  Hex_Digit_Display hex_digit_display_5 (.value(LedData[15:12]));  // open: dp
  Hex_Digit_Display hex_digit_display_6 (.value(LedData[11:8]));  // open: dp
  or or_7 (or_7_out, RST, BranchNop);
  IF_ID if_id_1 (
    .PCr_in(IF_PC), .PC_in(adder_3_out), .IR_in(\单级中断_Benchmark_data ), .PCr_out(ID_PC),
    .PC_out(if_id_1_pc_out), .IR_out({OP, if_id_1_ir_out, Func}), .Reset(or_7_out), .CLK(CLK),
    .Enable(and_9_out));  // open: PC_G_in, HG_in, PC_G_out, HG_out
  and and_9 (and_9_out, ~Loaduse, Halt);  // AND_Gate
  D_Flip_Flop #(.trigger("rising"), .Pre_Clr_Positions("LEGACY"), .NegatePresetClear("false"), .enable("true"), .NewFFLayout("false")) u_IR1 (
    .clk(CLK), .D(and_6_out), .Q(IR1_q));  // open: Qn, preset, en, reset
  D_Flip_Flop #(.trigger("rising"), .Pre_Clr_Positions("LEGACY"), .NegatePresetClear("false"), .enable("true"), .NewFFLayout("false")) u_IR2 (
    .clk(CLK), .D(and_7_out), .Q(IR2_q));  // open: Qn, preset, en, reset
  D_Flip_Flop #(.trigger("rising"), .Pre_Clr_Positions("LEGACY"), .NegatePresetClear("false"), .enable("true"), .NewFFLayout("false")) u_IR3 (
    .clk(CLK), .D(and_8_out), .Q(IR3_q));  // open: Qn, preset, en, reset
  Hex_Digit_Display hex_digit_display_7 (.value(LedData[3:0]));  // open: dp
  Hex_Digit_Display hex_digit_display_8 (.value(LedData[7:4]));  // open: dp
  // Probe on {OP, if_id_1_ir_out, Func}
  Priority_Encoder #(.select(2), .disabled("Z")) priority_encoder_1 (
    .in0(1'b1), .in1(IR1_q), .in2(IR2_q), .in3(IR3_q), .out(priority_encoder_1_out),
    .gs(priority_encoder_1_gs));  // open: en_out, en_in
  // Probe on priority_encoder_1_out
  Multiplexer #(.select(2), .width(1), .disabled("Z"), .enable("false")) multiplexer_2 (
    .in0(1'b0), .in1(priority_encoder_1_gs), .in2(priority_encoder_1_gs), .in3(priority_encoder_1_gs),
    .out(multiplexer_2_out), .sel(priority_encoder_1_out));
  // Probe on if_id_1_ir_out[20:16]
  Multiplexer #(.select(1), .width(5), .disabled("Z"), .enable("false")) multiplexer_3 (
    .in0(if_id_1_ir_out[20:16]), .in1(if_id_1_ir_out[15:11]), .out(multiplexer_3_out), .sel(ID_RDst));
  Multiplexer #(.select(2), .width(32), .disabled("Z"), .enable("false")) multiplexer_4 (
    .in0(nextPC), .in1(32'h4), .in2(32'h1c8), .in3(32'h38c), .out(multiplexer_4_out),
    .sel(priority_encoder_1_out));
  and and_10 (and_10_out, multiplexer_2_out, ~\中断状态_q );  // AND_Gate
  // Probe on \总周期数 
  // Probe on \无条件分支数 
  // Probe on \条件分支成功数 
  // Probe on \插入气泡数 
  // Probe on \LoadUse次数 
  \数据相关检测  \u_数据相关检测_1  (
    .ID_OP(OP), .ID_FUNC(Func), .ID_R1_num(ID_R1_num), .ID_R2_num(ID_R2_num),
    .EX_WriteReg_num(EX_WriteReg_num), .MEM_WriteReg_num(MEM_WriteReg_num), .EX_RegWrite(EX_RegWrite),
    .MEM_RegWrite(MEM_RegWrite), .EX_OP(EX_OP), .\数据相关 (\数据相关 ), .\Load_Use相关 (Loaduse),
    .R1_Forward(\数据相关检测_1_r1_forward ), .R2_Forward(\数据相关检测_1_r2_forward ), .MEM_OP(MEM_OP));
  \单周期硬布线控制器  \u_单周期硬布线控制器_1  (
    .Func(Func), .OP(OP), .ALU_OP(\单周期硬布线控制器_1_alu_op ), .MemToReg(\单周期硬布线控制器_1_memtoreg ),
    .MemWrite(\单周期硬布线控制器_1_memwrite ), .ALU_SRC(\单周期硬布线控制器_1_alu_src ), .RegWrite(\单周期硬布线控制器_1_regwrite ),
    .SysCALL(\单周期硬布线控制器_1_syscall ), .SignedExt(SignedExt), .RegDst(ID_RDst), .JR(\单周期硬布线控制器_1_jr ),
    .JMP(\单周期硬布线控制器_1_jmp ), .Beq(\单周期硬布线控制器_1_beq ), .JAL(ID_JAL), .Bne(\单周期硬布线控制器_1_bne ),
    .LBU(\单周期硬布线控制器_1_lbu ), .BLTZ(\单周期硬布线控制器_1_bltz ), .ERET(ERET));  // open: MFC0, MTC0, MF
  // Probe on if_id_1_ir_out[25:21]
  Multiplexer #(.select(1), .width(5), .disabled("Z"), .enable("false")) multiplexer_5 (
    .in0(if_id_1_ir_out[25:21]), .in1(5'b00100), .out(ID_R1_num), .sel(\单周期硬布线控制器_1_syscall ));
  Multiplexer #(.select(1), .width(5), .disabled("Z"), .enable("false")) multiplexer_6 (
    .in0(multiplexer_3_out), .in1({5{1'b1}}), .out(multiplexer_6_out), .sel(ID_JAL));
  assign bit_extender_1_out = {{16{1'b0}}, {if_id_1_ir_out[15:6], Func}};  // Bit_Extender bit_extender_1
  Multiplexer #(.select(1), .width(32), .disabled("Z"), .enable("false")) multiplexer_7 (
    .in0(bit_extender_1_out), .in1(bit_extender_2_out), .out(multiplexer_7_out), .sel(SignedExt));
  assign bit_extender_2_out = {{16{if_id_1_ir_out[15]}}, {if_id_1_ir_out[15:6], Func}};  // Bit_Extender bit_extender_2
  Multiplexer #(.select(1), .width(32), .disabled("Z"), .enable("false")) multiplexer_8 (
    .in0(nextPC), .in1(multiplexer_4_out), .out(multiplexer_8_out), .sel(and_10_out));
  and and_11 (and_11_out, and_10_out, ~ERET);  // AND_Gate
  or or_8 (or_8_out, and_10_out, \中断状态_q );
  // Probe on ID_PC[11:0]
  // Probe on IF_PC[11:0]
  Register #(.width(4), .trigger("rising"), .Select("low")) register_2 (
    .D({\数据相关检测_1_r2_forward , \数据相关检测_1_r1_forward }), .Q({R2_Forward, R1_Forward}), .clk(CLK), .clr(RST));  // open: en
  Multiplexer #(.select(1), .width(5), .disabled("Z"), .enable("false")) multiplexer_9 (
    .in0(if_id_1_ir_out[20:16]), .in1(5'b00010), .out(ID_R2_num), .sel(\单周期硬布线控制器_1_syscall ));
  Multiplexer #(.select(1), .width(32), .disabled("Z"), .enable("false")) multiplexer_10 (
    .in0(multiplexer_8_out), .in1(EPC_q), .out(PCout), .sel(ERET));
  Register #(.width(32), .trigger("rising"), .Select("low")) EPC (
    .D(IF_PC), .en(and_10_out), .Q(EPC_q), .clk(CLK));  // open: clr
  Register #(.width(1), .trigger("rising"), .Select("low")) \u_中断状态  (
    .D(or_8_out), .Q(\中断状态_q ), .clk(CLK), .clr(ERET));  // open: en
  // Probe on EX_PC[11:0]
  and and_12 (and_12_out, Halt, Loaduse);
  // Probe on PCout
  Register #(.width(2), .trigger("rising"), .Select("low")) cause (
    .D(priority_encoder_1_out), .en(and_11_out), .Q(IR_now), .clk(CLK), .clr(comparator_1_eq));
  // Probe on WB_PC[11:0]
  // Probe on MEM_PC[11:0]
  Counter #(.width(16), .max('hffff), .ongoal("wrap"), .trigger("rising"), .behavior("old")) counter_4 (
    .count(and_12_out), .Q(\LoadUse次数 ), .clk(CLK), .clr(RST));  // open: load, D, carry, preset
  MIPS_Regifile mips_regifile_1 (
    .Din(RDin), .Clk(CLK), .R1(mips_regifile_1_r1), .R2(mips_regifile_1_r2), .WE(WB_RegWrite),
    .W_num(multiplexer_19_out), .R1_num(ID_R1_num), .R2_num(ID_R2_num));
  Comparator #(.width(2), .mode("twosComplement")) comparator_1 (
    .a(priority_encoder_1_out), .b(2'b00), .eq(comparator_1_eq));  // open: gt, lt
  or or_9 (or_9_out, RST, Loaduse, BranchNop);
  ID_EX id_ex_1 (
    .BEQ_in(\单周期硬布线控制器_1_beq ), .BEQ_out(id_ex_1_beq_out), .IR_in({OP, if_id_1_ir_out, Func}),
    .IR_out({EX_OP, id_ex_1_ir_out, EX_Func}), .BNE_in(\单周期硬布线控制器_1_bne ), .BNE_out(id_ex_1_bne_out),
    .PC_in(if_id_1_pc_out), .PC_out(id_ex_1_pc_out), .MemToReg_in(\单周期硬布线控制器_1_memtoreg ),
    .MemToReg_out(id_ex_1_memtoreg_out), .R1_in(mips_regifile_1_r1), .R1_out(id_ex_1_r1_out),
    .MemWrite_in(\单周期硬布线控制器_1_memwrite ), .MemWrite_out(id_ex_1_memwrite_out), .R2_in(mips_regifile_1_r2),
    .AluSrcB_in(\单周期硬布线控制器_1_alu_src ), .R2_out(id_ex_1_r2_out), .AluSrcB_out(id_ex_1_alusrcb_out),
    .RegWrite_in(\单周期硬布线控制器_1_regwrite ), .Imm_in(multiplexer_7_out), .RegWrite_out(EX_RegWrite),
    .Imm_out(id_ex_1_imm_out), .JAL_in(ID_JAL), .JAL_out(id_ex_1_jal_out),
    .Address_in({if_id_1_pc_out[31:28], if_id_1_ir_out, Func, 2'b00}), .Address_out(id_ex_1_address_out),
    .RegDst_in(ID_RDst), .RegDst_out(id_ex_1_regdst_out), .AluOP_in(\单周期硬布线控制器_1_alu_op ),
    .AluOP_out(id_ex_1_aluop_out), .Syscall_in(\单周期硬布线控制器_1_syscall ), .Syscall_out(syscall),
    .Shamt_in(if_id_1_ir_out[10:6]), .Shamt_out(id_ex_1_shamt_out), .JMP_in(\单周期硬布线控制器_1_jmp ),
    .JMP_out(JMP), .JR_in(\单周期硬布线控制器_1_jr ), .LBU_in(\单周期硬布线控制器_1_lbu ), .JR_out(JR),
    .LBU_out(id_ex_1_lbu_out), .BLTZ_in(\单周期硬布线控制器_1_bltz ), .BLTZ_out(BLTZ), .W__in(multiplexer_6_out),
    .W__out(EX_WriteReg_num), .PCr_in(ID_PC), .PCr_out(EX_PC), .Reset(or_9_out), .Enable(Halt), .CLK(CLK));  // open: Halt_in, Halt_out, HG_in, HG_out, PCG_in, PCG_out, Interrupt_in, Interrupt_out
  ROM #(.addrWidth(10), .dataWidth(32), .Select("high")) u_BLTZ ();  // open: addr, data
  ROM #(.addrWidth(10), .dataWidth(32), .Select("high")) u_LBU ();  // open: addr, data
  Shifter #(.width(32), .shift("ll")) shifter_1 (.in(id_ex_1_imm_out), .\dist (5'b00010), .out(shifter_1_out));
  Multiplexer #(.select(2), .width(32), .disabled("Z"), .enable("false")) multiplexer_11 (
    .in0(id_ex_1_r1_out), .in1(WB_Alu), .in2(WB_MD), .in3(MEM_Alu), .out(a0), .sel(R1_Forward));
  Multiplexer #(.select(2), .width(32), .disabled("Z"), .enable("false")) multiplexer_12 (
    .in0(id_ex_1_r2_out), .in1(WB_Alu), .in2(WB_MD), .in3(MEM_Alu), .out(multiplexer_12_out), .sel(R2_Forward));
  Adder #(.width(32)) adder_4 (.a(id_ex_1_pc_out), .b(shifter_1_out), .out(adder_4_out));  // open: cin, cout
  Multiplexer #(.select(1), .width(32), .disabled("Z"), .enable("false")) multiplexer_13 (
    .in0(multiplexer_12_out), .in1(id_ex_1_imm_out), .out(multiplexer_13_out), .sel(id_ex_1_alusrcb_out));
  // Probe on {EX_OP, id_ex_1_ir_out, EX_Func}
  ROM #(.addrWidth(10), .dataWidth(32), .Select("high")) SUBU ();  // open: addr, data
  ROM #(.addrWidth(10), .dataWidth(32), .Select("high")) XOR ();  // open: addr, data
  Multiplexer #(.select(1), .width(32), .disabled("Z"), .enable("false")) multiplexer_14 (
    .in0(multiplexer_13_out), .in1({32{1'b0}}), .out(multiplexer_14_out), .sel(BLTZ));
  // Probe on id_ex_1_aluop_out
  Comparator #(.width(32), .mode("unsigned")) comparator_2 (
    .a(32'h22), .b(multiplexer_14_out), .eq(Equal));  // open: gt, lt
  ROM #(.addrWidth(10), .dataWidth(32), .Select("high")) Benchmark_test ();  // open: addr, data
  and and_13 (and_13_out, id_ex_1_beq_out, mips_alu_1_equal);
  and and_14 (and_14_out, id_ex_1_bne_out, ~mips_alu_1_equal);  // AND_Gate
  MIPS_ALU mips_alu_1 (
    .X(a0), .Y(multiplexer_14_out), .AluOP(id_ex_1_aluop_out), .Equal(mips_alu_1_equal),
    .Result(mips_alu_1_result), .shamt(id_ex_1_shamt_out));  // open: Result_2
  or or_10 (Conbranch, and_13_out, and_14_out, and_15_out);
  and and_15 (and_15_out, BLTZ, comparator_3_eq);
  Comparator #(.width(32), .mode("twosComplement")) comparator_3 (
    .a(32'h1), .b(mips_alu_1_result), .eq(comparator_3_eq));  // open: gt, lt
  // Probe on mips_alu_1_result
  or or_11 (BranchNop, JR, JMP, Conbranch);
  EX_MEM ex_mem_1 (
    .MemToReg_in(id_ex_1_memtoreg_out), .IR_in({EX_OP, id_ex_1_ir_out, EX_Func}),
    .MemToReg_out(ex_mem_1_memtoreg_out), .IR_out({MEM_OP, ex_mem_1_ir_out}),
    .MemWrite_in(id_ex_1_memwrite_out), .MemWrite_out(MemWrite), .PC_in(id_ex_1_pc_out),
    .PC_out(ex_mem_1_pc_out), .RegWrite_in(EX_RegWrite), .RegWrite_out(MEM_RegWrite),
    .R2_in(multiplexer_12_out), .R2_out(ex_mem_1_r2_out), .JAL_in(id_ex_1_jal_out),
    .JAL_out(ex_mem_1_jal_out), .AluR_in(mips_alu_1_result), .AluR_out(MEM_Alu),
    .RegDst_in(id_ex_1_regdst_out), .RegDst_out(ex_mem_1_regdst_out), .Halt_in(and_16_out),
    .Halt_out(ex_mem_1_halt_out), .Syscall_in(syscall), .Syscall_out(ex_mem_1_syscall_out),
    .LBU_in(id_ex_1_lbu_out), .LBU_out(LBU), .PCr_in(EX_PC), .W__in(EX_WriteReg_num), .PCr_out(MEM_PC),
    .W__out(MEM_WriteReg_num), .Reset(RST), .Enable(Halt), .CLK(CLK));  // open: Interrupt_in, Interrupt_out
  and and_16 (and_16_out, syscall, ~Equal);  // AND_Gate
  // Probe on MEM_Alu
  // Probe on R1_Forward
  // Probe on {MEM_OP, ex_mem_1_ir_out}
  // MIPS_RAM mips_ram_1: pin names not known; wires that end beside it: MEM_Alu[11:2], ex_mem_1_r2_out, MemWrite, CLK, RST, mips_ram_1_p6
  Multiplexer #(.select(2), .width(8), .disabled("Z"), .enable("false")) multiplexer_15 (
    .in0(mips_ram_1_p6[7:0]), .in1(mips_ram_1_p6[15:8]), .in2(mips_ram_1_p6[23:16]),
    .in3(mips_ram_1_p6[31:24]), .out(multiplexer_15_out), .sel(MEM_Alu[1:0]));
  assign bit_extender_3_out = {{24{1'b0}}, multiplexer_15_out};  // Bit_Extender bit_extender_3
  MEM_WB mem_wb_1 (
    .MemToReg_in(ex_mem_1_memtoreg_out), .IR_in({MEM_OP, ex_mem_1_ir_out}), .MemToReg_out(MemToReg),
    .IR_out(mem_wb_1_ir_out), .RegWrite_in(MEM_RegWrite), .PC_in(ex_mem_1_pc_out),
    .RegWrite_out(WB_RegWrite), .PC_out(mem_wb_1_pc_out), .JAL_in(ex_mem_1_jal_out), .JAL_out(JAL),
    .MemD_in(multiplexer_16_out), .MemD_out(WB_MD), .RegDst_in(ex_mem_1_regdst_out), .RegDst_out(RDst),
    .AluR_in(MEM_Alu), .AluR_out(WB_Alu), .Syscall_in(ex_mem_1_syscall_out), .Syscall_out(Sys),
    .Halt_in(ex_mem_1_halt_out), .Halt_out(mem_wb_1_halt_out), .W__in(MEM_WriteReg_num), .PCr_in(MEM_PC),
    .PCr_out(WB_PC), .Reset(RST), .Enable(Halt), .CLK(CLK));  // open: W__out, Interrupt_in, Interrupt_out, R2_in, R2_out
  Multiplexer #(.select(1), .width(32), .disabled("Z"), .enable("false")) multiplexer_16 (
    .in0(mips_ram_1_p6), .in1(bit_extender_3_out), .out(multiplexer_16_out), .sel(LBU));
  not not_1 (not_1_out, mem_wb_1_halt_out);
  Multiplexer #(.select(1), .width(32), .disabled("Z"), .enable("false")) multiplexer_17 (
    .in0(WB_Alu), .in1(WB_MD), .out(multiplexer_17_out), .sel(MemToReg));
  Multiplexer #(.select(1), .width(5), .disabled("Z"), .enable("false")) multiplexer_18 (
    .in0(mem_wb_1_ir_out[20:16]), .in1(mem_wb_1_ir_out[15:11]), .out(multiplexer_18_out), .sel(RDst));
  Multiplexer #(.select(1), .width(5), .disabled("Z"), .enable("false")) multiplexer_19 (
    .in0(multiplexer_18_out), .in1({5{1'b1}}), .out(multiplexer_19_out), .sel(JAL));
  or or_12 (Halt, Go, RST, not_1_out);
  Multiplexer #(.select(1), .width(32), .disabled("Z"), .enable("false")) multiplexer_20 (
    .in0(multiplexer_17_out), .in1(mem_wb_1_pc_out), .out(RDin), .sel(JAL));

  // Other names for the same wires on the sheet: R1[31:0] = a0; 字节选择[1:0] = MEM_Alu[1:0]; PC[31:0] = IF_PC

  // Notes on the sheet:
  //   中断源
  //   中断等待指示
  //   中断优先级3>2>1>CPU(0）)
  //   数码管输出
  //   contents of 单级中断_Benchmark (hex, n*v repeats v):
  //   8000d54 23bdfffc afa10000 23bdfffc afa20000 23bdfffc afa30000 23bdfffc afa40000 23bdfffc afa50000
  //   23bdfffc afa60000 23bdfffc afa70000 23bdfffc afa80000 23bdfffc afa90000 23bdfffc afaa0000 23bdfffc
  //   afab0000 23bdfffc afac0000 23bdfffc afad0000 23bdfffc afae0000 23bdfffc afaf0000 23bdfffc afb00000
  //   23bd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
  //   Reset 
  //   Reset 
  //   Reset 
  //   指令字
  //   imm
  //   OP
  //   Func
  //   rs
  //   rt
  //   rd
  //   shamt
  //   关中断信号
  //   JMP
  //   JR
  //   OP
  //   Func
  //   Beq
  //   Bne
  //   MemToReg
  //   MemWrite
  //   AluOP
  //   AluSrcB
  //   RegWrite
  //   JAL
  //   RegDst
  //   Syscall
  //   流水调试日志用
  //   contents of BLTZ (hex, n*v repeats v):
  //   2011fff1 112020 20020022 c 22310001 620fffb 2002000a c
  //   contents of LBU (hex, n*v repeats v):
  //   20090000 200b0010 34118483 20120404 118c00 129400 36318281 22520404 ad310000 2328820 21290004
  //   216bffff 1560fffb 200b0020 20090000 91310000 112020 20020022 c 21290001 216bffff 1560fff9 2002000a c
  //   contents of SUBU (hex, n*v repeats v):
  //   20080001 20110010 112020 20020022 c 200b0020 2288823 112020 20020022 c 216bffff 1560fffa 2002000a c
  //   contents of XOR (hex, n*v repeats v):
  //   2008ffff 20117777 112020 20020022 c 200b0010 2288826 112020 20020022 c 216bffff 1560fffa 2002000a c
  //   contents of Benchmark_test (hex, n*v repeats v):
  //   20110001 8000c05 20110001 20120002 20130003 8000c09 20110001 20120002 20130003 8000c0d 20110001
  //   20120002 20130003 8000c11 20110001 20120002 20130003 c000cb8 20100001 20110001 118fc0 112020
  //   20020022 c 118882 12200001 8000c15 112020 20020022 c 20110001 118880 112020 20020022 c 12200001
  //   8000c1f 2011000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
  //   rt
  //   rd
  //   W#
endmodule
